// Logisim project processor_w_ram.circ as structural Verilog: 36 circuits, main circuit somador1b
module main (
  input  in_1,
  input  in_2,
  input  in_3,
  input  in_4
);

  wire _0_2_out, _0_3_out, _0_out, _1_2_out, _1_3_out, _1_out, _2_2_out, _2_3_out, _2_out, _3_2_out,
       _3_3_out, _3_out, _4_2_out, _4_3_out, _4_out, _5_2_out, _5_3_out, _5_out, _6_2_out, _6_3_out, _6_out,
       _7_2_out, _7_3_out, _7_out, bcd8421_1_b, bcd8421_1_c, bcd8421_1_d, bcd8421_2_b, bcd8421_2_c,
       bcd8421_2_d, bcd8421_3_b, bcd8421_3_c, bcd8421_3_d, bcd8421_4_b, bcd8421_4_c, bcd8421_4_d,
       button_1_out, button_2_out, button_3_out, button_4_out, button_5_out, button_6_out, button_7_out,
       button_8_out, button_9_out, clock_1_out, demux1_16_1_out_6, demux1_16_1_out_7, demux1_16_1_out_8,
       demux1_16_1_out_9, demux1_16_1_out_10, demux1_16_1_out_11, demux1_16_1_out_12, demux1_16_1_out_13,
       demux1_16_1_out_14, demux1_16_1_out_15, demux1_16_1_out_16, demux1_16_1_out_17, demux1_16_1_out_18,
       demux1_16_1_out_19, demux1_16_1_out_20, demux1_16_1_out_21, dmux1_8_1_s0, dmux1_8_1_s1, dmux1_8_1_s2,
       dmux1_8_1_s3, dmux1_8_1_s4, dmux1_8_1_s5, dmux1_8_1_s6, dmux1_8_1_s7, l1_32b_1_p9, l1_32b_1_p10,
       l1_32b_1_p11, l1_32b_1_p12, l2_256b_1_dest_4, l2_256b_1_dest_5, l2_256b_1_dest_6, l2_256b_1_ins_4,
       l2_256b_1_ins_5, l2_256b_1_ins_6, s_out;
  wire [2:0] l2_256b_1_out_r1_3, l2_256b_1_out_r2_3;
  wire [3:0] bcdd8421_0_15_1_d, counter_1_q, dullentry_1_b0_2, entryslt_1_c0, l1_32b_1_p13, l1_32b_1_p17,
       l1_32b_1_p21, l1_32b_1_p25, l1_32b_1_p29, l1_32b_1_p33, l1_32b_1_p37, l1_32b_1_p41,
       l2_256b_1_out_input_4, multiplexer_1_out, multiplexer_2_out;
  wire [15:0] _0_4_out;

  Button button_1 (.out(button_1_out));
  Button _1 (.out(_1_out));
  Button _0 (.out(_0_out));
  BCD8421 bcd8421_1 (
    ._0(_0_out), ._1(_1_out), ._2(_2_out), ._3(_3_out), ._4(_4_out), ._5(_5_out), ._6(_6_out), ._7(_7_out),
    ._8(1'b0), ._9(1'b0), .B(bcd8421_1_b), .C(bcd8421_1_c), .D(bcd8421_1_d));  // open: A
  Button button_2 (.out(button_2_out));
  Dmux1_8 dmux1_8_1 (
    .E(button_1_out), .in_1(l2_256b_1_dest_4), .in_2(l2_256b_1_dest_5), .in_3(l2_256b_1_dest_6),
    .S0(dmux1_8_1_s0), .S1(dmux1_8_1_s1), .S2(dmux1_8_1_s2), .S3(dmux1_8_1_s3), .S4(dmux1_8_1_s4),
    .S5(dmux1_8_1_s5), .S6(dmux1_8_1_s6), .S7(dmux1_8_1_s7));
  Button _3 (.out(_3_out));
  Button _2 (.out(_2_out));
  Button _4 (.out(_4_out));
  Button _5 (.out(_5_out));
  Demux1_16 demux1_16_1 (
    .in_5(button_2_out), .out_6(demux1_16_1_out_6), .out_7(demux1_16_1_out_7), .out_8(demux1_16_1_out_8),
    .out_9(demux1_16_1_out_9), .out_10(demux1_16_1_out_10), .out_11(demux1_16_1_out_11),
    .out_12(demux1_16_1_out_12), .out_13(demux1_16_1_out_13), .out_14(demux1_16_1_out_14),
    .out_15(demux1_16_1_out_15), .out_16(demux1_16_1_out_16), .out_17(demux1_16_1_out_17),
    .out_18(demux1_16_1_out_18), .out_19(demux1_16_1_out_19), .out_20(demux1_16_1_out_20),
    .out_21(demux1_16_1_out_21), .in_1(in_1), .in_2(in_2), .in_3(in_3), .in_4(in_4));
  Button _6 (.out(_6_out));
  Button _7 (.out(_7_out));
  // L1_32b l1_32b_1: pin names not known; wires that end beside it: dmux1_8_1_s0, dmux1_8_1_s1, dmux1_8_1_s2, dmux1_8_1_s3, dmux1_8_1_s4, dmux1_8_1_s5, dmux1_8_1_s6, dmux1_8_1_s7, l1_32b_1_p9, l1_32b_1_p10, l1_32b_1_p11, l1_32b_1_p12, l1_32b_1_p13[0], l1_32b_1_p13[1], l1_32b_1_p13[2], l1_32b_1_p13[3], l1_32b_1_p17[0], l1_32b_1_p17[1], l1_32b_1_p17[2], l1_32b_1_p17[3], l1_32b_1_p21[0], l1_32b_1_p21[1], l1_32b_1_p21[2], l1_32b_1_p21[3], l1_32b_1_p25[0], l1_32b_1_p25[1], l1_32b_1_p25[2], l1_32b_1_p25[3], l1_32b_1_p29[0], l1_32b_1_p29[1], l1_32b_1_p29[2], l1_32b_1_p29[3], l1_32b_1_p33[0], l1_32b_1_p33[1], l1_32b_1_p33[2], l1_32b_1_p33[3], l1_32b_1_p37[0], l1_32b_1_p37[1], l1_32b_1_p37[2], l1_32b_1_p37[3], l1_32b_1_p41[0], l1_32b_1_p41[1], l1_32b_1_p41[2], l1_32b_1_p41[3]
  Hex_Digit_Display hex_digit_display_1 (.value(l1_32b_1_p13));  // open: dp
  Hex_Digit_Display hex_digit_display_2 (.value(l1_32b_1_p17));  // open: dp
  Hex_Digit_Display hex_digit_display_3 (.value(l1_32b_1_p21));  // open: dp
  Hex_Digit_Display hex_digit_display_4 (.value(l1_32b_1_p25));  // open: dp
  Hex_Digit_Display hex_digit_display_5 (.value(l1_32b_1_p29));  // open: dp
  Hex_Digit_Display hex_digit_display_6 (.value(l1_32b_1_p33));  // open: dp
  Hex_Digit_Display hex_digit_display_7 (.value(l1_32b_1_p37));  // open: dp
  Hex_Digit_Display hex_digit_display_8 (.value(l1_32b_1_p41));  // open: dp
  Button button_3 (.out(button_3_out));
  Button button_4 (.out(button_4_out));
  Button button_5 (.out(button_5_out));
  Button button_6 (.out(button_6_out));
  BCD8421 bcd8421_2 (
    ._0(button_4_out), ._1(button_3_out), ._2(button_8_out), ._3(button_7_out), ._4(button_5_out),
    ._5(button_6_out), ._6(button_9_out), ._7(s_out), ._8(1'b0), ._9(1'b0), .B(bcd8421_2_b), .C(bcd8421_2_c),
    .D(bcd8421_2_d));  // open: A
  Button button_7 (.out(button_7_out));
  Button button_8 (.out(button_8_out));
  Button s (.out(s_out));
  Button button_9 (.out(button_9_out));
  Button _2_2 (.out(_2_2_out));
  Button _1_2 (.out(_1_2_out));
  Button _0_2 (.out(_0_2_out));
  Button _3_2 (.out(_3_2_out));
  BCD8421 bcd8421_3 (
    ._0(_0_2_out), ._1(_1_2_out), ._2(_2_2_out), ._3(_3_2_out), ._4(_4_2_out), ._5(_5_2_out), ._6(_6_2_out),
    ._7(_7_2_out), ._8(1'b0), ._9(1'b0), .B(bcd8421_3_b), .C(bcd8421_3_c), .D(bcd8421_3_d));  // open: A
  Button _4_2 (.out(_4_2_out));
  Button _7_2 (.out(_7_2_out));
  Button _5_2 (.out(_5_2_out));
  Button _6_2 (.out(_6_2_out));
  Multiplexer #(.select(3), .width(4)) multiplexer_1 (
    .in0(l1_32b_1_p13), .in1(l1_32b_1_p17), .in2(l1_32b_1_p21), .in3(l1_32b_1_p25), .in4(l1_32b_1_p29),
    .in5(l1_32b_1_p33), .in6(l1_32b_1_p37), .in7(l1_32b_1_p41), .out(multiplexer_1_out),
    .sel(l2_256b_1_out_r1_3));  // open: en
  Multiplexer #(.select(3), .width(4)) multiplexer_2 (
    .in0(l1_32b_1_p13), .in1(l1_32b_1_p17), .in2(l1_32b_1_p21), .in3(l1_32b_1_p25), .in4(l1_32b_1_p29),
    .in5(l1_32b_1_p33), .in6(l1_32b_1_p37), .in7(l1_32b_1_p41), .out(multiplexer_2_out),
    .sel(l2_256b_1_out_r2_3));  // open: en
  Button _1_3 (.out(_1_3_out));
  Button _0_3 (.out(_0_3_out));
  Button _2_3 (.out(_2_3_out));
  BCD8421 bcd8421_4 (
    ._0(_0_3_out), ._1(_1_3_out), ._2(_2_3_out), ._3(_3_3_out), ._4(_4_3_out), ._5(_5_3_out), ._6(_6_3_out),
    ._7(_7_3_out), ._8(1'b0), ._9(1'b0), .B(bcd8421_4_b), .C(bcd8421_4_c), .D(bcd8421_4_d));  // open: A
  L2_256b l2_256b_1 (
    .R1_5(demux1_16_1_out_6), .R2_4(demux1_16_1_out_7), .R3(demux1_16_1_out_8), .R4(demux1_16_1_out_9),
    .R5(demux1_16_1_out_10), .R6(demux1_16_1_out_11), .R7(demux1_16_1_out_12), .R8(demux1_16_1_out_13),
    .R9(demux1_16_1_out_14), .R10(demux1_16_1_out_15), .R11(demux1_16_1_out_16), .R12(demux1_16_1_out_17),
    .R13(demux1_16_1_out_18), .R14(demux1_16_1_out_19), .R15(demux1_16_1_out_20), .R16(demux1_16_1_out_21),
    .DEST(bcd8421_1_b), .DEST_2(bcd8421_1_c), .DEST_3(bcd8421_1_d), .INS(bcd8421_2_b), .INS_2(bcd8421_2_c),
    .INS_3(bcd8421_2_d), .R1(bcd8421_3_b), .R1_2(bcd8421_3_c), .R1_3(bcd8421_3_d), .R2(bcd8421_4_b),
    .R2_2(bcd8421_4_c), .R2_3(bcd8421_4_d), .R1_4(bcdd8421_0_15_1_d[3]), .INPUT(bcdd8421_0_15_1_d[2]),
    .INPUT_2(bcdd8421_0_15_1_d[1]), .INPUT_3(bcdd8421_0_15_1_d[0]), .DEST_4(l2_256b_1_dest_4),
    .DEST_5(l2_256b_1_dest_5), .DEST_6(l2_256b_1_dest_6), .INS_4(l2_256b_1_ins_4), .INS_5(l2_256b_1_ins_5),
    .INS_6(l2_256b_1_ins_6), .OUT_R1(l2_256b_1_out_r1_3[2]), .OUT_R1_2(l2_256b_1_out_r1_3[1]),
    .OUT_R1_3(l2_256b_1_out_r1_3[0]), .OUT_R2(l2_256b_1_out_r2_3[2]), .OUT_R2_2(l2_256b_1_out_r2_3[1]),
    .OUT_R2_3(l2_256b_1_out_r2_3[0]), .OUT_INPUT(l2_256b_1_out_input_4[3]),
    .OUT_INPUT_2(l2_256b_1_out_input_4[2]), .OUT_INPUT_3(l2_256b_1_out_input_4[1]),
    .OUT_INPUT_4(l2_256b_1_out_input_4[0]), .SELECT(counter_1_q));
  Button _6_3 (.out(_6_3_out));
  Button _4_3 (.out(_4_3_out));
  Button _5_3 (.out(_5_3_out));
  Button _3_3 (.out(_3_3_out));
  Hex_Digit_Display hex_digit_display_9 (.value(multiplexer_1_out));  // open: dp
  Hex_Digit_Display hex_digit_display_10 (.value(multiplexer_2_out));  // open: dp
  Button _7_3 (.out(_7_3_out));
  Counter #(.width(4), .max('hf)) counter_1 (.Q(counter_1_q), .clk(clock_1_out));  // open: load, D, count, carry, clr
  Button _1_4 (.out(_0_4_out[1]));
  Button _0_4 (.out(_0_4_out[0]));
  Button _5_4 (.out(_0_4_out[5]));
  Button _4_4 (.out(_0_4_out[4]));
  Button _9 (.out(_0_4_out[9]));
  Button _8 (.out(_0_4_out[8]));
  Button _12 (.out(_0_4_out[12]));
  Button _13 (.out(_0_4_out[13]));
  Clock clock_1 (.out(clock_1_out));
  ENTRYSLT entryslt_1 (
    .A0(multiplexer_1_out[0]), .A1(multiplexer_1_out[1]), .A2(multiplexer_1_out[2]),
    .A3(multiplexer_1_out[3]), .B0(l2_256b_1_out_input_4[0]), .B1(l2_256b_1_out_input_4[1]),
    .B2(l2_256b_1_out_input_4[2]), .B3(l2_256b_1_out_input_4[3]), .in_1(l2_256b_1_ins_4),
    .in_2(l2_256b_1_ins_5), .in_3(l2_256b_1_ins_6), .C0(entryslt_1_c0[0]), .C1(entryslt_1_c0[1]),
    .C2(entryslt_1_c0[2]), .C3(entryslt_1_c0[3]));
  DULLENTRY dullentry_1 (
    .B0(multiplexer_2_out[0]), .B1(multiplexer_2_out[1]), .B2(multiplexer_2_out[2]),
    .B3(multiplexer_2_out[3]), .in_1(l2_256b_1_ins_4), .in_2(l2_256b_1_ins_5), .in_3(l2_256b_1_ins_6),
    .B0_2(dullentry_1_b0_2[0]), .B1_2(dullentry_1_b0_2[1]), .B2_2(dullentry_1_b0_2[2]),
    .B3_2(dullentry_1_b0_2[3]));
  BCDD8421_0_15 bcdd8421_0_15_1 (
    ._0(_0_4_out[0]), ._1(_0_4_out[1]), ._2(_0_4_out[2]), ._3(_0_4_out[3]), ._4(_0_4_out[4]),
    ._5(_0_4_out[5]), ._6(_0_4_out[6]), ._7(_0_4_out[7]), ._8(_0_4_out[8]), ._9(_0_4_out[9]),
    ._10(_0_4_out[10]), ._11(_0_4_out[11]), ._12(_0_4_out[12]), ._13(_0_4_out[13]), ._14(_0_4_out[14]),
    ._15(_0_4_out[15]), .A(bcdd8421_0_15_1_d[3]), .B(bcdd8421_0_15_1_d[2]), .C(bcdd8421_0_15_1_d[1]),
    .D(bcdd8421_0_15_1_d[0]));
  Button _2_4 (.out(_0_4_out[2]));
  Button _3_4 (.out(_0_4_out[3]));
  Button _6_4 (.out(_0_4_out[6]));
  Button _7_4 (.out(_0_4_out[7]));
  Button _10 (.out(_0_4_out[10]));
  Button _11 (.out(_0_4_out[11]));
  Button _14 (.out(_0_4_out[14]));
  Button _15 (.out(_0_4_out[15]));
  Hex_Digit_Display hex_digit_display_11 (.value(bcdd8421_0_15_1_d));  // open: dp
  ULA ula_1 (
    .D0(entryslt_1_c0[0]), .C0(entryslt_1_c0[1]), .B0(entryslt_1_c0[2]), .A0(entryslt_1_c0[3]),
    .D1(dullentry_1_b0_2[0]), .C1(dullentry_1_b0_2[1]), .B1(dullentry_1_b0_2[2]), .A1(dullentry_1_b0_2[3]),
    .in_1(l2_256b_1_ins_4), .in_2(l2_256b_1_ins_5), .in_3(l2_256b_1_ins_6), .D(l1_32b_1_p12),
    .C(l1_32b_1_p11), .B(l1_32b_1_p10), .A(l1_32b_1_p9));

  // Notes on the sheet:
  //   INPUT
endmodule

// +
module somador1b (
  input  Te,
  input  A,
  input  B,
  output S,
  output Ts
);

  wire and_1_out, and_2_out, and_3_out, xor_1_out;

  xor xor_1 (xor_1_out, A, B);
  and and_1 (and_1_out, B, A);
  and and_2 (and_2_out, Te, B);
  and and_3 (and_3_out, A, Te);
  xor xor_2 (S, xor_1_out, Te);
  or or_1 (Ts, and_1_out, and_2_out, and_3_out);
endmodule

// Somador4b
module somador4b (
  input  D0,
  input  D1,
  input  C0,
  input  C1,
  input  B0,
  input  B1,
  input  A0,
  input  A1,
  output D,
  output C,
  output B,
  output A,
  output Ovf
);

  wire somador1b_1_ts, somador1b_2_ts, somador1b_3_ts;

  somador1b somador1b_1 (.Te(1'b0), .A(D0), .B(D1), .S(D), .Ts(somador1b_1_ts));
  somador1b somador1b_2 (.Te(somador1b_1_ts), .A(C0), .B(C1), .S(C), .Ts(somador1b_2_ts));
  somador1b somador1b_3 (.Te(somador1b_2_ts), .A(B0), .B(B1), .S(B), .Ts(somador1b_3_ts));
  somador1b somador1b_4 (.Te(somador1b_3_ts), .A(A0), .B(A1), .S(A), .Ts(Ovf));
endmodule

module AND4b (
  input  D0,
  input  D1,
  input  C0,
  input  C1,
  input  B0,
  input  B1,
  input  A0,
  input  A1,
  output D,
  output C,
  output B,
  output A
);

  and and_1 (D, D0, D1);
  and and_2 (C, C0, C1);
  and and_3 (B, B0, B1);
  and and_4 (A, A0, A1);
endmodule

module Complemento_2 (
  input  in_1,
  input  in_2,
  input  in_3,
  input  in_4,
  output out_5,
  output out_6,
  output out_7,
  output out_8,
  output out_9
);

  wire not_1_out, not_2_out, not_3_out, not_4_out;

  not not_1 (not_1_out, in_1);
  not not_2 (not_2_out, in_2);
  not not_3 (not_3_out, in_3);
  not not_4 (not_4_out, in_4);
  somador4b somador4b_1 (
    .D0(not_1_out), .D1(1'b1), .C0(not_2_out), .C1(1'b0), .B0(not_3_out), .B1(1'b0), .A0(not_4_out),
    .A1(1'b0), .Ovf(out_9), .D(out_5), .C(out_6), .B(out_7), .A(out_8));
endmodule

// Mux 32:4
module Mux32_4 (
  input  in_1,
  input  in_2,
  input  in_3,
  input  D,
  input  C,
  input  B,
  input  A,
  input  D_2,
  input  C_2,
  input  B_2,
  input  A_2,
  input  D_3,
  input  C_3,
  input  B_3,
  input  A_3,
  input  D_4,
  input  C_4,
  input  B_4,
  input  A_4,
  input  D_5,
  input  C_5,
  input  B_5,
  input  A_5,
  input  D_6,
  input  C_6,
  input  B_6,
  input  A_6,
  input  D_7,
  input  C_7,
  input  B_7,
  input  A_7,
  input  D_8,
  input  C_8,
  input  B_8,
  input  A_8,
  output D_9,
  output C_9,
  output B_9,
  output A_9
);

  wire _0_out, _1_out, _2_out, _3_out, _4_out, _5_out, _6_out, _7_out, _8_out, _9_out, _10_out, _11_out,
       _12_out, _13_out, _14_out, _15_out, _16_out, _17_out, _18_out, _19_out, _20_out, _21_out, _22_out,
       _23_out, _24_out, _25_out, _26_out, _27_out, _28_out, _29_out, _30_out, _31_out, and_1_out, and_2_out,
       and_3_out, and_4_out, and_5_out, and_6_out, and_7_out, and_8_out, not_1_out, not_2_out, not_3_out,
       or_1_out, or_2_out, or_3_out, or_4_out, or_5_out, or_6_out, or_7_out, or_8_out;

  not not_1 (not_1_out, in_2);
  not not_2 (not_2_out, in_3);
  and _0 (_0_out, D, not_1_out, not_2_out);
  and _1 (_1_out, D_2, not_1_out, in_3);
  and _2 (_2_out, D_3, in_2, not_2_out);
  and _3 (_3_out, D_4, in_2, in_3);
  and _4 (_4_out, D_5, not_1_out, not_2_out);
  and _5 (_5_out, D_6, not_1_out, in_3);
  and _6 (_6_out, D_7, in_2, not_2_out);
  and _7 (_7_out, D_8, in_2, in_3);
  and _8 (_8_out, C, not_1_out, not_2_out);
  and _9 (_9_out, C_2, not_1_out, in_3);
  and _10 (_10_out, C_3, in_2, not_2_out);
  and _11 (_11_out, C_4, in_2, in_3);
  and _12 (_12_out, C_5, not_1_out, not_2_out);
  and _13 (_13_out, C_6, not_1_out, in_3);
  and _14 (_14_out, C_7, in_2, not_2_out);
  and _15 (_15_out, C_8, C_8, in_2, in_3);
  and _16 (_16_out, B, not_1_out, not_2_out);
  and _17 (_17_out, B_2, not_1_out, in_3);
  and _18 (_18_out, B_3, in_2, not_2_out);
  and _19 (_19_out, B_4, in_2, in_3);
  and _20 (_20_out, B_5, not_1_out, not_2_out);
  and _21 (_21_out, B_6, not_1_out, in_3);
  and _22 (_22_out, B_7, in_2, not_2_out);
  and _23 (_23_out, B_8, in_2, in_3);
  and _24 (_24_out, A, not_1_out, not_2_out);
  and _25 (_25_out, A_2, not_1_out, in_3);
  and _26 (_26_out, A_3, in_2, not_2_out);
  and _27 (_27_out, A_4, in_2, in_3);
  and _28 (_28_out, A_5, not_1_out, not_2_out);
  and _29 (_29_out, A_6, not_1_out, in_3);
  and _30 (_30_out, A_7, in_2, not_2_out);
  and _31 (_31_out, A_8, in_2, in_3);
  or or_1 (or_1_out, _0_out, _1_out, _2_out, _3_out);
  or or_2 (or_2_out, _4_out, _5_out, _6_out, _7_out);
  or or_3 (or_3_out, _8_out, _9_out, _10_out, _11_out);
  or or_4 (or_4_out, _12_out, _13_out, _14_out, _15_out);
  or or_5 (or_5_out, _16_out, _17_out, _18_out, _19_out);
  or or_6 (or_6_out, _20_out, _21_out, _22_out, _23_out);
  or or_7 (or_7_out, _24_out, _25_out, _26_out, _27_out);
  or or_8 (or_8_out, _28_out, _29_out, _30_out, _31_out);
  not not_3 (not_3_out, in_1);
  and and_1 (and_1_out, or_1_out, not_3_out);
  and and_2 (and_2_out, or_2_out, in_1);
  and and_3 (and_3_out, or_3_out, not_3_out);
  and and_4 (and_4_out, or_4_out, in_1);
  and and_5 (and_5_out, or_5_out, not_3_out);
  and and_6 (and_6_out, or_6_out, in_1);
  and and_7 (and_7_out, or_7_out, not_3_out);
  and and_8 (and_8_out, or_8_out, in_1);
  or or_9 (D_9, and_1_out, and_2_out);
  or or_10 (C_9, and_3_out, and_4_out);
  or or_11 (B_9, and_5_out, and_6_out);
  or or_12 (A_9, and_7_out, and_8_out);
endmodule

// OR 4b
module OR4b (
  input  D0,
  input  D1,
  input  C0,
  input  C1,
  input  B0,
  input  B1,
  input  A0,
  input  A1,
  output D,
  output C,
  output B,
  output A
);

  or or_1 (D, D0, D1);
  or or_2 (C, C0, C1);
  or or_3 (B, B0, B1);
  or or_4 (A, A0, A1);
endmodule

// NAND 4B
module NAND4b (
  input  D0,
  input  D1,
  input  C0,
  input  C1,
  input  B0,
  input  B1,
  input  A0,
  input  A1,
  output out_9,
  output out_10,
  output out_11,
  output out_12
);

  nand nand_1 (out_9, D0, D1);
  nand nand_2 (out_10, C0, C1);
  nand nand_3 (out_11, B0, B1);
  nand nand_4 (out_12, A0, A1);
endmodule

// XOR 4B
module XOR4b (
  input  D0,
  input  D1,
  input  C0,
  input  C1,
  input  B0,
  input  B1,
  input  A0,
  input  A1,
  output D,
  output C,
  output B,
  output A
);

  xor xor_1 (D, D0, D1);
  xor xor_2 (C, C0, C1);
  xor xor_3 (B, B0, B1);
  xor xor_4 (A, A0, A1);
endmodule

// SLT 4B
module SLT4b (
  input  D0,
  input  D1,
  input  C0,
  input  C1,
  input  B0,
  input  B1,
  input  A0,
  input  A1,
  output out_9,
  output out_10,
  output out_11,
  output out_12
);

  subtrador4b subtrador4b_1 (
    .D0(D0), .D1(D1), .C0(C0), .C1(C1), .B0(B0), .B1(B1), .A0(A0), .A1(A1), .Overflow(out_9));  // open: out_9, out_10, out_11, out_12

  assign out_10 = 1'b0;
  assign out_11 = 1'b0;
  assign out_12 = 1'b0;
endmodule

// -
module subtrador1b (
  input  in_1,
  input  in_2,
  input  in_3,
  output out_4,
  output out_5
);

  wire and_1_out, and_2_out, and_3_out, not_1_out, xor_1_out;

  not not_1 (not_1_out, in_2);
  xor xor_1 (xor_1_out, in_2, in_3);
  and and_1 (and_1_out, not_1_out, in_3);
  and and_2 (and_2_out, not_1_out, in_1);
  and and_3 (and_3_out, in_3, in_1);
  xor xor_2 (out_4, xor_1_out, in_1);
  or or_1 (out_5, and_1_out, and_2_out, and_3_out);
endmodule

// subtrador 4B
module subtrador4b (
  input  D0,
  input  D1,
  input  C0,
  input  C1,
  input  B0,
  input  B1,
  input  A0,
  input  A1,
  output out_9,
  output out_10,
  output out_11,
  output out_12,
  output Overflow
);

  wire subtrador1b_1_out_5, subtrador1b_2_out_5, subtrador1b_3_out_5;

  subtrador1b subtrador1b_1 (.in_1(1'b0), .in_2(D0), .in_3(D1), .out_4(out_9), .out_5(subtrador1b_1_out_5));
  subtrador1b subtrador1b_2 (
    .in_1(subtrador1b_1_out_5), .in_2(C0), .in_3(C1), .out_4(out_10), .out_5(subtrador1b_2_out_5));
  subtrador1b subtrador1b_3 (
    .in_1(subtrador1b_2_out_5), .in_2(B0), .in_3(B1), .out_4(out_11), .out_5(subtrador1b_3_out_5));
  subtrador1b subtrador1b_4 (.in_1(subtrador1b_3_out_5), .in_2(A0), .in_3(A1), .out_4(out_12), .out_5(Overflow));
endmodule

// M2:1
module Mux2_1 (
  input  in_1,
  input  in_2,
  input  in_3,
  output out_4
);

  wire and_1_out, and_2_out, not_1_out;

  and and_1 (and_1_out, in_1, in_2);
  and and_2 (and_2_out, in_3, not_1_out);
  not not_1 (not_1_out, in_1);
  or or_1 (out_4, and_1_out, and_2_out);
endmodule

// RFFP
module RG4B (
  input  in_1,
  input  in_2,
  input  in_3,
  input  in_4,
  input  in_5,
  output out_6,
  output out_7,
  output out_8,
  output out_9
);

  D_Flip_Flop d_ff_1 (.clk(in_5), .D(in_1), .Q(out_6));  // open: Qn, preset, en, reset
  D_Flip_Flop d_ff_2 (.clk(in_5), .D(in_2), .Q(out_7));  // open: Qn, preset, en, reset
  D_Flip_Flop d_ff_3 (.clk(in_5), .D(in_3), .Q(out_8));  // open: Qn, preset, en, reset
  D_Flip_Flop d_ff_4 (.clk(in_5), .D(in_4), .Q(out_9));  // open: Qn, preset, en, reset
endmodule

// FFD
module Flip_Flop_D (
  input  D,
  input  CLK,
  output Q_prime,
  output Q
);

  wire and_1_out, and_2_out, not_1_out;

  not not_1 (not_1_out, D);
  and and_1 (and_1_out, D, CLK);
  and and_2 (and_2_out, not_1_out, CLK);
  nor nor_1 (Q_prime, and_1_out, Q);
  nor nor_2 (Q, Q_prime, and_2_out);
endmodule

// RG
module R4B (
  input  DA,
  input  DB,
  input  DC,
  input  DD,
  input  in_5,
  output QA,
  output QB,
  output QC,
  output QD
);

  Flip_Flop_D flip_flop_d_1 (.D(DB), .CLK(in_5), .Q(QB));  // open: Q_prime
  Flip_Flop_D flip_flop_d_2 (.D(DA), .CLK(in_5), .Q(QA));  // open: Q_prime
  Flip_Flop_D flip_flop_d_3 (.D(DC), .CLK(in_5), .Q(QC));  // open: Q_prime
  Flip_Flop_D flip_flop_d_4 (.D(DD), .CLK(in_5), .Q(QD));  // open: Q_prime
endmodule

// ULA 4B
module ULA (
  input  in_1,
  input  in_2,
  input  in_3,
  input  D0,
  input  C0,
  input  B0,
  input  A0,
  input  D1,
  input  C1,
  input  B1,
  input  A1,
  output D,
  output C,
  output B,
  output A
);

  wire and4b_1_a, and4b_1_b, and4b_1_c, and4b_1_d, nand4b_1_out_9, nand4b_1_out_10, nand4b_1_out_11,
       nand4b_1_out_12, or4b_1_a, or4b_1_b, or4b_1_c, or4b_1_d, slt4b_1_out_9, slt4b_1_out_10,
       slt4b_1_out_11, slt4b_1_out_12, somador4b_1_a, somador4b_1_b, somador4b_1_c, somador4b_1_d,
       somador4b_2_a, somador4b_2_b, somador4b_2_c, somador4b_2_d, subtrador4b_1_out_9, subtrador4b_1_out_10,
       subtrador4b_1_out_11, subtrador4b_1_out_12, xor4b_1_a, xor4b_1_b, xor4b_1_c, xor4b_1_d;

  AND4b and4b_1 (
    .D0(D0), .D1(D1), .C0(C0), .C1(C1), .B0(B0), .B1(B1), .A0(A0), .A1(A1), .D(and4b_1_d), .C(and4b_1_c),
    .B(and4b_1_b), .A(and4b_1_a));
  OR4b or4b_1 (
    .D0(D0), .D1(D1), .C0(C0), .C1(C1), .B0(B0), .B1(B1), .A0(A0), .A1(A1), .D(or4b_1_d), .C(or4b_1_c),
    .B(or4b_1_b), .A(or4b_1_a));
  NAND4b nand4b_1 (
    .D0(D0), .D1(D1), .C0(C0), .C1(C1), .B0(B0), .B1(B1), .A0(A0), .A1(A1), .out_9(nand4b_1_out_9),
    .out_10(nand4b_1_out_10), .out_11(nand4b_1_out_11), .out_12(nand4b_1_out_12));
  XOR4b xor4b_1 (
    .D0(D0), .D1(D1), .C0(C0), .C1(C1), .B0(B0), .B1(B1), .A0(A0), .A1(A1), .D(xor4b_1_d), .C(xor4b_1_c),
    .B(xor4b_1_b), .A(xor4b_1_a));
  somador4b somador4b_1 (
    .D0(D0), .D1(D1), .C0(C0), .C1(C1), .B0(B0), .B1(B1), .A0(A0), .A1(A1), .D(somador4b_1_d),
    .C(somador4b_1_c), .B(somador4b_1_b), .A(somador4b_1_a));  // open: Ovf
  subtrador4b subtrador4b_1 (
    .D0(D0), .D1(D1), .C0(C0), .C1(C1), .B0(B0), .B1(B1), .A0(A0), .A1(A1), .out_9(subtrador4b_1_out_9),
    .out_10(subtrador4b_1_out_10), .out_11(subtrador4b_1_out_11), .out_12(subtrador4b_1_out_12));  // open: Overflow
  somador4b somador4b_2 (
    .D0(D0), .D1(D1), .C0(C0), .C1(C1), .B0(B0), .B1(B1), .A0(A0), .A1(A1), .D(somador4b_2_d),
    .C(somador4b_2_c), .B(somador4b_2_b), .A(somador4b_2_a));  // open: Ovf
  SLT4b slt4b_1 (
    .D0(D0), .D1(D1), .C0(C0), .C1(C1), .B0(B0), .B1(B1), .A0(A0), .A1(A1), .out_9(slt4b_1_out_9),
    .out_10(slt4b_1_out_10), .out_11(slt4b_1_out_11), .out_12(slt4b_1_out_12));
  Mux32_4 mux32_4_1 (
    .D(and4b_1_d), .C(and4b_1_c), .B(and4b_1_b), .A(and4b_1_a), .D_2(or4b_1_d), .C_2(or4b_1_c),
    .B_2(or4b_1_b), .A_2(or4b_1_a), .D_3(nand4b_1_out_9), .C_3(nand4b_1_out_10), .B_3(nand4b_1_out_11),
    .A_3(nand4b_1_out_12), .D_4(xor4b_1_d), .C_4(xor4b_1_c), .B_4(xor4b_1_b), .A_4(xor4b_1_a),
    .D_5(somador4b_1_d), .C_5(somador4b_1_c), .B_5(somador4b_1_b), .A_5(somador4b_1_a),
    .D_6(subtrador4b_1_out_9), .C_6(subtrador4b_1_out_10), .B_6(subtrador4b_1_out_11),
    .A_6(subtrador4b_1_out_12), .D_7(somador4b_2_d), .C_7(somador4b_2_c), .B_7(somador4b_2_b),
    .A_7(somador4b_2_a), .D_8(slt4b_1_out_9), .C_8(slt4b_1_out_10), .B_8(slt4b_1_out_11),
    .A_8(slt4b_1_out_12), .in_1(in_1), .in_2(in_2), .in_3(in_3), .D_9(D), .C_9(C), .B_9(B), .A_9(A));
endmodule

// L1 32 BITS
module L1_32b (
  input  A,
  input  B,
  input  C,
  input  D,
  input  R0,
  input  R1,
  input  R2,
  input  R3,
  input  R4,
  input  R5,
  input  R6,
  input  R7,
  output D_2,
  output C_2,
  output B_2,
  output A_2,
  output D_3,
  output C_3,
  output B_3,
  output A_3,
  output D_4,
  output C_4,
  output B_4,
  output A_4,
  output D_5,
  output C_5,
  output B_5,
  output A_5,
  output D_6,
  output C_6,
  output B_6,
  output A_6,
  output D_7,
  output C_7,
  output B_7,
  output A_7,
  output D_8,
  output C_8,
  output B_8,
  output A_8,
  output D_9,
  output C_9,
  output B_9,
  output A_9
);

  R4B r4b_1 (.in_5(R0), .DA(A), .DB(B), .DC(C), .DD(D), .QA(A_2), .QB(B_2), .QC(C_2), .QD(D_2));
  R4B r4b_2 (.in_5(R1), .DA(A), .DB(B), .DC(C), .DD(D), .QA(A_3), .QB(B_3), .QC(C_3), .QD(D_3));
  R4B r4b_3 (.in_5(R2), .DA(A), .DB(B), .DC(C), .DD(D), .QA(A_4), .QB(B_4), .QC(C_4), .QD(D_4));
  R4B r4b_4 (.in_5(R3), .DA(A), .DB(B), .DC(C), .DD(D), .QA(A_5), .QB(B_5), .QC(C_5), .QD(D_5));
  R4B r4b_5 (.in_5(R4), .DA(A), .DB(B), .DC(C), .DD(D), .QA(A_6), .QB(B_6), .QC(C_6), .QD(D_6));
  R4B r4b_6 (.in_5(R5), .DA(A), .DB(B), .DC(C), .DD(D), .QA(A_7), .QB(B_7), .QC(C_7), .QD(D_7));
  R4B r4b_7 (.in_5(R6), .DA(A), .DB(B), .DC(C), .DD(D), .QA(A_8), .QB(B_8), .QC(C_8), .QD(D_8));
  R4B r4b_8 (.in_5(R7), .DA(A), .DB(B), .DC(C), .DD(D), .QA(A_9), .QB(B_9), .QC(C_9), .QD(D_9));
endmodule

// Dmux 1:8
module Dmux1_8 (
  input  in_1,
  input  in_2,
  input  in_3,
  input  E,
  output S0,
  output S1,
  output S2,
  output S3,
  output S4,
  output S5,
  output S6,
  output S7
);

  wire not_1_out, not_2_out, not_3_out, not_4_out, not_5_out, not_6_out, not_7_out, not_8_out, not_9_out,
       not_10_out, not_11_out, not_12_out;

  not not_1 (not_1_out, in_1);
  not not_2 (not_2_out, in_2);
  not not_3 (not_3_out, in_3);
  not not_4 (not_4_out, in_1);
  not not_5 (not_5_out, in_2);
  not not_6 (not_6_out, in_1);
  not not_7 (not_7_out, in_3);
  not not_8 (not_8_out, in_1);
  not not_9 (not_9_out, in_2);
  not not_10 (not_10_out, in_3);
  not not_11 (not_11_out, in_2);
  not not_12 (not_12_out, in_3);
  and and_1 (S0, not_1_out, not_2_out, not_3_out, E);
  and and_2 (S1, not_4_out, not_5_out, in_3, E);
  and and_3 (S2, not_6_out, in_2, not_7_out, E);
  and and_4 (S3, not_8_out, in_2, in_3, E);
  and and_5 (S4, in_1, not_9_out, not_10_out, E);
  and and_6 (S5, in_1, not_11_out, in_3, E);
  and and_7 (S6, in_1, in_2, not_12_out, E);
  and and_8 (S7, in_1, in_2, in_3, E);
endmodule

module BCD8421 (
  input  _0,
  input  _1,
  input  _2,
  input  _3,
  input  _4,
  input  _5,
  input  _6,
  input  _7,
  input  _8,
  input  _9,
  output A,
  output B,
  output C,
  output D
);

  wire nand_1_out, nand_2_out, nand_3_out, nand_4_out, not_1_out, not_2_out, not_3_out, not_4_out, not_5_out,
       not_6_out, not_7_out, not_8_out, not_9_out, or_1_out;

  or or_1 (or_1_out, _9, _8, _7, _6, _5, _4, _3, _2, _1, _0);
  not not_1 (not_1_out, _2);
  not not_2 (not_2_out, _1);
  not not_3 (not_3_out, _3);
  not not_4 (not_4_out, _4);
  R4B r4b_1 (
    .in_5(or_1_out), .DA(nand_4_out), .DB(nand_3_out), .DC(nand_2_out), .DD(nand_1_out), .QA(A), .QB(B),
    .QC(C), .QD(D));
  not not_5 (not_5_out, _5);
  not not_6 (not_6_out, _6);
  not not_7 (not_7_out, _8);
  not not_8 (not_8_out, _7);
  not not_9 (not_9_out, _9);
  nand nand_1 (nand_1_out, not_2_out, not_3_out, not_5_out, not_8_out, not_9_out);
  nand nand_2 (nand_2_out, not_1_out, not_3_out, not_6_out, not_8_out);
  nand nand_3 (nand_3_out, not_4_out, not_5_out, not_6_out, not_8_out);
  nand nand_4 (nand_4_out, not_7_out, not_9_out);
endmodule

// Mux 8:4
module Mux8_4 (
  input  in_1,
  input  D,
  input  C,
  input  B,
  input  A,
  input  D_2,
  input  C_2,
  input  B_2,
  input  A_2,
  output D_3,
  output C_3,
  output B_3,
  output A_3
);

  wire and_1_out, and_2_out, and_3_out, and_4_out, and_5_out, and_6_out, and_7_out, and_8_out, not_1_out,
       not_2_out, not_3_out, not_4_out;

  not not_1 (not_1_out, in_1);
  not not_2 (not_2_out, in_1);
  not not_3 (not_3_out, in_1);
  not not_4 (not_4_out, in_1);
  and and_1 (and_1_out, D, in_1);
  and and_2 (and_2_out, D_2, not_1_out);
  and and_3 (and_3_out, C, in_1);
  and and_4 (and_4_out, C_2, not_2_out);
  and and_5 (and_5_out, B, in_1);
  and and_6 (and_6_out, B_2, not_3_out);
  and and_7 (and_7_out, A, in_1);
  and and_8 (and_8_out, A_2, not_4_out);
  or or_1 (D_3, and_1_out, and_2_out);
  or or_2 (C_3, and_3_out, and_4_out);
  or or_3 (B_3, and_5_out, and_6_out);
  or or_4 (A_3, and_7_out, and_8_out);
endmodule

module Keyboards (
);

  wire _0_2_out, _1_2_out, _2_2_out, _3_2_out, _4_2_out, _5_2_out, _6_2_out, _7_2_out, bcd8421_1_b,
       bcd8421_1_c, bcd8421_1_d, bcd8421_2_a, bcd8421_2_b, bcd8421_2_c, bcd8421_2_d, bcdd8421_0_15_1_a,
       bcdd8421_0_15_1_b, bcdd8421_0_15_1_c, bcdd8421_0_15_1_d, button_2_out, button_3_out, button_4_out,
       button_5_out, button_6_out, button_7_out, button_out, s_out;
  wire [3:0] bcdd8421_0_15_2_d;
  wire [15:0] _0_3_out, _0_out;

  Button _0 (.out(_0_out[0]));
  Button _1 (.out(_0_out[1]));
  Button _4 (.out(_0_out[4]));
  Button _5 (.out(_0_out[5]));
  Button _9 (.out(_0_out[9]));
  Button _8 (.out(_0_out[8]));
  Button _13 (.out(_0_out[13]));
  Button _12 (.out(_0_out[12]));
  BCDD8421_0_15 bcdd8421_0_15_1 (
    ._0(_0_out[0]), ._1(_0_out[1]), ._2(_0_out[2]), ._3(_0_out[3]), ._4(_0_out[4]), ._5(_0_out[5]),
    ._6(_0_out[6]), ._7(_0_out[7]), ._8(_0_out[8]), ._9(_0_out[9]), ._10(_0_out[10]), ._11(_0_out[11]),
    ._12(_0_out[12]), ._13(_0_out[13]), ._14(_0_out[14]), ._15(_0_out[15]), .A(bcdd8421_0_15_1_a),
    .B(bcdd8421_0_15_1_b), .C(bcdd8421_0_15_1_c), .D(bcdd8421_0_15_1_d));
  Button _2 (.out(_0_out[2]));
  Button _3 (.out(_0_out[3]));
  Button _6 (.out(_0_out[6]));
  Button _7 (.out(_0_out[7]));
  Button _11 (.out(_0_out[11]));
  Button _10 (.out(_0_out[10]));
  Button _14 (.out(_0_out[14]));
  Button _15 (.out(_0_out[15]));
  Button _1_2 (.out(_1_2_out));
  Button _0_2 (.out(_0_2_out));
  BCD8421 bcd8421_1 (
    ._0(_0_2_out), ._1(_1_2_out), ._2(_2_2_out), ._3(_3_2_out), ._4(_4_2_out), ._5(_5_2_out), ._6(_6_2_out),
    ._7(_7_2_out), ._8(1'b0), ._9(1'b0), .B(bcd8421_1_b), .C(bcd8421_1_c), .D(bcd8421_1_d));  // open: A
  Button _3_2 (.out(_3_2_out));
  Button _2_2 (.out(_2_2_out));
  Button _4_2 (.out(_4_2_out));
  Button _5_2 (.out(_5_2_out));
  Button _0_3 (.out(_0_3_out[0]));
  Button _4_3 (.out(_0_3_out[4]));
  Button _8_2 (.out(_0_3_out[8]));
  Button _12_2 (.out(_0_3_out[12]));
  Button _7_2 (.out(_7_2_out));
  Button _6_2 (.out(_6_2_out));
  BCDD8421_0_15 bcdd8421_0_15_2 (
    ._0(_0_3_out[0]), ._1(_0_3_out[1]), ._2(_0_3_out[2]), ._3(_0_3_out[3]), ._4(_0_3_out[4]),
    ._5(_0_3_out[5]), ._6(_0_3_out[6]), ._7(_0_3_out[7]), ._8(_0_3_out[8]), ._9(_0_3_out[9]),
    ._10(_0_3_out[10]), ._11(_0_3_out[11]), ._12(_0_3_out[12]), ._13(_0_3_out[13]), ._14(_0_3_out[14]),
    ._15(_0_3_out[15]), .A(bcdd8421_0_15_2_d[3]), .B(bcdd8421_0_15_2_d[2]), .C(bcdd8421_0_15_2_d[1]),
    .D(bcdd8421_0_15_2_d[0]));
  Button _3_3 (.out(_0_3_out[3]));
  Button _2_3 (.out(_0_3_out[2]));
  Button _1_3 (.out(_0_3_out[1]));
  Button _6_3 (.out(_0_3_out[6]));
  Button _5_3 (.out(_0_3_out[5]));
  Button _7_3 (.out(_0_3_out[7]));
  Button _11_2 (.out(_0_3_out[11]));
  Button _10_2 (.out(_0_3_out[10]));
  Button _9_2 (.out(_0_3_out[9]));
  Button _14_2 (.out(_0_3_out[14]));
  Button _13_2 (.out(_0_3_out[13]));
  Button _15_2 (.out(_0_3_out[15]));
  Button button (.out(button_out));
  Button button_2 (.out(button_2_out));
  BCD8421 bcd8421_2 (
    ._0(button_out), ._1(button_4_out), ._2(button_3_out), ._3(button_5_out), ._4(button_2_out),
    ._5(button_6_out), ._6(button_7_out), ._7(s_out), ._8(1'b0), ._9(1'b0), .A(bcd8421_2_a), .B(bcd8421_2_b),
    .C(bcd8421_2_c), .D(bcd8421_2_d));
  Hex_Digit_Display hex_digit_display_1 (.value(bcdd8421_0_15_2_d));  // open: dp
  Button button_3 (.out(button_3_out));
  Button button_4 (.out(button_4_out));
  Button button_5 (.out(button_5_out));
  Button button_6 (.out(button_6_out));
  Button button_7 (.out(button_7_out));
  Button s (.out(s_out));

  // Notes on the sheet:
  //   INPUT
  //   INPUT
endmodule

// MUX 12:1
module Mux12_1 (
  input  in_1,
  input  in_2,
  input  in_3,
  input  in_4,
  input  in_5,
  input  in_6,
  input  in_7,
  input  in_8,
  input  in_9,
  input  in_10,
  input  in_11,
  input  in_12,
  input  in_13,
  input  in_14,
  input  in_15,
  input  in_16,
  input  in_17,
  input  in_18,
  input  in_19,
  input  in_20,
  output out_21,
  output out_22,
  output out_23,
  output out_24,
  output out_25
);

  wire and_1_out, and_2_out, and_3_out, and_4_out, and_5_out, and_6_out, and_7_out, and_8_out, and_9_out,
       and_10_out, and_11_out, and_12_out, and_14_out, and_15_out, and_16_out, and_17_out, and_18_out,
       and_19_out, and_20_out, and_21_out, and_22_out, and_23_out, and_24_out, and_25_out, and_26_out,
       and_27_out, and_28_out, and_29_out, and_30_out, and_31_out, and_32_out;

  and and_1 (and_1_out, ~in_1, ~in_2, ~in_3, ~in_4);  // AND_Gate
  and and_2 (and_2_out, ~in_1, ~in_2, ~in_3, in_4);  // AND_Gate
  and and_3 (and_3_out, ~in_1, ~in_2, in_3, ~in_4);  // AND_Gate
  and and_4 (and_4_out, ~in_1, ~in_2, in_3, in_4);  // AND_Gate
  and and_5 (and_5_out, ~in_1, in_2, ~in_3, ~in_4);  // AND_Gate
  and and_6 (and_6_out, ~in_1, in_2, ~in_3, in_4);  // AND_Gate
  and and_7 (and_7_out, ~in_1, in_2, in_3, ~in_4);  // AND_Gate
  and and_8 (and_8_out, ~in_1, in_2, in_3, in_4);  // AND_Gate
  and and_9 (and_9_out, in_1, ~in_2, ~in_3, ~in_4);  // AND_Gate
  and and_10 (and_10_out, in_1, ~in_2, ~in_3, in_4);  // AND_Gate
  and and_11 (and_11_out, in_1, ~in_2, in_3, ~in_4);  // AND_Gate
  and and_12 (and_12_out, in_1, ~in_2, in_3, in_4);  // AND_Gate
  // AND_Gate and_13 has open pins: in0=in_1, in1=in_2, in2=in_3, in3=in_4, out=open
  and and_14 (and_14_out, in_1, in_2, ~in_3, in_4);  // AND_Gate
  and and_15 (and_15_out, in_1, in_2, in_3, ~in_4);  // AND_Gate
  and and_16 (and_16_out, in_1, in_2, in_3, in_4);
  and and_17 (and_17_out, and_1_out, in_5);
  and and_18 (and_18_out, and_2_out, in_6);
  and and_19 (and_19_out, and_3_out, in_7);
  and and_20 (and_20_out, and_4_out, in_8);
  and and_21 (and_21_out, and_5_out, in_9);
  and and_22 (and_22_out, and_6_out, in_10);
  and and_23 (and_23_out, and_7_out, in_11);
  and and_24 (and_24_out, and_8_out, in_12);
  and and_25 (and_25_out, and_9_out, in_13);
  and and_26 (and_26_out, and_10_out, in_14);
  and and_27 (and_27_out, and_11_out, in_15);
  and and_28 (and_28_out, and_12_out, in_16);
  buf and_29 (and_29_out, in_17);  // AND_Gate
  and and_30 (and_30_out, and_14_out, in_18);
  and and_31 (and_31_out, and_15_out, in_19);
  and and_32 (and_32_out, and_16_out, in_20);
  or or_1 (out_21, and_17_out, and_18_out, and_19_out, and_20_out, and_21_out, and_22_out, and_23_out, and_24_out, and_25_out, and_26_out, and_27_out, and_28_out, and_29_out, and_30_out, and_31_out, and_32_out);

  assign out_22 = in_1;
  assign out_23 = in_2;
  assign out_24 = in_3;
  assign out_25 = in_4;
endmodule

// RG12B
module Registrador12B (
  input  in_1,
  input  in_2,
  input  in_3,
  input  in_4,
  input  in_5,
  input  in_6,
  input  in_7,
  input  in_8,
  input  in_9,
  input  in_10,
  input  in_11,
  input  in_12,
  input  in_13,
  output out_14,
  output out_15,
  output out_16,
  output out_17,
  output out_18,
  output out_19,
  output out_20,
  output out_21,
  output out_22,
  output out_23,
  output out_24,
  output out_25
);

  Flip_Flop_D flip_flop_d_1 (.D(in_1), .CLK(in_13), .Q(out_14));  // open: Q_prime
  Flip_Flop_D flip_flop_d_2 (.D(in_2), .CLK(in_13), .Q(out_15));  // open: Q_prime
  Flip_Flop_D flip_flop_d_3 (.D(in_3), .CLK(in_13), .Q(out_16));  // open: Q_prime
  Flip_Flop_D flip_flop_d_4 (.D(in_4), .CLK(in_13), .Q(out_17));  // open: Q_prime
  Flip_Flop_D flip_flop_d_5 (.D(in_5), .CLK(in_13), .Q(out_18));  // open: Q_prime
  Flip_Flop_D flip_flop_d_6 (.D(in_6), .CLK(in_13), .Q(out_19));  // open: Q_prime
  Flip_Flop_D flip_flop_d_7 (.D(in_8), .CLK(in_13), .Q(out_21));  // open: Q_prime
  Flip_Flop_D flip_flop_d_8 (.D(in_7), .CLK(in_13), .Q(out_20));  // open: Q_prime
  Flip_Flop_D flip_flop_d_9 (.D(in_9), .CLK(in_13), .Q(out_22));  // open: Q_prime
  Flip_Flop_D flip_flop_d_10 (.D(in_10), .CLK(in_13), .Q(out_23));  // open: Q_prime
  Flip_Flop_D flip_flop_d_11 (.D(in_11), .CLK(in_13), .Q(out_24));  // open: Q_prime
  Flip_Flop_D flip_flop_d_12 (.D(in_12), .CLK(in_13), .Q(out_25));  // open: Q_prime
endmodule

module R12 (
  input  A,
  input  B,
  input  C,
  input  D,
  input  E,
  input  F,
  input  G,
  input  H,
  input  I,
  input  J,
  input  L,
  input  M,
  input  in_13,
  output out_14,
  output out_15,
  output out_16,
  output out_17,
  output out_18,
  output out_19,
  output out_20,
  output out_21,
  output out_22,
  output out_23,
  output out_24,
  output out_25,
  output out_26,
  output out_27,
  output out_28,
  output out_29,
  output out_30,
  output out_31,
  output out_32,
  output out_33,
  output out_34,
  output out_35,
  output out_36,
  output out_37
);

  Registrador12B registrador12b_1 (
    .in_13(in_13), .in_1(M), .in_2(L), .in_3(J), .in_4(I), .in_5(H), .in_6(G), .in_7(F), .in_8(E), .in_9(D),
    .in_10(C), .in_11(B), .in_12(A), .out_14(out_25), .out_15(out_24), .out_16(out_23), .out_17(out_22),
    .out_18(out_21), .out_19(out_20), .out_20(out_19), .out_21(out_18), .out_22(out_17), .out_23(out_16),
    .out_24(out_15), .out_25(out_14));

  assign out_26 = A;
  assign out_27 = B;
  assign out_28 = C;
  assign out_29 = D;
  assign out_30 = E;
  assign out_31 = F;
  assign out_32 = G;
  assign out_33 = H;
  assign out_34 = I;
  assign out_35 = J;
  assign out_36 = L;
  assign out_37 = M;
endmodule

// REGISTRADOR DE INSTRUNÇÕES 12 BITS
module RI12_12Bits (
  input  BRCLK2,
  input  BRCLK1,
  input  BRCLK0,
  input  MuxA2,
  input  MuxA1,
  input  MuxA0,
  input  MuxB2,
  input  MuxB1,
  input  MuxB0,
  input  ULA2,
  input  ULA1,
  input  ULA0,
  input  in_13,
  input  in_14,
  input  in_15,
  input  in_16,
  input  in_17,
  input  in_18,
  input  in_19,
  input  in_20,
  input  in_21,
  input  in_22,
  input  in_23,
  input  in_24,
  input  in_25,
  input  in_26,
  input  in_27,
  input  in_28,
  output out_29,
  output out_30,
  output out_31,
  output out_32,
  output out_33,
  output out_34,
  output out_35,
  output out_36,
  output out_37,
  output out_38,
  output out_39,
  output out_40,
  output out_41,
  output out_42,
  output out_43,
  output out_44,
  output out_45,
  output out_46,
  output out_47,
  output out_48,
  output out_49,
  output out_50,
  output out_51,
  output out_52,
  output out_53,
  output out_54,
  output out_55,
  output out_56,
  output out_57,
  output out_58,
  output out_59,
  output out_60,
  output out_61,
  output out_62,
  output out_63,
  output out_64,
  output out_65,
  output out_66,
  output out_67,
  output out_68,
  output out_69,
  output out_70,
  output out_71,
  output out_72,
  output out_73,
  output out_74,
  output out_75,
  output out_76,
  output out_77,
  output out_78,
  output out_79,
  output out_80,
  output out_81,
  output out_82,
  output out_83,
  output out_84,
  output out_85,
  output out_86,
  output out_87,
  output out_88,
  output out_89,
  output out_90,
  output out_91,
  output out_92,
  output out_93,
  output out_94,
  output out_95,
  output out_96,
  output out_97,
  output out_98,
  output out_99,
  output out_100,
  output out_101,
  output out_102,
  output out_103,
  output out_104,
  output out_105,
  output out_106,
  output out_107,
  output out_108,
  output out_109,
  output out_110,
  output out_111,
  output out_112,
  output out_113,
  output out_114,
  output out_115,
  output out_116,
  output out_117,
  output out_118,
  output out_119,
  output out_120,
  output out_121,
  output out_122,
  output out_123,
  output out_124,
  output out_125,
  output out_126,
  output out_127,
  output out_128,
  output out_129,
  output out_130,
  output out_131,
  output out_132,
  output out_133,
  output out_134,
  output out_135,
  output out_136,
  output out_137,
  output out_138,
  output out_139,
  output out_140,
  output out_141,
  output out_142,
  output out_143,
  output out_144,
  output out_145,
  output out_146,
  output out_147,
  output out_148,
  output out_149,
  output out_150,
  output out_151,
  output out_152,
  output out_153,
  output out_154,
  output out_155,
  output out_156,
  output out_157,
  output out_158,
  output out_159,
  output out_160,
  output out_161,
  output out_162,
  output out_163,
  output out_164,
  output out_165,
  output out_166,
  output out_167,
  output out_168,
  output out_169,
  output out_170,
  output out_171,
  output out_172,
  output out_173,
  output out_174,
  output out_175,
  output out_176,
  output out_177,
  output out_178,
  output out_179,
  output out_180,
  output out_181,
  output out_182,
  output out_183,
  output out_184,
  output out_185,
  output out_186,
  output out_187,
  output out_188,
  output out_189,
  output out_190,
  output out_191,
  output out_192,
  output out_193,
  output out_194,
  output out_195,
  output out_196,
  output out_197,
  output out_198,
  output out_199,
  output out_200,
  output out_201,
  output out_202,
  output out_203,
  output out_204,
  output out_205,
  output out_206,
  output out_207,
  output out_208,
  output out_209,
  output out_210,
  output out_211,
  output out_212,
  output out_213,
  output out_214,
  output out_215,
  output out_216,
  output out_217,
  output out_218,
  output out_219,
  output out_220
);

  wire r12_1_out_26, r12_1_out_27, r12_1_out_28, r12_1_out_29, r12_1_out_30, r12_1_out_31, r12_1_out_32,
       r12_1_out_33, r12_1_out_34, r12_1_out_35, r12_1_out_36, r12_1_out_37, r12_2_out_26, r12_2_out_27,
       r12_2_out_28, r12_2_out_29, r12_2_out_30, r12_2_out_31, r12_2_out_32, r12_2_out_33, r12_2_out_34,
       r12_2_out_35, r12_2_out_36, r12_2_out_37, r12_3_out_26, r12_3_out_27, r12_3_out_28, r12_3_out_29,
       r12_3_out_30, r12_3_out_31, r12_3_out_32, r12_3_out_33, r12_3_out_34, r12_3_out_35, r12_3_out_36,
       r12_3_out_37, r12_4_out_26, r12_4_out_27, r12_4_out_28, r12_4_out_29, r12_4_out_30, r12_4_out_31,
       r12_4_out_32, r12_4_out_33, r12_4_out_34, r12_4_out_35, r12_4_out_36, r12_4_out_37, r12_5_out_26,
       r12_5_out_27, r12_5_out_28, r12_5_out_29, r12_5_out_30, r12_5_out_31, r12_5_out_32, r12_5_out_33,
       r12_5_out_34, r12_5_out_35, r12_5_out_36, r12_5_out_37, r12_6_out_26, r12_6_out_27, r12_6_out_28,
       r12_6_out_29, r12_6_out_30, r12_6_out_31, r12_6_out_32, r12_6_out_33, r12_6_out_34, r12_6_out_35,
       r12_6_out_36, r12_6_out_37, r12_7_out_26, r12_7_out_27, r12_7_out_28, r12_7_out_29, r12_7_out_30,
       r12_7_out_31, r12_7_out_32, r12_7_out_33, r12_7_out_34, r12_7_out_35, r12_7_out_36, r12_7_out_37,
       r12_8_out_26, r12_8_out_27, r12_8_out_28, r12_8_out_29, r12_8_out_30, r12_8_out_31, r12_8_out_32,
       r12_8_out_33, r12_8_out_34, r12_8_out_35, r12_8_out_36, r12_8_out_37, r12_9_out_26, r12_9_out_27,
       r12_9_out_28, r12_9_out_29, r12_9_out_30, r12_9_out_31, r12_9_out_32, r12_9_out_33, r12_9_out_34,
       r12_9_out_35, r12_9_out_36, r12_9_out_37, r12_10_out_26, r12_10_out_27, r12_10_out_28, r12_10_out_29,
       r12_10_out_30, r12_10_out_31, r12_10_out_32, r12_10_out_33, r12_10_out_34, r12_10_out_35,
       r12_10_out_36, r12_10_out_37, r12_11_out_26, r12_11_out_27, r12_11_out_28, r12_11_out_29,
       r12_11_out_30, r12_11_out_31, r12_11_out_32, r12_11_out_33, r12_11_out_34, r12_11_out_35,
       r12_11_out_36, r12_11_out_37, r12_12_out_26, r12_12_out_27, r12_12_out_28, r12_12_out_29,
       r12_12_out_30, r12_12_out_31, r12_12_out_32, r12_12_out_33, r12_12_out_34, r12_12_out_35,
       r12_12_out_36, r12_12_out_37, r12_13_out_26, r12_13_out_27, r12_13_out_28, r12_13_out_29,
       r12_13_out_30, r12_13_out_31, r12_13_out_32, r12_13_out_33, r12_13_out_34, r12_13_out_35,
       r12_13_out_36, r12_13_out_37, r12_14_out_26, r12_14_out_27, r12_14_out_28, r12_14_out_29,
       r12_14_out_30, r12_14_out_31, r12_14_out_32, r12_14_out_33, r12_14_out_34, r12_14_out_35,
       r12_14_out_36, r12_14_out_37, r12_15_out_26, r12_15_out_27, r12_15_out_28, r12_15_out_29,
       r12_15_out_30, r12_15_out_31, r12_15_out_32, r12_15_out_33, r12_15_out_34, r12_15_out_35,
       r12_15_out_36, r12_15_out_37;

  R12 r12_1 (
    .in_13(in_13), .out_14(out_29), .out_15(out_30), .out_16(out_31), .out_17(out_32), .out_18(out_33),
    .out_19(out_34), .out_20(out_35), .out_21(out_36), .out_22(out_37), .out_23(out_38), .out_24(out_39),
    .out_25(out_40), .A(BRCLK2), .B(BRCLK1), .C(BRCLK0), .D(MuxA2), .E(MuxA1), .F(MuxA0), .G(MuxB2),
    .H(MuxB1), .I(MuxB0), .J(ULA2), .L(ULA1), .M(ULA0), .out_26(r12_1_out_26), .out_27(r12_1_out_27),
    .out_28(r12_1_out_28), .out_29(r12_1_out_29), .out_30(r12_1_out_30), .out_31(r12_1_out_31),
    .out_32(r12_1_out_32), .out_33(r12_1_out_33), .out_34(r12_1_out_34), .out_35(r12_1_out_35),
    .out_36(r12_1_out_36), .out_37(r12_1_out_37));
  R12 r12_2 (
    .in_13(in_14), .out_14(out_41), .out_15(out_42), .out_16(out_43), .out_17(out_44), .out_18(out_45),
    .out_19(out_46), .out_20(out_47), .out_21(out_48), .out_22(out_49), .out_23(out_50), .out_24(out_51),
    .out_25(out_52), .A(r12_1_out_26), .B(r12_1_out_27), .C(r12_1_out_28), .D(r12_1_out_29),
    .E(r12_1_out_30), .F(r12_1_out_31), .G(r12_1_out_32), .H(r12_1_out_33), .I(r12_1_out_34),
    .J(r12_1_out_35), .L(r12_1_out_36), .M(r12_1_out_37), .out_26(r12_2_out_26), .out_27(r12_2_out_27),
    .out_28(r12_2_out_28), .out_29(r12_2_out_29), .out_30(r12_2_out_30), .out_31(r12_2_out_31),
    .out_32(r12_2_out_32), .out_33(r12_2_out_33), .out_34(r12_2_out_34), .out_35(r12_2_out_35),
    .out_36(r12_2_out_36), .out_37(r12_2_out_37));
  R12 r12_3 (
    .in_13(in_15), .out_14(out_53), .out_15(out_54), .out_16(out_55), .out_17(out_56), .out_18(out_57),
    .out_19(out_58), .out_20(out_59), .out_21(out_60), .out_22(out_61), .out_23(out_62), .out_24(out_63),
    .out_25(out_64), .A(r12_2_out_26), .B(r12_2_out_27), .C(r12_2_out_28), .D(r12_2_out_29),
    .E(r12_2_out_30), .F(r12_2_out_31), .G(r12_2_out_32), .H(r12_2_out_33), .I(r12_2_out_34),
    .J(r12_2_out_35), .L(r12_2_out_36), .M(r12_2_out_37), .out_26(r12_3_out_26), .out_27(r12_3_out_27),
    .out_28(r12_3_out_28), .out_29(r12_3_out_29), .out_30(r12_3_out_30), .out_31(r12_3_out_31),
    .out_32(r12_3_out_32), .out_33(r12_3_out_33), .out_34(r12_3_out_34), .out_35(r12_3_out_35),
    .out_36(r12_3_out_36), .out_37(r12_3_out_37));
  R12 r12_4 (
    .in_13(in_16), .out_14(out_65), .out_15(out_66), .out_16(out_67), .out_17(out_68), .out_18(out_69),
    .out_19(out_70), .out_20(out_71), .out_21(out_72), .out_22(out_73), .out_23(out_74), .out_24(out_75),
    .out_25(out_76), .A(r12_3_out_26), .B(r12_3_out_27), .C(r12_3_out_28), .D(r12_3_out_29),
    .E(r12_3_out_30), .F(r12_3_out_31), .G(r12_3_out_32), .H(r12_3_out_33), .I(r12_3_out_34),
    .J(r12_3_out_35), .L(r12_3_out_36), .M(r12_3_out_37), .out_26(r12_4_out_26), .out_27(r12_4_out_27),
    .out_28(r12_4_out_28), .out_29(r12_4_out_29), .out_30(r12_4_out_30), .out_31(r12_4_out_31),
    .out_32(r12_4_out_32), .out_33(r12_4_out_33), .out_34(r12_4_out_34), .out_35(r12_4_out_35),
    .out_36(r12_4_out_36), .out_37(r12_4_out_37));
  R12 r12_5 (
    .in_13(in_17), .out_14(out_77), .out_15(out_78), .out_16(out_79), .out_17(out_80), .out_18(out_81),
    .out_19(out_82), .out_20(out_83), .out_21(out_84), .out_22(out_85), .out_23(out_86), .out_24(out_87),
    .out_25(out_88), .A(r12_4_out_26), .B(r12_4_out_27), .C(r12_4_out_28), .D(r12_4_out_29),
    .E(r12_4_out_30), .F(r12_4_out_31), .G(r12_4_out_32), .H(r12_4_out_33), .I(r12_4_out_34),
    .J(r12_4_out_35), .L(r12_4_out_36), .M(r12_4_out_37), .out_26(r12_5_out_26), .out_27(r12_5_out_27),
    .out_28(r12_5_out_28), .out_29(r12_5_out_29), .out_30(r12_5_out_30), .out_31(r12_5_out_31),
    .out_32(r12_5_out_32), .out_33(r12_5_out_33), .out_34(r12_5_out_34), .out_35(r12_5_out_35),
    .out_36(r12_5_out_36), .out_37(r12_5_out_37));
  R12 r12_6 (
    .in_13(in_18), .out_14(out_89), .out_15(out_90), .out_16(out_91), .out_17(out_92), .out_18(out_93),
    .out_19(out_94), .out_20(out_95), .out_21(out_96), .out_22(out_97), .out_23(out_98), .out_24(out_99),
    .out_25(out_100), .A(r12_5_out_26), .B(r12_5_out_27), .C(r12_5_out_28), .D(r12_5_out_29),
    .E(r12_5_out_30), .F(r12_5_out_31), .G(r12_5_out_32), .H(r12_5_out_33), .I(r12_5_out_34),
    .J(r12_5_out_35), .L(r12_5_out_36), .M(r12_5_out_37), .out_26(r12_6_out_26), .out_27(r12_6_out_27),
    .out_28(r12_6_out_28), .out_29(r12_6_out_29), .out_30(r12_6_out_30), .out_31(r12_6_out_31),
    .out_32(r12_6_out_32), .out_33(r12_6_out_33), .out_34(r12_6_out_34), .out_35(r12_6_out_35),
    .out_36(r12_6_out_36), .out_37(r12_6_out_37));
  R12 r12_7 (
    .in_13(in_19), .out_14(out_101), .out_15(out_102), .out_16(out_103), .out_17(out_104), .out_18(out_105),
    .out_19(out_106), .out_20(out_107), .out_21(out_108), .out_22(out_109), .out_23(out_110),
    .out_24(out_111), .out_25(out_112), .A(r12_6_out_26), .B(r12_6_out_27), .C(r12_6_out_28),
    .D(r12_6_out_29), .E(r12_6_out_30), .F(r12_6_out_31), .G(r12_6_out_32), .H(r12_6_out_33),
    .I(r12_6_out_34), .J(r12_6_out_35), .L(r12_6_out_36), .M(r12_6_out_37), .out_26(r12_7_out_26),
    .out_27(r12_7_out_27), .out_28(r12_7_out_28), .out_29(r12_7_out_29), .out_30(r12_7_out_30),
    .out_31(r12_7_out_31), .out_32(r12_7_out_32), .out_33(r12_7_out_33), .out_34(r12_7_out_34),
    .out_35(r12_7_out_35), .out_36(r12_7_out_36), .out_37(r12_7_out_37));
  R12 r12_8 (
    .in_13(in_20), .out_14(out_113), .out_15(out_114), .out_16(out_115), .out_17(out_116), .out_18(out_117),
    .out_19(out_118), .out_20(out_119), .out_21(out_120), .out_22(out_121), .out_23(out_122),
    .out_24(out_123), .out_25(out_124), .A(r12_7_out_26), .B(r12_7_out_27), .C(r12_7_out_28),
    .D(r12_7_out_29), .E(r12_7_out_30), .F(r12_7_out_31), .G(r12_7_out_32), .H(r12_7_out_33),
    .I(r12_7_out_34), .J(r12_7_out_35), .L(r12_7_out_36), .M(r12_7_out_37), .out_26(r12_8_out_26),
    .out_27(r12_8_out_27), .out_28(r12_8_out_28), .out_29(r12_8_out_29), .out_30(r12_8_out_30),
    .out_31(r12_8_out_31), .out_32(r12_8_out_32), .out_33(r12_8_out_33), .out_34(r12_8_out_34),
    .out_35(r12_8_out_35), .out_36(r12_8_out_36), .out_37(r12_8_out_37));
  R12 r12_9 (
    .in_13(in_21), .out_14(out_125), .out_15(out_126), .out_16(out_127), .out_17(out_128), .out_18(out_129),
    .out_19(out_130), .out_20(out_131), .out_21(out_132), .out_22(out_133), .out_23(out_134),
    .out_24(out_135), .out_25(out_136), .A(r12_8_out_26), .B(r12_8_out_27), .C(r12_8_out_28),
    .D(r12_8_out_29), .E(r12_8_out_30), .F(r12_8_out_31), .G(r12_8_out_32), .H(r12_8_out_33),
    .I(r12_8_out_34), .J(r12_8_out_35), .L(r12_8_out_36), .M(r12_8_out_37), .out_26(r12_9_out_26),
    .out_27(r12_9_out_27), .out_28(r12_9_out_28), .out_29(r12_9_out_29), .out_30(r12_9_out_30),
    .out_31(r12_9_out_31), .out_32(r12_9_out_32), .out_33(r12_9_out_33), .out_34(r12_9_out_34),
    .out_35(r12_9_out_35), .out_36(r12_9_out_36), .out_37(r12_9_out_37));
  R12 r12_10 (
    .in_13(in_22), .out_14(out_137), .out_15(out_138), .out_16(out_139), .out_17(out_140), .out_18(out_141),
    .out_19(out_142), .out_20(out_143), .out_21(out_144), .out_22(out_145), .out_23(out_146),
    .out_24(out_147), .out_25(out_148), .A(r12_9_out_26), .B(r12_9_out_27), .C(r12_9_out_28),
    .D(r12_9_out_29), .E(r12_9_out_30), .F(r12_9_out_31), .G(r12_9_out_32), .H(r12_9_out_33),
    .I(r12_9_out_34), .J(r12_9_out_35), .L(r12_9_out_36), .M(r12_9_out_37), .out_26(r12_10_out_26),
    .out_27(r12_10_out_27), .out_28(r12_10_out_28), .out_29(r12_10_out_29), .out_30(r12_10_out_30),
    .out_31(r12_10_out_31), .out_32(r12_10_out_32), .out_33(r12_10_out_33), .out_34(r12_10_out_34),
    .out_35(r12_10_out_35), .out_36(r12_10_out_36), .out_37(r12_10_out_37));
  R12 r12_11 (
    .in_13(in_23), .out_14(out_149), .out_15(out_150), .out_16(out_151), .out_17(out_152), .out_18(out_153),
    .out_19(out_154), .out_20(out_155), .out_21(out_156), .out_22(out_157), .out_23(out_158),
    .out_24(out_159), .out_25(out_160), .A(r12_10_out_26), .B(r12_10_out_27), .C(r12_10_out_28),
    .D(r12_10_out_29), .E(r12_10_out_30), .F(r12_10_out_31), .G(r12_10_out_32), .H(r12_10_out_33),
    .I(r12_10_out_34), .J(r12_10_out_35), .L(r12_10_out_36), .M(r12_10_out_37), .out_26(r12_11_out_26),
    .out_27(r12_11_out_27), .out_28(r12_11_out_28), .out_29(r12_11_out_29), .out_30(r12_11_out_30),
    .out_31(r12_11_out_31), .out_32(r12_11_out_32), .out_33(r12_11_out_33), .out_34(r12_11_out_34),
    .out_35(r12_11_out_35), .out_36(r12_11_out_36), .out_37(r12_11_out_37));
  R12 r12_12 (
    .in_13(in_24), .out_14(out_161), .out_15(out_162), .out_16(out_163), .out_17(out_164), .out_18(out_165),
    .out_19(out_166), .out_20(out_167), .out_21(out_168), .out_22(out_169), .out_23(out_170),
    .out_24(out_171), .out_25(out_172), .A(r12_11_out_26), .B(r12_11_out_27), .C(r12_11_out_28),
    .D(r12_11_out_29), .E(r12_11_out_30), .F(r12_11_out_31), .G(r12_11_out_32), .H(r12_11_out_33),
    .I(r12_11_out_34), .J(r12_11_out_35), .L(r12_11_out_36), .M(r12_11_out_37), .out_26(r12_12_out_26),
    .out_27(r12_12_out_27), .out_28(r12_12_out_28), .out_29(r12_12_out_29), .out_30(r12_12_out_30),
    .out_31(r12_12_out_31), .out_32(r12_12_out_32), .out_33(r12_12_out_33), .out_34(r12_12_out_34),
    .out_35(r12_12_out_35), .out_36(r12_12_out_36), .out_37(r12_12_out_37));
  R12 r12_13 (
    .in_13(in_25), .out_14(out_173), .out_15(out_174), .out_16(out_175), .out_17(out_176), .out_18(out_177),
    .out_19(out_178), .out_20(out_179), .out_21(out_180), .out_22(out_181), .out_23(out_182),
    .out_24(out_183), .out_25(out_184), .A(r12_12_out_26), .B(r12_12_out_27), .C(r12_12_out_28),
    .D(r12_12_out_29), .E(r12_12_out_30), .F(r12_12_out_31), .G(r12_12_out_32), .H(r12_12_out_33),
    .I(r12_12_out_34), .J(r12_12_out_35), .L(r12_12_out_36), .M(r12_12_out_37), .out_26(r12_13_out_26),
    .out_27(r12_13_out_27), .out_28(r12_13_out_28), .out_29(r12_13_out_29), .out_30(r12_13_out_30),
    .out_31(r12_13_out_31), .out_32(r12_13_out_32), .out_33(r12_13_out_33), .out_34(r12_13_out_34),
    .out_35(r12_13_out_35), .out_36(r12_13_out_36), .out_37(r12_13_out_37));
  R12 r12_14 (
    .in_13(in_26), .out_14(out_185), .out_15(out_186), .out_16(out_187), .out_17(out_188), .out_18(out_189),
    .out_19(out_190), .out_20(out_191), .out_21(out_192), .out_22(out_193), .out_23(out_194),
    .out_24(out_195), .out_25(out_196), .A(r12_13_out_26), .B(r12_13_out_27), .C(r12_13_out_28),
    .D(r12_13_out_29), .E(r12_13_out_30), .F(r12_13_out_31), .G(r12_13_out_32), .H(r12_13_out_33),
    .I(r12_13_out_34), .J(r12_13_out_35), .L(r12_13_out_36), .M(r12_13_out_37), .out_26(r12_14_out_26),
    .out_27(r12_14_out_27), .out_28(r12_14_out_28), .out_29(r12_14_out_29), .out_30(r12_14_out_30),
    .out_31(r12_14_out_31), .out_32(r12_14_out_32), .out_33(r12_14_out_33), .out_34(r12_14_out_34),
    .out_35(r12_14_out_35), .out_36(r12_14_out_36), .out_37(r12_14_out_37));
  R12 r12_15 (
    .in_13(in_27), .out_14(out_197), .out_15(out_198), .out_16(out_199), .out_17(out_200), .out_18(out_201),
    .out_19(out_202), .out_20(out_203), .out_21(out_204), .out_22(out_205), .out_23(out_206),
    .out_24(out_207), .out_25(out_208), .A(r12_14_out_26), .B(r12_14_out_27), .C(r12_14_out_28),
    .D(r12_14_out_29), .E(r12_14_out_30), .F(r12_14_out_31), .G(r12_14_out_32), .H(r12_14_out_33),
    .I(r12_14_out_34), .J(r12_14_out_35), .L(r12_14_out_36), .M(r12_14_out_37), .out_26(r12_15_out_26),
    .out_27(r12_15_out_27), .out_28(r12_15_out_28), .out_29(r12_15_out_29), .out_30(r12_15_out_30),
    .out_31(r12_15_out_31), .out_32(r12_15_out_32), .out_33(r12_15_out_33), .out_34(r12_15_out_34),
    .out_35(r12_15_out_35), .out_36(r12_15_out_36), .out_37(r12_15_out_37));
  R12 r12_16 (
    .in_13(in_28), .out_14(out_209), .out_15(out_210), .out_16(out_211), .out_17(out_212), .out_18(out_213),
    .out_19(out_214), .out_20(out_215), .out_21(out_216), .out_22(out_217), .out_23(out_218),
    .out_24(out_219), .out_25(out_220), .A(r12_15_out_26), .B(r12_15_out_27), .C(r12_15_out_28),
    .D(r12_15_out_29), .E(r12_15_out_30), .F(r12_15_out_31), .G(r12_15_out_32), .H(r12_15_out_33),
    .I(r12_15_out_34), .J(r12_15_out_35), .L(r12_15_out_36), .M(r12_15_out_37));  // open: out_26, out_27, out_28, out_29, out_30, out_31, out_32, out_33, out_34, out_35, out_36, out_37
endmodule

module contadorRI (
  input  in_1,
  input  in_2,
  input  in_3,
  input  in_4,
  input  in_5,
  output out_6,
  output out_7,
  output out_8,
  output out_9
);

  wire and_1_out, t_ff_1_q, t_ff_2_q, t_ff_3_q, t_ff_4_q, xor4b_1_a, xor4b_1_b, xor4b_1_c, xor4b_1_d;

  T_Flip_Flop t_ff_1 (.clk(in_1), .T(1'b1), .Q(t_ff_1_q), .reset(and_1_out));  // open: Qn, preset, en
  not not_1 (out_9, t_ff_1_q);
  T_Flip_Flop t_ff_2 (.clk(t_ff_1_q), .T(1'b1), .Q(t_ff_2_q), .reset(and_1_out));  // open: Qn, preset, en
  XOR4b xor4b_1 (
    .D0(in_5), .D1(out_9), .C0(in_4), .C1(out_8), .B0(in_3), .B1(out_7), .A0(in_2), .A1(out_6),
    .D(xor4b_1_d), .C(xor4b_1_c), .B(xor4b_1_b), .A(xor4b_1_a));
  and and_1 (and_1_out, ~xor4b_1_a, ~xor4b_1_b, ~xor4b_1_c, ~xor4b_1_d);  // AND_Gate
  not not_2 (out_8, t_ff_2_q);
  T_Flip_Flop t_ff_3 (.clk(t_ff_2_q), .T(1'b1), .Q(t_ff_3_q), .reset(and_1_out));  // open: Qn, preset, en
  not not_3 (out_7, t_ff_3_q);
  T_Flip_Flop t_ff_4 (.clk(t_ff_3_q), .T(1'b1), .Q(t_ff_4_q), .reset(and_1_out));  // open: Qn, preset, en
  not not_4 (out_6, t_ff_4_q);
endmodule

module Demux1_16 (
  input  in_1,
  input  in_2,
  input  in_3,
  input  in_4,
  input  in_5,
  output out_6,
  output out_7,
  output out_8,
  output out_9,
  output out_10,
  output out_11,
  output out_12,
  output out_13,
  output out_14,
  output out_15,
  output out_16,
  output out_17,
  output out_18,
  output out_19,
  output out_20,
  output out_21
);

  and and_1 (out_6, ~in_1, ~in_2, ~in_3, ~in_4, in_5);  // AND_Gate
  and and_2 (out_7, ~in_1, ~in_2, ~in_3, in_4, in_5);  // AND_Gate
  and and_3 (out_8, ~in_1, ~in_2, in_3, ~in_4, in_5);  // AND_Gate
  and and_4 (out_9, ~in_1, ~in_2, in_3, in_4, in_5);  // AND_Gate
  and and_5 (out_10, ~in_1, in_2, ~in_3, ~in_4, in_5);  // AND_Gate
  and and_6 (out_11, ~in_1, in_2, ~in_3, in_4, in_5);  // AND_Gate
  and and_7 (out_12, ~in_1, in_2, in_3, ~in_4, in_5);  // AND_Gate
  and and_8 (out_13, ~in_1, in_2, in_3, in_4, in_5);  // AND_Gate
  and and_9 (out_14, in_1, ~in_2, ~in_3, ~in_4, in_5);  // AND_Gate
  and and_10 (out_15, in_1, ~in_2, ~in_3, in_4, in_5);  // AND_Gate
  and and_11 (out_16, in_1, ~in_2, in_3, ~in_4, in_5);  // AND_Gate
  and and_12 (out_17, in_1, ~in_2, in_3, in_4, in_5);  // AND_Gate
  and and_13 (out_18, in_1, in_2, ~in_3, ~in_4, in_5);  // AND_Gate
  and and_14 (out_19, in_1, in_2, ~in_3, in_4, in_5);  // AND_Gate
  and and_15 (out_20, in_1, in_2, in_3, ~in_4, in_5);  // AND_Gate
  and and_16 (out_21, in_1, in_2, in_3, in_4, in_5);
endmodule

module UC (
  input  CLK_BR,
  input  CLK_BR_2,
  input  CLK_BR_3,
  input  MUXA,
  input  MUXA_2,
  input  MUXA_3,
  input  MUXB,
  input  MUXB_2,
  input  MUXB_3,
  input  ULA,
  input  ULA_2,
  input  ULA_3,
  input  in_13,
  input  in_14,
  input  in_15,
  input  in_16,
  input  in_17,
  input  in_18,
  input  in_19,
  input  in_20,
  input  in_21,
  input  in_22,
  input  in_23,
  input  in_24,
  input  in_25,
  input  in_26,
  input  in_27,
  input  in_28,
  input  in_29,
  input  in_30,
  input  in_31,
  input  in_32,
  output out_33,
  output out_34,
  output out_35,
  output out_36,
  output out_37,
  output out_38,
  output out_39,
  output out_40,
  output out_41,
  output out_42,
  output out_43,
  output out_44
);

  wire ri12_12bits_1_out_29, ri12_12bits_1_out_30, ri12_12bits_1_out_31, ri12_12bits_1_out_32,
       ri12_12bits_1_out_33, ri12_12bits_1_out_34, ri12_12bits_1_out_35, ri12_12bits_1_out_36,
       ri12_12bits_1_out_37, ri12_12bits_1_out_38, ri12_12bits_1_out_39, ri12_12bits_1_out_40,
       ri12_12bits_1_out_41, ri12_12bits_1_out_42, ri12_12bits_1_out_43, ri12_12bits_1_out_44,
       ri12_12bits_1_out_45, ri12_12bits_1_out_46, ri12_12bits_1_out_47, ri12_12bits_1_out_48,
       ri12_12bits_1_out_49, ri12_12bits_1_out_50, ri12_12bits_1_out_51, ri12_12bits_1_out_52,
       ri12_12bits_1_out_53, ri12_12bits_1_out_54, ri12_12bits_1_out_55, ri12_12bits_1_out_56,
       ri12_12bits_1_out_57, ri12_12bits_1_out_58, ri12_12bits_1_out_59, ri12_12bits_1_out_60,
       ri12_12bits_1_out_61, ri12_12bits_1_out_62, ri12_12bits_1_out_63, ri12_12bits_1_out_64,
       ri12_12bits_1_out_65, ri12_12bits_1_out_66, ri12_12bits_1_out_67, ri12_12bits_1_out_68,
       ri12_12bits_1_out_69, ri12_12bits_1_out_70, ri12_12bits_1_out_71, ri12_12bits_1_out_72,
       ri12_12bits_1_out_73, ri12_12bits_1_out_74, ri12_12bits_1_out_75, ri12_12bits_1_out_76,
       ri12_12bits_1_out_77, ri12_12bits_1_out_78, ri12_12bits_1_out_79, ri12_12bits_1_out_80,
       ri12_12bits_1_out_81, ri12_12bits_1_out_82, ri12_12bits_1_out_83, ri12_12bits_1_out_84,
       ri12_12bits_1_out_85, ri12_12bits_1_out_86, ri12_12bits_1_out_87, ri12_12bits_1_out_88,
       ri12_12bits_1_out_89, ri12_12bits_1_out_90, ri12_12bits_1_out_91, ri12_12bits_1_out_92,
       ri12_12bits_1_out_93, ri12_12bits_1_out_94, ri12_12bits_1_out_95, ri12_12bits_1_out_96,
       ri12_12bits_1_out_97, ri12_12bits_1_out_98, ri12_12bits_1_out_99, ri12_12bits_1_out_100,
       ri12_12bits_1_out_101, ri12_12bits_1_out_102, ri12_12bits_1_out_103, ri12_12bits_1_out_104,
       ri12_12bits_1_out_105, ri12_12bits_1_out_106, ri12_12bits_1_out_107, ri12_12bits_1_out_108,
       ri12_12bits_1_out_109, ri12_12bits_1_out_110, ri12_12bits_1_out_111, ri12_12bits_1_out_112,
       ri12_12bits_1_out_113, ri12_12bits_1_out_114, ri12_12bits_1_out_115, ri12_12bits_1_out_116,
       ri12_12bits_1_out_117, ri12_12bits_1_out_118, ri12_12bits_1_out_119, ri12_12bits_1_out_120,
       ri12_12bits_1_out_121, ri12_12bits_1_out_122, ri12_12bits_1_out_123, ri12_12bits_1_out_124,
       ri12_12bits_1_out_125, ri12_12bits_1_out_126, ri12_12bits_1_out_127, ri12_12bits_1_out_128,
       ri12_12bits_1_out_129, ri12_12bits_1_out_130, ri12_12bits_1_out_131, ri12_12bits_1_out_132,
       ri12_12bits_1_out_133, ri12_12bits_1_out_134, ri12_12bits_1_out_135, ri12_12bits_1_out_136,
       ri12_12bits_1_out_137, ri12_12bits_1_out_138, ri12_12bits_1_out_139, ri12_12bits_1_out_140,
       ri12_12bits_1_out_141, ri12_12bits_1_out_142, ri12_12bits_1_out_143, ri12_12bits_1_out_144,
       ri12_12bits_1_out_145, ri12_12bits_1_out_146, ri12_12bits_1_out_147, ri12_12bits_1_out_148,
       ri12_12bits_1_out_149, ri12_12bits_1_out_150, ri12_12bits_1_out_151, ri12_12bits_1_out_152,
       ri12_12bits_1_out_153, ri12_12bits_1_out_154, ri12_12bits_1_out_155, ri12_12bits_1_out_156,
       ri12_12bits_1_out_157, ri12_12bits_1_out_158, ri12_12bits_1_out_159, ri12_12bits_1_out_160,
       ri12_12bits_1_out_161, ri12_12bits_1_out_162, ri12_12bits_1_out_163, ri12_12bits_1_out_164,
       ri12_12bits_1_out_165, ri12_12bits_1_out_166, ri12_12bits_1_out_167, ri12_12bits_1_out_168,
       ri12_12bits_1_out_169, ri12_12bits_1_out_170, ri12_12bits_1_out_171, ri12_12bits_1_out_172,
       ri12_12bits_1_out_173, ri12_12bits_1_out_174, ri12_12bits_1_out_175, ri12_12bits_1_out_176,
       ri12_12bits_1_out_177, ri12_12bits_1_out_178, ri12_12bits_1_out_179, ri12_12bits_1_out_180,
       ri12_12bits_1_out_181, ri12_12bits_1_out_182, ri12_12bits_1_out_183, ri12_12bits_1_out_184,
       ri12_12bits_1_out_185, ri12_12bits_1_out_186, ri12_12bits_1_out_187, ri12_12bits_1_out_188,
       ri12_12bits_1_out_189, ri12_12bits_1_out_190, ri12_12bits_1_out_191, ri12_12bits_1_out_192,
       ri12_12bits_1_out_193, ri12_12bits_1_out_194, ri12_12bits_1_out_195, ri12_12bits_1_out_196,
       ri12_12bits_1_out_197, ri12_12bits_1_out_198, ri12_12bits_1_out_199, ri12_12bits_1_out_200,
       ri12_12bits_1_out_201, ri12_12bits_1_out_202, ri12_12bits_1_out_203, ri12_12bits_1_out_204,
       ri12_12bits_1_out_205, ri12_12bits_1_out_206, ri12_12bits_1_out_207, ri12_12bits_1_out_208,
       ri12_12bits_1_out_209, ri12_12bits_1_out_210, ri12_12bits_1_out_211, ri12_12bits_1_out_212,
       ri12_12bits_1_out_213, ri12_12bits_1_out_214, ri12_12bits_1_out_215, ri12_12bits_1_out_216,
       ri12_12bits_1_out_217, ri12_12bits_1_out_218, ri12_12bits_1_out_219, ri12_12bits_1_out_220;

  RI12_12Bits ri12_12bits_1 (
    .in_13(in_17), .in_14(in_18), .in_15(in_19), .in_16(in_20), .in_17(in_21), .in_18(in_22), .in_19(in_23),
    .in_20(in_24), .in_21(in_25), .in_22(in_26), .in_23(in_27), .in_24(in_28), .in_25(in_29), .in_26(in_30),
    .in_27(in_31), .in_28(in_32), .BRCLK2(CLK_BR), .BRCLK1(CLK_BR_2), .BRCLK0(CLK_BR_3), .MuxA2(MUXA),
    .MuxA1(MUXA_2), .MuxA0(MUXA_3), .MuxB2(MUXB), .MuxB1(MUXB_2), .MuxB0(MUXB_3), .ULA2(ULA), .ULA1(ULA_2),
    .ULA0(ULA_3), .out_29(ri12_12bits_1_out_29), .out_30(ri12_12bits_1_out_30),
    .out_31(ri12_12bits_1_out_31), .out_32(ri12_12bits_1_out_32), .out_33(ri12_12bits_1_out_33),
    .out_34(ri12_12bits_1_out_34), .out_35(ri12_12bits_1_out_35), .out_36(ri12_12bits_1_out_36),
    .out_37(ri12_12bits_1_out_37), .out_38(ri12_12bits_1_out_38), .out_39(ri12_12bits_1_out_39),
    .out_40(ri12_12bits_1_out_40), .out_41(ri12_12bits_1_out_41), .out_42(ri12_12bits_1_out_42),
    .out_43(ri12_12bits_1_out_43), .out_44(ri12_12bits_1_out_44), .out_45(ri12_12bits_1_out_45),
    .out_46(ri12_12bits_1_out_46), .out_47(ri12_12bits_1_out_47), .out_48(ri12_12bits_1_out_48),
    .out_49(ri12_12bits_1_out_49), .out_50(ri12_12bits_1_out_50), .out_51(ri12_12bits_1_out_51),
    .out_52(ri12_12bits_1_out_52), .out_53(ri12_12bits_1_out_53), .out_54(ri12_12bits_1_out_54),
    .out_55(ri12_12bits_1_out_55), .out_56(ri12_12bits_1_out_56), .out_57(ri12_12bits_1_out_57),
    .out_58(ri12_12bits_1_out_58), .out_59(ri12_12bits_1_out_59), .out_60(ri12_12bits_1_out_60),
    .out_61(ri12_12bits_1_out_61), .out_62(ri12_12bits_1_out_62), .out_63(ri12_12bits_1_out_63),
    .out_64(ri12_12bits_1_out_64), .out_65(ri12_12bits_1_out_65), .out_66(ri12_12bits_1_out_66),
    .out_67(ri12_12bits_1_out_67), .out_68(ri12_12bits_1_out_68), .out_69(ri12_12bits_1_out_69),
    .out_70(ri12_12bits_1_out_70), .out_71(ri12_12bits_1_out_71), .out_72(ri12_12bits_1_out_72),
    .out_73(ri12_12bits_1_out_73), .out_74(ri12_12bits_1_out_74), .out_75(ri12_12bits_1_out_75),
    .out_76(ri12_12bits_1_out_76), .out_77(ri12_12bits_1_out_77), .out_78(ri12_12bits_1_out_78),
    .out_79(ri12_12bits_1_out_79), .out_80(ri12_12bits_1_out_80), .out_81(ri12_12bits_1_out_81),
    .out_82(ri12_12bits_1_out_82), .out_83(ri12_12bits_1_out_83), .out_84(ri12_12bits_1_out_84),
    .out_85(ri12_12bits_1_out_85), .out_86(ri12_12bits_1_out_86), .out_87(ri12_12bits_1_out_87),
    .out_88(ri12_12bits_1_out_88), .out_89(ri12_12bits_1_out_89), .out_90(ri12_12bits_1_out_90),
    .out_91(ri12_12bits_1_out_91), .out_92(ri12_12bits_1_out_92), .out_93(ri12_12bits_1_out_93),
    .out_94(ri12_12bits_1_out_94), .out_95(ri12_12bits_1_out_95), .out_96(ri12_12bits_1_out_96),
    .out_97(ri12_12bits_1_out_97), .out_98(ri12_12bits_1_out_98), .out_99(ri12_12bits_1_out_99),
    .out_100(ri12_12bits_1_out_100), .out_101(ri12_12bits_1_out_101), .out_102(ri12_12bits_1_out_102),
    .out_103(ri12_12bits_1_out_103), .out_104(ri12_12bits_1_out_104), .out_105(ri12_12bits_1_out_105),
    .out_106(ri12_12bits_1_out_106), .out_107(ri12_12bits_1_out_107), .out_108(ri12_12bits_1_out_108),
    .out_109(ri12_12bits_1_out_109), .out_110(ri12_12bits_1_out_110), .out_111(ri12_12bits_1_out_111),
    .out_112(ri12_12bits_1_out_112), .out_113(ri12_12bits_1_out_113), .out_114(ri12_12bits_1_out_114),
    .out_115(ri12_12bits_1_out_115), .out_116(ri12_12bits_1_out_116), .out_117(ri12_12bits_1_out_117),
    .out_118(ri12_12bits_1_out_118), .out_119(ri12_12bits_1_out_119), .out_120(ri12_12bits_1_out_120),
    .out_121(ri12_12bits_1_out_121), .out_122(ri12_12bits_1_out_122), .out_123(ri12_12bits_1_out_123),
    .out_124(ri12_12bits_1_out_124), .out_125(ri12_12bits_1_out_125), .out_126(ri12_12bits_1_out_126),
    .out_127(ri12_12bits_1_out_127), .out_128(ri12_12bits_1_out_128), .out_129(ri12_12bits_1_out_129),
    .out_130(ri12_12bits_1_out_130), .out_131(ri12_12bits_1_out_131), .out_132(ri12_12bits_1_out_132),
    .out_133(ri12_12bits_1_out_133), .out_134(ri12_12bits_1_out_134), .out_135(ri12_12bits_1_out_135),
    .out_136(ri12_12bits_1_out_136), .out_137(ri12_12bits_1_out_137), .out_138(ri12_12bits_1_out_138),
    .out_139(ri12_12bits_1_out_139), .out_140(ri12_12bits_1_out_140), .out_141(ri12_12bits_1_out_141),
    .out_142(ri12_12bits_1_out_142), .out_143(ri12_12bits_1_out_143), .out_144(ri12_12bits_1_out_144),
    .out_145(ri12_12bits_1_out_145), .out_146(ri12_12bits_1_out_146), .out_147(ri12_12bits_1_out_147),
    .out_148(ri12_12bits_1_out_148), .out_149(ri12_12bits_1_out_149), .out_150(ri12_12bits_1_out_150),
    .out_151(ri12_12bits_1_out_151), .out_152(ri12_12bits_1_out_152), .out_153(ri12_12bits_1_out_153),
    .out_154(ri12_12bits_1_out_154), .out_155(ri12_12bits_1_out_155), .out_156(ri12_12bits_1_out_156),
    .out_157(ri12_12bits_1_out_157), .out_158(ri12_12bits_1_out_158), .out_159(ri12_12bits_1_out_159),
    .out_160(ri12_12bits_1_out_160), .out_161(ri12_12bits_1_out_161), .out_162(ri12_12bits_1_out_162),
    .out_163(ri12_12bits_1_out_163), .out_164(ri12_12bits_1_out_164), .out_165(ri12_12bits_1_out_165),
    .out_166(ri12_12bits_1_out_166), .out_167(ri12_12bits_1_out_167), .out_168(ri12_12bits_1_out_168),
    .out_169(ri12_12bits_1_out_169), .out_170(ri12_12bits_1_out_170), .out_171(ri12_12bits_1_out_171),
    .out_172(ri12_12bits_1_out_172), .out_173(ri12_12bits_1_out_173), .out_174(ri12_12bits_1_out_174),
    .out_175(ri12_12bits_1_out_175), .out_176(ri12_12bits_1_out_176), .out_177(ri12_12bits_1_out_177),
    .out_178(ri12_12bits_1_out_178), .out_179(ri12_12bits_1_out_179), .out_180(ri12_12bits_1_out_180),
    .out_181(ri12_12bits_1_out_181), .out_182(ri12_12bits_1_out_182), .out_183(ri12_12bits_1_out_183),
    .out_184(ri12_12bits_1_out_184), .out_185(ri12_12bits_1_out_185), .out_186(ri12_12bits_1_out_186),
    .out_187(ri12_12bits_1_out_187), .out_188(ri12_12bits_1_out_188), .out_189(ri12_12bits_1_out_189),
    .out_190(ri12_12bits_1_out_190), .out_191(ri12_12bits_1_out_191), .out_192(ri12_12bits_1_out_192),
    .out_193(ri12_12bits_1_out_193), .out_194(ri12_12bits_1_out_194), .out_195(ri12_12bits_1_out_195),
    .out_196(ri12_12bits_1_out_196), .out_197(ri12_12bits_1_out_197), .out_198(ri12_12bits_1_out_198),
    .out_199(ri12_12bits_1_out_199), .out_200(ri12_12bits_1_out_200), .out_201(ri12_12bits_1_out_201),
    .out_202(ri12_12bits_1_out_202), .out_203(ri12_12bits_1_out_203), .out_204(ri12_12bits_1_out_204),
    .out_205(ri12_12bits_1_out_205), .out_206(ri12_12bits_1_out_206), .out_207(ri12_12bits_1_out_207),
    .out_208(ri12_12bits_1_out_208), .out_209(ri12_12bits_1_out_209), .out_210(ri12_12bits_1_out_210),
    .out_211(ri12_12bits_1_out_211), .out_212(ri12_12bits_1_out_212), .out_213(ri12_12bits_1_out_213),
    .out_214(ri12_12bits_1_out_214), .out_215(ri12_12bits_1_out_215), .out_216(ri12_12bits_1_out_216),
    .out_217(ri12_12bits_1_out_217), .out_218(ri12_12bits_1_out_218), .out_219(ri12_12bits_1_out_219),
    .out_220(ri12_12bits_1_out_220));
  Mux_192_12 mux_192_12_1 (
    .A(ri12_12bits_1_out_29), .B(ri12_12bits_1_out_30), .C(ri12_12bits_1_out_31), .D(ri12_12bits_1_out_32),
    .E(ri12_12bits_1_out_33), .F(ri12_12bits_1_out_34), .G(ri12_12bits_1_out_35), .H(ri12_12bits_1_out_36),
    .I(ri12_12bits_1_out_37), .J(ri12_12bits_1_out_38), .L(ri12_12bits_1_out_39), .M(ri12_12bits_1_out_40),
    .A_2(ri12_12bits_1_out_41), .B_2(ri12_12bits_1_out_42), .C_2(ri12_12bits_1_out_43),
    .D_2(ri12_12bits_1_out_44), .E_2(ri12_12bits_1_out_45), .F_2(ri12_12bits_1_out_46),
    .G_2(ri12_12bits_1_out_47), .H_2(ri12_12bits_1_out_48), .I_2(ri12_12bits_1_out_49),
    .J_2(ri12_12bits_1_out_50), .L_2(ri12_12bits_1_out_51), .M_2(ri12_12bits_1_out_52),
    .A_3(ri12_12bits_1_out_53), .B_3(ri12_12bits_1_out_54), .C_3(ri12_12bits_1_out_55),
    .D_3(ri12_12bits_1_out_56), .E_3(ri12_12bits_1_out_57), .F_3(ri12_12bits_1_out_58),
    .G_3(ri12_12bits_1_out_59), .H_3(ri12_12bits_1_out_60), .I_3(ri12_12bits_1_out_61),
    .J_3(ri12_12bits_1_out_62), .L_3(ri12_12bits_1_out_63), .M_3(ri12_12bits_1_out_64),
    .A_4(ri12_12bits_1_out_65), .B_4(ri12_12bits_1_out_66), .C_4(ri12_12bits_1_out_67),
    .D_4(ri12_12bits_1_out_68), .E_4(ri12_12bits_1_out_69), .F_4(ri12_12bits_1_out_70),
    .G_4(ri12_12bits_1_out_71), .H_4(ri12_12bits_1_out_72), .I_4(ri12_12bits_1_out_73),
    .J_4(ri12_12bits_1_out_74), .L_4(ri12_12bits_1_out_75), .M_4(ri12_12bits_1_out_76),
    .A_5(ri12_12bits_1_out_77), .B_5(ri12_12bits_1_out_78), .C_5(ri12_12bits_1_out_79),
    .D_5(ri12_12bits_1_out_80), .E_5(ri12_12bits_1_out_81), .F_5(ri12_12bits_1_out_82),
    .G_5(ri12_12bits_1_out_83), .H_5(ri12_12bits_1_out_84), .I_5(ri12_12bits_1_out_85),
    .J_5(ri12_12bits_1_out_86), .L_5(ri12_12bits_1_out_87), .M_5(ri12_12bits_1_out_88),
    .A_6(ri12_12bits_1_out_89), .B_6(ri12_12bits_1_out_90), .C_6(ri12_12bits_1_out_91),
    .D_6(ri12_12bits_1_out_92), .E_6(ri12_12bits_1_out_93), .F_6(ri12_12bits_1_out_94),
    .G_6(ri12_12bits_1_out_95), .H_6(ri12_12bits_1_out_96), .I_6(ri12_12bits_1_out_97),
    .J_6(ri12_12bits_1_out_98), .L_6(ri12_12bits_1_out_99), .M_6(ri12_12bits_1_out_100),
    .A_7(ri12_12bits_1_out_101), .B_7(ri12_12bits_1_out_102), .C_7(ri12_12bits_1_out_103),
    .D_7(ri12_12bits_1_out_104), .E_7(ri12_12bits_1_out_105), .F_7(ri12_12bits_1_out_106),
    .G_7(ri12_12bits_1_out_107), .H_7(ri12_12bits_1_out_108), .I_7(ri12_12bits_1_out_109),
    .J_7(ri12_12bits_1_out_110), .L_7(ri12_12bits_1_out_111), .M_7(ri12_12bits_1_out_112),
    .A_8(ri12_12bits_1_out_113), .B_8(ri12_12bits_1_out_114), .C_8(ri12_12bits_1_out_115),
    .D_8(ri12_12bits_1_out_116), .E_8(ri12_12bits_1_out_117), .F_8(ri12_12bits_1_out_118),
    .G_8(ri12_12bits_1_out_119), .H_8(ri12_12bits_1_out_120), .I_8(ri12_12bits_1_out_121),
    .J_8(ri12_12bits_1_out_122), .L_8(ri12_12bits_1_out_123), .M_8(ri12_12bits_1_out_124),
    .A_9(ri12_12bits_1_out_125), .B_9(ri12_12bits_1_out_126), .C_9(ri12_12bits_1_out_127),
    .D_9(ri12_12bits_1_out_128), .E_9(ri12_12bits_1_out_129), .F_9(ri12_12bits_1_out_130),
    .G_9(ri12_12bits_1_out_131), .H_9(ri12_12bits_1_out_132), .I_9(ri12_12bits_1_out_133),
    .J_9(ri12_12bits_1_out_134), .L_9(ri12_12bits_1_out_135), .M_9(ri12_12bits_1_out_136),
    .A_10(ri12_12bits_1_out_137), .B_10(ri12_12bits_1_out_138), .C_10(ri12_12bits_1_out_139),
    .D_10(ri12_12bits_1_out_140), .E_10(ri12_12bits_1_out_141), .F_10(ri12_12bits_1_out_142),
    .G_10(ri12_12bits_1_out_143), .H_10(ri12_12bits_1_out_144), .I_10(ri12_12bits_1_out_145),
    .J_10(ri12_12bits_1_out_146), .L_10(ri12_12bits_1_out_147), .M_10(ri12_12bits_1_out_148),
    .A_11(ri12_12bits_1_out_149), .B_11(ri12_12bits_1_out_150), .C_11(ri12_12bits_1_out_151),
    .D_11(ri12_12bits_1_out_152), .E_11(ri12_12bits_1_out_153), .F_11(ri12_12bits_1_out_154),
    .G_11(ri12_12bits_1_out_155), .H_11(ri12_12bits_1_out_156), .I_11(ri12_12bits_1_out_157),
    .J_11(ri12_12bits_1_out_158), .L_11(ri12_12bits_1_out_159), .M_11(ri12_12bits_1_out_160),
    .A_12(ri12_12bits_1_out_161), .B_12(ri12_12bits_1_out_162), .C_12(ri12_12bits_1_out_163),
    .D_12(ri12_12bits_1_out_164), .E_12(ri12_12bits_1_out_165), .F_12(ri12_12bits_1_out_166),
    .G_12(ri12_12bits_1_out_167), .H_12(ri12_12bits_1_out_168), .I_12(ri12_12bits_1_out_169),
    .J_12(ri12_12bits_1_out_170), .L_12(ri12_12bits_1_out_171), .M_12(ri12_12bits_1_out_172),
    .A_13(ri12_12bits_1_out_173), .B_13(ri12_12bits_1_out_174), .C_13(ri12_12bits_1_out_175),
    .D_13(ri12_12bits_1_out_176), .E_13(ri12_12bits_1_out_177), .F_13(ri12_12bits_1_out_178),
    .G_13(ri12_12bits_1_out_179), .H_13(ri12_12bits_1_out_180), .I_13(ri12_12bits_1_out_181),
    .J_13(ri12_12bits_1_out_182), .L_13(ri12_12bits_1_out_183), .M_13(ri12_12bits_1_out_184),
    .A_14(ri12_12bits_1_out_185), .B_14(ri12_12bits_1_out_186), .C_14(ri12_12bits_1_out_187),
    .D_14(ri12_12bits_1_out_188), .E_14(ri12_12bits_1_out_189), .F_14(ri12_12bits_1_out_190),
    .G_14(ri12_12bits_1_out_191), .H_14(ri12_12bits_1_out_192), .I_14(ri12_12bits_1_out_193),
    .J_14(ri12_12bits_1_out_194), .L_14(ri12_12bits_1_out_195), .M_14(ri12_12bits_1_out_196),
    .A_15(ri12_12bits_1_out_197), .B_15(ri12_12bits_1_out_198), .C_15(ri12_12bits_1_out_199),
    .D_15(ri12_12bits_1_out_200), .E_15(ri12_12bits_1_out_201), .F_15(ri12_12bits_1_out_202),
    .G_15(ri12_12bits_1_out_203), .H_15(ri12_12bits_1_out_204), .I_15(ri12_12bits_1_out_205),
    .J_15(ri12_12bits_1_out_206), .L_15(ri12_12bits_1_out_207), .M_15(ri12_12bits_1_out_208),
    .A_16(ri12_12bits_1_out_209), .B_16(ri12_12bits_1_out_210), .C_16(ri12_12bits_1_out_211),
    .D_16(ri12_12bits_1_out_212), .E_16(ri12_12bits_1_out_213), .F_16(ri12_12bits_1_out_214),
    .G_16(ri12_12bits_1_out_215), .H_16(ri12_12bits_1_out_216), .I_16(ri12_12bits_1_out_217),
    .J_16(ri12_12bits_1_out_218), .L_16(ri12_12bits_1_out_219), .M_16(ri12_12bits_1_out_220), .in_3(in_13),
    .in_4(in_14), .in_5(in_15), .in_6(in_16), .out_197(out_33), .out_198(out_34), .out_199(out_35),
    .out_200(out_36), .out_201(out_37), .out_202(out_38), .out_203(out_39), .out_204(out_40),
    .out_205(out_41), .out_206(out_42), .out_207(out_43), .out_208(out_44));
endmodule

module Mux_192_12 (
  input  A,
  input  B,
  input  in_3,
  input  in_4,
  input  in_5,
  input  in_6,
  input  C,
  input  D,
  input  E,
  input  F,
  input  G,
  input  H,
  input  I,
  input  J,
  input  L,
  input  M,
  input  A_2,
  input  B_2,
  input  C_2,
  input  D_2,
  input  E_2,
  input  F_2,
  input  G_2,
  input  H_2,
  input  I_2,
  input  J_2,
  input  L_2,
  input  M_2,
  input  A_3,
  input  B_3,
  input  C_3,
  input  D_3,
  input  E_3,
  input  F_3,
  input  G_3,
  input  H_3,
  input  I_3,
  input  J_3,
  input  L_3,
  input  M_3,
  input  A_4,
  input  B_4,
  input  C_4,
  input  D_4,
  input  E_4,
  input  F_4,
  input  G_4,
  input  H_4,
  input  I_4,
  input  J_4,
  input  L_4,
  input  M_4,
  input  A_5,
  input  B_5,
  input  C_5,
  input  D_5,
  input  E_5,
  input  F_5,
  input  G_5,
  input  H_5,
  input  I_5,
  input  J_5,
  input  L_5,
  input  M_5,
  input  A_6,
  input  B_6,
  input  C_6,
  input  D_6,
  input  E_6,
  input  F_6,
  input  G_6,
  input  H_6,
  input  I_6,
  input  J_6,
  input  L_6,
  input  M_6,
  input  A_7,
  input  B_7,
  input  C_7,
  input  D_7,
  input  E_7,
  input  F_7,
  input  G_7,
  input  H_7,
  input  I_7,
  input  J_7,
  input  L_7,
  input  M_7,
  input  A_8,
  input  B_8,
  input  C_8,
  input  D_8,
  input  E_8,
  input  F_8,
  input  G_8,
  input  H_8,
  input  I_8,
  input  J_8,
  input  L_8,
  input  M_8,
  input  A_9,
  input  B_9,
  input  C_9,
  input  D_9,
  input  E_9,
  input  F_9,
  input  G_9,
  input  H_9,
  input  I_9,
  input  J_9,
  input  L_9,
  input  M_9,
  input  A_10,
  input  B_10,
  input  C_10,
  input  D_10,
  input  E_10,
  input  F_10,
  input  G_10,
  input  H_10,
  input  I_10,
  input  J_10,
  input  L_10,
  input  M_10,
  input  A_11,
  input  B_11,
  input  C_11,
  input  D_11,
  input  E_11,
  input  F_11,
  input  G_11,
  input  H_11,
  input  I_11,
  input  J_11,
  input  L_11,
  input  M_11,
  input  A_12,
  input  B_12,
  input  C_12,
  input  D_12,
  input  E_12,
  input  F_12,
  input  G_12,
  input  H_12,
  input  I_12,
  input  J_12,
  input  L_12,
  input  M_12,
  input  A_13,
  input  B_13,
  input  C_13,
  input  D_13,
  input  E_13,
  input  F_13,
  input  G_13,
  input  H_13,
  input  I_13,
  input  J_13,
  input  L_13,
  input  M_13,
  input  A_14,
  input  B_14,
  input  C_14,
  input  D_14,
  input  E_14,
  input  F_14,
  input  G_14,
  input  H_14,
  input  I_14,
  input  J_14,
  input  L_14,
  input  M_14,
  input  A_15,
  input  B_15,
  input  C_15,
  input  D_15,
  input  E_15,
  input  F_15,
  input  G_15,
  input  H_15,
  input  I_15,
  input  J_15,
  input  L_15,
  input  M_15,
  input  A_16,
  input  B_16,
  input  C_16,
  input  D_16,
  input  E_16,
  input  F_16,
  input  G_16,
  input  H_16,
  input  I_16,
  input  J_16,
  input  L_16,
  input  M_16,
  output out_197,
  output out_198,
  output out_199,
  output out_200,
  output out_201,
  output out_202,
  output out_203,
  output out_204,
  output out_205,
  output out_206,
  output out_207,
  output out_208
);

  Multiplexer #(.select(4), .width(12)) multiplexer_1 (
    .in0({M, L, J, I, H, G, F, E, D, C, B, A}),
    .in1({M_2, L_2, J_2, I_2, H_2, G_2, F_2, E_2, D_2, C_2, B_2, A_2}),
    .in2({M_3, L_3, J_3, I_3, H_3, G_3, F_3, E_3, D_3, C_3, B_3, A_3}),
    .in3({M_4, L_4, J_4, I_4, H_4, G_4, F_4, E_4, D_4, C_4, B_4, A_4}),
    .in4({M_5, L_5, J_5, I_5, H_5, G_5, F_5, E_5, D_5, C_5, B_5, A_5}),
    .in5({M_6, L_6, J_6, I_6, H_6, G_6, F_6, E_6, D_6, C_6, B_6, A_6}),
    .in6({M_7, L_7, J_7, I_7, H_7, G_7, F_7, E_7, D_7, C_7, B_7, A_7}),
    .in7({M_8, L_8, J_8, I_8, H_8, G_8, F_8, E_8, D_8, C_8, B_8, A_8}),
    .in8({M_9, L_9, J_9, I_9, H_9, G_9, F_9, E_9, D_9, C_9, B_9, A_9}),
    .in9({M_10, L_10, J_10, I_10, H_10, G_10, F_10, E_10, D_10, C_10, B_10, A_10}),
    .in10({M_11, L_11, J_11, I_11, H_11, G_11, F_11, E_11, D_11, C_11, B_11, A_11}),
    .in11({M_12, L_12, J_12, I_12, H_12, G_12, F_12, E_12, D_12, C_12, B_12, A_12}),
    .in12({M_13, L_13, J_13, I_13, H_13, G_13, F_13, E_13, D_13, C_13, B_13, A_13}),
    .in13({M_14, L_14, J_14, I_14, H_14, G_14, F_14, E_14, D_14, C_14, B_14, A_14}),
    .in14({M_15, L_15, J_15, I_15, H_15, G_15, F_15, E_15, D_15, C_15, B_15, A_15}),
    .in15({M_16, L_16, J_16, I_16, H_16, G_16, F_16, E_16, D_16, C_16, B_16, A_16}),
    .out({out_197, out_198, out_199, out_200, out_201, out_202, out_203, out_204, out_205, out_206, out_207, out_208}),
    .sel({in_3, in_4, in_5, in_6}));  // open: en
endmodule

module BCDD8421_0_15 (
  input  _0,
  input  _1,
  input  _2,
  input  _3,
  input  _4,
  input  _5,
  input  _6,
  input  _7,
  input  _8,
  input  _9,
  input  _10,
  input  _11,
  input  _12,
  input  _13,
  input  _14,
  input  _15,
  output A,
  output B,
  output C,
  output D
);

  wire nand_1_out, nand_2_out, nand_3_out, nand_4_out, not_1_out, not_2_out, not_3_out, not_4_out, not_5_out,
       not_6_out, not_7_out, not_8_out, not_9_out, not_10_out, not_11_out, not_12_out, not_13_out,
       not_14_out, not_15_out, or_1_out;

  or or_1 (or_1_out, _15, _14, _13, _12, _11, _10, _9, _8, _7, _6, _5, _4, _3, _2, _1, _0);
  not not_1 (not_1_out, _1);
  not not_2 (not_2_out, _2);
  R4B r4b_1 (
    .in_5(or_1_out), .DA(nand_4_out), .DB(nand_3_out), .DC(nand_2_out), .DD(nand_1_out), .QA(A), .QB(B),
    .QC(C), .QD(D));
  not not_3 (not_3_out, _3);
  not not_4 (not_4_out, _4);
  not not_5 (not_5_out, _5);
  not not_6 (not_6_out, _6);
  not not_7 (not_7_out, _7);
  not not_8 (not_8_out, _8);
  not not_9 (not_9_out, _10);
  not not_10 (not_10_out, _9);
  not not_11 (not_11_out, _11);
  not not_12 (not_12_out, _12);
  not not_13 (not_13_out, _14);
  not not_14 (not_14_out, _13);
  not not_15 (not_15_out, _15);
  nand nand_1 (nand_1_out, not_15_out, not_14_out, not_11_out, not_10_out, not_7_out, not_5_out, not_3_out, not_1_out);
  nand nand_2 (nand_2_out, not_15_out, not_13_out, not_11_out, not_9_out, not_7_out, not_6_out, not_3_out, not_2_out);
  nand nand_3 (nand_3_out, not_15_out, not_13_out, not_14_out, not_12_out, not_7_out, not_6_out, not_5_out, not_4_out);
  nand nand_4 (nand_4_out, not_15_out, not_13_out, not_14_out, not_12_out, not_11_out, not_9_out, not_10_out, not_8_out);
endmodule

module DULLENTRY (
  input  in_1,
  input  in_2,
  input  in_3,
  input  B0,
  input  B1,
  input  B2,
  input  B3,
  output B0_2,
  output B1_2,
  output B2_2,
  output B3_2
);

  wire and_1_out, not_1_out;

  not not_1 (not_1_out, in_3);
  Multiplexer #(.width(4)) multiplexer_1 (
    .in0({B3, B2, B1, B0}), .in1(4'b0000), .out({B3_2, B2_2, B1_2, B0_2}), .sel(and_1_out));  // open: en
  and and_1 (and_1_out, not_1_out, in_2, in_1);
endmodule

module ENTRYSLT (
  input  in_1,
  input  in_2,
  input  in_3,
  input  A0,
  input  A1,
  input  A2,
  input  A3,
  input  B0,
  input  B1,
  input  B2,
  input  B3,
  output C0,
  output C1,
  output C2,
  output C3
);

  wire and_1_out, not_1_out;

  not not_1 (not_1_out, in_3);
  Multiplexer #(.width(4)) multiplexer_1 (
    .in0({A3, A2, A1, A0}), .in1({B3, B2, B1, B0}), .out({C3, C2, C1, C0}), .sel(and_1_out));  // open: en
  and and_1 (and_1_out, not_1_out, in_2, in_1);
endmodule

module L2_RG16b (
  input  in_1,
  input  in_2,
  input  in_3,
  input  in_4,
  input  in_5,
  input  in_6,
  input  in_7,
  input  in_8,
  input  in_9,
  input  in_10,
  input  in_11,
  input  in_12,
  input  in_13,
  input  in_14,
  input  in_15,
  input  in_16,
  input  in_17,
  output out_18,
  output out_19,
  output out_20,
  output out_21,
  output out_22,
  output out_23,
  output out_24,
  output out_25,
  output out_26,
  output out_27,
  output out_28,
  output out_29,
  output out_30,
  output out_31,
  output out_32,
  output out_33
);

  Flip_Flop_D flip_flop_d_1 (.D(in_1), .CLK(in_17), .Q(out_19));  // open: Q_prime
  Flip_Flop_D flip_flop_d_2 (.D(in_2), .CLK(in_17), .Q(out_20));  // open: Q_prime
  Flip_Flop_D flip_flop_d_3 (.D(in_3), .CLK(in_17), .Q(out_21));  // open: Q_prime
  Flip_Flop_D flip_flop_d_4 (.D(in_4), .CLK(in_17), .Q(out_22));  // open: Q_prime
  Flip_Flop_D flip_flop_d_5 (.D(in_5), .CLK(in_17), .Q(out_23));  // open: Q_prime
  Flip_Flop_D flip_flop_d_6 (.D(in_6), .CLK(in_17), .Q(out_24));  // open: Q_prime
  Flip_Flop_D flip_flop_d_7 (.D(in_7), .CLK(in_17), .Q(out_25));  // open: Q_prime
  Flip_Flop_D flip_flop_d_8 (.D(in_8), .CLK(in_17), .Q(out_26));  // open: Q_prime
  Flip_Flop_D flip_flop_d_9 (.D(in_9), .CLK(in_17), .Q(out_27));  // open: Q_prime
  Flip_Flop_D flip_flop_d_10 (.D(in_10), .CLK(in_17), .Q(out_28));  // open: Q_prime
  Flip_Flop_D flip_flop_d_11 (.D(in_11), .CLK(in_17), .Q(out_29));  // open: Q_prime
  Flip_Flop_D flip_flop_d_12 (.D(in_12), .CLK(in_17), .Q(out_30));  // open: Q_prime
  Flip_Flop_D flip_flop_d_13 (.D(in_13), .CLK(in_17), .Q(out_31));  // open: Q_prime
  Flip_Flop_D flip_flop_d_14 (.D(in_14), .CLK(in_17), .Q(out_32));  // open: Q_prime
  Flip_Flop_D flip_flop_d_15 (.D(in_15), .CLK(in_17), .Q(out_33));  // open: Q_prime
  Flip_Flop_D flip_flop_d_16 (.D(in_16), .CLK(in_17), .Q(out_18));  // open: Q_prime
endmodule
// L2 256 BITS
module L2_256b (
  input  DEST,
  input  DEST_2,
  input  DEST_3,
  input  INS,
  input  INS_2,
  input  INS_3,
  input  R1,
  input  R1_2,
  input  R1_3,
  input  R2,
  input  R2_2,
  input  R2_3,
  input  R1_4,
  input  INPUT,
  input  INPUT_2,
  input  INPUT_3,
  input  R1_5,
  input  R2_4,
  input  R3,
  input  R4,
  input  R5,
  input  R6,
  input  R7,
  input  R8,
  input  [3:0] SELECT,
  input  R9,
  input  R10,
  input  R11,
  input  R12,
  input  R13,
  input  R14,
  input  R15,
  input  R16,
  output DEST_4,
  output DEST_5,
  output DEST_6,
  output INS_4,
  output INS_5,
  output INS_6,
  output OUT_INPUT,
  output OUT_INPUT_2,
  output OUT_INPUT_3,
  output OUT_INPUT_4,
  output OUT_R1,
  output OUT_R1_2,
  output OUT_R1_3,
  output OUT_R2,
  output OUT_R2_2,
  output OUT_R2_3
);

  wire l2_rg16plug_1_out_34, l2_rg16plug_1_out_35, l2_rg16plug_1_out_36, l2_rg16plug_1_out_37,
       l2_rg16plug_1_out_38, l2_rg16plug_1_out_39, l2_rg16plug_1_out_40, l2_rg16plug_1_out_41,
       l2_rg16plug_1_out_42, l2_rg16plug_1_out_43, l2_rg16plug_1_out_44, l2_rg16plug_1_out_45,
       l2_rg16plug_1_out_46, l2_rg16plug_1_out_47, l2_rg16plug_1_out_48, l2_rg16plug_1_out_49,
       l2_rg16plug_2_out_34, l2_rg16plug_2_out_35, l2_rg16plug_2_out_36, l2_rg16plug_2_out_37,
       l2_rg16plug_2_out_38, l2_rg16plug_2_out_39, l2_rg16plug_2_out_40, l2_rg16plug_2_out_41,
       l2_rg16plug_2_out_42, l2_rg16plug_2_out_43, l2_rg16plug_2_out_44, l2_rg16plug_2_out_45,
       l2_rg16plug_2_out_46, l2_rg16plug_2_out_47, l2_rg16plug_2_out_48, l2_rg16plug_2_out_49,
       l2_rg16plug_3_out_34, l2_rg16plug_3_out_35, l2_rg16plug_3_out_36, l2_rg16plug_3_out_37,
       l2_rg16plug_3_out_38, l2_rg16plug_3_out_39, l2_rg16plug_3_out_40, l2_rg16plug_3_out_41,
       l2_rg16plug_3_out_42, l2_rg16plug_3_out_43, l2_rg16plug_3_out_44, l2_rg16plug_3_out_45,
       l2_rg16plug_3_out_46, l2_rg16plug_3_out_47, l2_rg16plug_3_out_48, l2_rg16plug_3_out_49,
       l2_rg16plug_4_out_34, l2_rg16plug_4_out_35, l2_rg16plug_4_out_36, l2_rg16plug_4_out_37,
       l2_rg16plug_4_out_38, l2_rg16plug_4_out_39, l2_rg16plug_4_out_40, l2_rg16plug_4_out_41,
       l2_rg16plug_4_out_42, l2_rg16plug_4_out_43, l2_rg16plug_4_out_44, l2_rg16plug_4_out_45,
       l2_rg16plug_4_out_46, l2_rg16plug_4_out_47, l2_rg16plug_4_out_48, l2_rg16plug_4_out_49,
       l2_rg16plug_5_out_34, l2_rg16plug_5_out_35, l2_rg16plug_5_out_36, l2_rg16plug_5_out_37,
       l2_rg16plug_5_out_38, l2_rg16plug_5_out_39, l2_rg16plug_5_out_40, l2_rg16plug_5_out_41,
       l2_rg16plug_5_out_42, l2_rg16plug_5_out_43, l2_rg16plug_5_out_44, l2_rg16plug_5_out_45,
       l2_rg16plug_5_out_46, l2_rg16plug_5_out_47, l2_rg16plug_5_out_48, l2_rg16plug_5_out_49,
       l2_rg16plug_6_out_34, l2_rg16plug_6_out_35, l2_rg16plug_6_out_36, l2_rg16plug_6_out_37,
       l2_rg16plug_6_out_38, l2_rg16plug_6_out_39, l2_rg16plug_6_out_40, l2_rg16plug_6_out_41,
       l2_rg16plug_6_out_42, l2_rg16plug_6_out_43, l2_rg16plug_6_out_44, l2_rg16plug_6_out_45,
       l2_rg16plug_6_out_46, l2_rg16plug_6_out_47, l2_rg16plug_6_out_48, l2_rg16plug_6_out_49,
       l2_rg16plug_7_out_34, l2_rg16plug_7_out_35, l2_rg16plug_7_out_36, l2_rg16plug_7_out_37,
       l2_rg16plug_7_out_38, l2_rg16plug_7_out_39, l2_rg16plug_7_out_40, l2_rg16plug_7_out_41,
       l2_rg16plug_7_out_42, l2_rg16plug_7_out_43, l2_rg16plug_7_out_44, l2_rg16plug_7_out_45,
       l2_rg16plug_7_out_46, l2_rg16plug_7_out_47, l2_rg16plug_7_out_48, l2_rg16plug_7_out_49,
       l2_rg16plug_8_out_34, l2_rg16plug_8_out_35, l2_rg16plug_8_out_36, l2_rg16plug_8_out_37,
       l2_rg16plug_8_out_38, l2_rg16plug_8_out_39, l2_rg16plug_8_out_40, l2_rg16plug_8_out_41,
       l2_rg16plug_8_out_42, l2_rg16plug_8_out_43, l2_rg16plug_8_out_44, l2_rg16plug_8_out_45,
       l2_rg16plug_8_out_46, l2_rg16plug_8_out_47, l2_rg16plug_8_out_48, l2_rg16plug_8_out_49,
       l2_rg16plug_9_out_34, l2_rg16plug_9_out_35, l2_rg16plug_9_out_36, l2_rg16plug_9_out_37,
       l2_rg16plug_9_out_38, l2_rg16plug_9_out_39, l2_rg16plug_9_out_40, l2_rg16plug_9_out_41,
       l2_rg16plug_9_out_42, l2_rg16plug_9_out_43, l2_rg16plug_9_out_44, l2_rg16plug_9_out_45,
       l2_rg16plug_9_out_46, l2_rg16plug_9_out_47, l2_rg16plug_9_out_48, l2_rg16plug_9_out_49,
       l2_rg16plug_10_out_34, l2_rg16plug_10_out_35, l2_rg16plug_10_out_36, l2_rg16plug_10_out_37,
       l2_rg16plug_10_out_38, l2_rg16plug_10_out_39, l2_rg16plug_10_out_40, l2_rg16plug_10_out_41,
       l2_rg16plug_10_out_42, l2_rg16plug_10_out_43, l2_rg16plug_10_out_44, l2_rg16plug_10_out_45,
       l2_rg16plug_10_out_46, l2_rg16plug_10_out_47, l2_rg16plug_10_out_48, l2_rg16plug_10_out_49,
       l2_rg16plug_11_out_34, l2_rg16plug_11_out_35, l2_rg16plug_11_out_36, l2_rg16plug_11_out_37,
       l2_rg16plug_11_out_38, l2_rg16plug_11_out_39, l2_rg16plug_11_out_40, l2_rg16plug_11_out_41,
       l2_rg16plug_11_out_42, l2_rg16plug_11_out_43, l2_rg16plug_11_out_44, l2_rg16plug_11_out_45,
       l2_rg16plug_11_out_46, l2_rg16plug_11_out_47, l2_rg16plug_11_out_48, l2_rg16plug_11_out_49,
       l2_rg16plug_12_out_34, l2_rg16plug_12_out_35, l2_rg16plug_12_out_36, l2_rg16plug_12_out_37,
       l2_rg16plug_12_out_38, l2_rg16plug_12_out_39, l2_rg16plug_12_out_40, l2_rg16plug_12_out_41,
       l2_rg16plug_12_out_42, l2_rg16plug_12_out_43, l2_rg16plug_12_out_44, l2_rg16plug_12_out_45,
       l2_rg16plug_12_out_46, l2_rg16plug_12_out_47, l2_rg16plug_12_out_48, l2_rg16plug_12_out_49,
       l2_rg16plug_13_out_34, l2_rg16plug_13_out_35, l2_rg16plug_13_out_36, l2_rg16plug_13_out_37,
       l2_rg16plug_13_out_38, l2_rg16plug_13_out_39, l2_rg16plug_13_out_40, l2_rg16plug_13_out_41,
       l2_rg16plug_13_out_42, l2_rg16plug_13_out_43, l2_rg16plug_13_out_44, l2_rg16plug_13_out_45,
       l2_rg16plug_13_out_46, l2_rg16plug_13_out_47, l2_rg16plug_13_out_48, l2_rg16plug_13_out_49,
       l2_rg16plug_14_out_34, l2_rg16plug_14_out_35, l2_rg16plug_14_out_36, l2_rg16plug_14_out_37,
       l2_rg16plug_14_out_38, l2_rg16plug_14_out_39, l2_rg16plug_14_out_40, l2_rg16plug_14_out_41,
       l2_rg16plug_14_out_42, l2_rg16plug_14_out_43, l2_rg16plug_14_out_44, l2_rg16plug_14_out_45,
       l2_rg16plug_14_out_46, l2_rg16plug_14_out_47, l2_rg16plug_14_out_48, l2_rg16plug_14_out_49,
       l2_rg16plug_15_out_34, l2_rg16plug_15_out_35, l2_rg16plug_15_out_36, l2_rg16plug_15_out_37,
       l2_rg16plug_15_out_38, l2_rg16plug_15_out_39, l2_rg16plug_15_out_40, l2_rg16plug_15_out_41,
       l2_rg16plug_15_out_42, l2_rg16plug_15_out_43, l2_rg16plug_15_out_44, l2_rg16plug_15_out_45,
       l2_rg16plug_15_out_46, l2_rg16plug_15_out_47, l2_rg16plug_15_out_48, l2_rg16plug_15_out_49;
  wire [15:0] l2_rg16plug_1_out_18, l2_rg16plug_2_out_18, l2_rg16plug_3_out_18, l2_rg16plug_4_out_18,
       l2_rg16plug_5_out_18, l2_rg16plug_6_out_18, l2_rg16plug_7_out_18, l2_rg16plug_8_out_18,
       l2_rg16plug_9_out_18, l2_rg16plug_10_out_18, l2_rg16plug_11_out_18, l2_rg16plug_12_out_18,
       l2_rg16plug_13_out_18, l2_rg16plug_14_out_18, l2_rg16plug_15_out_18, l2_rg16plug_16_out_18;

  L2_RG16PLUG l2_rg16plug_1 (
    .in_17(R1_5), .A(DEST), .B(DEST_2), .C(DEST_3), .D(INS), .E(INS_2), .F(INS_3), .G(R1), .H(R1_2),
    .I(R1_3), .J(R2), .L(R2_2), .M(R2_3), .N(R1_4), .O(INPUT), .P(INPUT_2), .Q(INPUT_3),
    .out_34(l2_rg16plug_1_out_34), .out_35(l2_rg16plug_1_out_35), .out_36(l2_rg16plug_1_out_36),
    .out_37(l2_rg16plug_1_out_37), .out_38(l2_rg16plug_1_out_38), .out_39(l2_rg16plug_1_out_39),
    .out_40(l2_rg16plug_1_out_40), .out_41(l2_rg16plug_1_out_41), .out_42(l2_rg16plug_1_out_42),
    .out_43(l2_rg16plug_1_out_43), .out_44(l2_rg16plug_1_out_44), .out_45(l2_rg16plug_1_out_45),
    .out_46(l2_rg16plug_1_out_46), .out_47(l2_rg16plug_1_out_47), .out_48(l2_rg16plug_1_out_48),
    .out_49(l2_rg16plug_1_out_49), .out_18(l2_rg16plug_1_out_18[0]), .out_19(l2_rg16plug_1_out_18[1]),
    .out_20(l2_rg16plug_1_out_18[2]), .out_21(l2_rg16plug_1_out_18[3]), .out_22(l2_rg16plug_1_out_18[4]),
    .out_23(l2_rg16plug_1_out_18[5]), .out_24(l2_rg16plug_1_out_18[6]), .out_25(l2_rg16plug_1_out_18[7]),
    .out_26(l2_rg16plug_1_out_18[8]), .out_27(l2_rg16plug_1_out_18[9]), .out_28(l2_rg16plug_1_out_18[10]),
    .out_29(l2_rg16plug_1_out_18[11]), .out_30(l2_rg16plug_1_out_18[12]), .out_31(l2_rg16plug_1_out_18[13]),
    .out_32(l2_rg16plug_1_out_18[14]), .out_33(l2_rg16plug_1_out_18[15]));
  L2_RG16PLUG l2_rg16plug_2 (
    .in_17(R2_4), .A(l2_rg16plug_1_out_34), .B(l2_rg16plug_1_out_35), .C(l2_rg16plug_1_out_36),
    .D(l2_rg16plug_1_out_37), .E(l2_rg16plug_1_out_38), .F(l2_rg16plug_1_out_39), .G(l2_rg16plug_1_out_40),
    .H(l2_rg16plug_1_out_41), .I(l2_rg16plug_1_out_42), .J(l2_rg16plug_1_out_43), .L(l2_rg16plug_1_out_44),
    .M(l2_rg16plug_1_out_45), .N(l2_rg16plug_1_out_46), .O(l2_rg16plug_1_out_47), .P(l2_rg16plug_1_out_48),
    .Q(l2_rg16plug_1_out_49), .out_34(l2_rg16plug_2_out_34), .out_35(l2_rg16plug_2_out_35),
    .out_36(l2_rg16plug_2_out_36), .out_37(l2_rg16plug_2_out_37), .out_38(l2_rg16plug_2_out_38),
    .out_39(l2_rg16plug_2_out_39), .out_40(l2_rg16plug_2_out_40), .out_41(l2_rg16plug_2_out_41),
    .out_42(l2_rg16plug_2_out_42), .out_43(l2_rg16plug_2_out_43), .out_44(l2_rg16plug_2_out_44),
    .out_45(l2_rg16plug_2_out_45), .out_46(l2_rg16plug_2_out_46), .out_47(l2_rg16plug_2_out_47),
    .out_48(l2_rg16plug_2_out_48), .out_49(l2_rg16plug_2_out_49), .out_18(l2_rg16plug_2_out_18[0]),
    .out_19(l2_rg16plug_2_out_18[1]), .out_20(l2_rg16plug_2_out_18[2]), .out_21(l2_rg16plug_2_out_18[3]),
    .out_22(l2_rg16plug_2_out_18[4]), .out_23(l2_rg16plug_2_out_18[5]), .out_24(l2_rg16plug_2_out_18[6]),
    .out_25(l2_rg16plug_2_out_18[7]), .out_26(l2_rg16plug_2_out_18[8]), .out_27(l2_rg16plug_2_out_18[9]),
    .out_28(l2_rg16plug_2_out_18[10]), .out_29(l2_rg16plug_2_out_18[11]), .out_30(l2_rg16plug_2_out_18[12]),
    .out_31(l2_rg16plug_2_out_18[13]), .out_32(l2_rg16plug_2_out_18[14]), .out_33(l2_rg16plug_2_out_18[15]));
  L2_RG16PLUG l2_rg16plug_3 (
    .in_17(R3), .A(l2_rg16plug_2_out_34), .B(l2_rg16plug_2_out_35), .C(l2_rg16plug_2_out_36),
    .D(l2_rg16plug_2_out_37), .E(l2_rg16plug_2_out_38), .F(l2_rg16plug_2_out_39), .G(l2_rg16plug_2_out_40),
    .H(l2_rg16plug_2_out_41), .I(l2_rg16plug_2_out_42), .J(l2_rg16plug_2_out_43), .L(l2_rg16plug_2_out_44),
    .M(l2_rg16plug_2_out_45), .N(l2_rg16plug_2_out_46), .O(l2_rg16plug_2_out_47), .P(l2_rg16plug_2_out_48),
    .Q(l2_rg16plug_2_out_49), .out_34(l2_rg16plug_3_out_34), .out_35(l2_rg16plug_3_out_35),
    .out_36(l2_rg16plug_3_out_36), .out_37(l2_rg16plug_3_out_37), .out_38(l2_rg16plug_3_out_38),
    .out_39(l2_rg16plug_3_out_39), .out_40(l2_rg16plug_3_out_40), .out_41(l2_rg16plug_3_out_41),
    .out_42(l2_rg16plug_3_out_42), .out_43(l2_rg16plug_3_out_43), .out_44(l2_rg16plug_3_out_44),
    .out_45(l2_rg16plug_3_out_45), .out_46(l2_rg16plug_3_out_46), .out_47(l2_rg16plug_3_out_47),
    .out_48(l2_rg16plug_3_out_48), .out_49(l2_rg16plug_3_out_49), .out_18(l2_rg16plug_3_out_18[0]),
    .out_19(l2_rg16plug_3_out_18[1]), .out_20(l2_rg16plug_3_out_18[2]), .out_21(l2_rg16plug_3_out_18[3]),
    .out_22(l2_rg16plug_3_out_18[4]), .out_23(l2_rg16plug_3_out_18[5]), .out_24(l2_rg16plug_3_out_18[6]),
    .out_25(l2_rg16plug_3_out_18[7]), .out_26(l2_rg16plug_3_out_18[8]), .out_27(l2_rg16plug_3_out_18[9]),
    .out_28(l2_rg16plug_3_out_18[10]), .out_29(l2_rg16plug_3_out_18[11]), .out_30(l2_rg16plug_3_out_18[12]),
    .out_31(l2_rg16plug_3_out_18[13]), .out_32(l2_rg16plug_3_out_18[14]), .out_33(l2_rg16plug_3_out_18[15]));
  L2_RG16PLUG l2_rg16plug_4 (
    .in_17(R4), .A(l2_rg16plug_3_out_34), .B(l2_rg16plug_3_out_35), .C(l2_rg16plug_3_out_36),
    .D(l2_rg16plug_3_out_37), .E(l2_rg16plug_3_out_38), .F(l2_rg16plug_3_out_39), .G(l2_rg16plug_3_out_40),
    .H(l2_rg16plug_3_out_41), .I(l2_rg16plug_3_out_42), .J(l2_rg16plug_3_out_43), .L(l2_rg16plug_3_out_44),
    .M(l2_rg16plug_3_out_45), .N(l2_rg16plug_3_out_46), .O(l2_rg16plug_3_out_47), .P(l2_rg16plug_3_out_48),
    .Q(l2_rg16plug_3_out_49), .out_34(l2_rg16plug_4_out_34), .out_35(l2_rg16plug_4_out_35),
    .out_36(l2_rg16plug_4_out_36), .out_37(l2_rg16plug_4_out_37), .out_38(l2_rg16plug_4_out_38),
    .out_39(l2_rg16plug_4_out_39), .out_40(l2_rg16plug_4_out_40), .out_41(l2_rg16plug_4_out_41),
    .out_42(l2_rg16plug_4_out_42), .out_43(l2_rg16plug_4_out_43), .out_44(l2_rg16plug_4_out_44),
    .out_45(l2_rg16plug_4_out_45), .out_46(l2_rg16plug_4_out_46), .out_47(l2_rg16plug_4_out_47),
    .out_48(l2_rg16plug_4_out_48), .out_49(l2_rg16plug_4_out_49), .out_18(l2_rg16plug_4_out_18[0]),
    .out_19(l2_rg16plug_4_out_18[1]), .out_20(l2_rg16plug_4_out_18[2]), .out_21(l2_rg16plug_4_out_18[3]),
    .out_22(l2_rg16plug_4_out_18[4]), .out_23(l2_rg16plug_4_out_18[5]), .out_24(l2_rg16plug_4_out_18[6]),
    .out_25(l2_rg16plug_4_out_18[7]), .out_26(l2_rg16plug_4_out_18[8]), .out_27(l2_rg16plug_4_out_18[9]),
    .out_28(l2_rg16plug_4_out_18[10]), .out_29(l2_rg16plug_4_out_18[11]), .out_30(l2_rg16plug_4_out_18[12]),
    .out_31(l2_rg16plug_4_out_18[13]), .out_32(l2_rg16plug_4_out_18[14]), .out_33(l2_rg16plug_4_out_18[15]));
  L2_RG16PLUG l2_rg16plug_5 (
    .in_17(R5), .A(l2_rg16plug_4_out_34), .B(l2_rg16plug_4_out_35), .C(l2_rg16plug_4_out_36),
    .D(l2_rg16plug_4_out_37), .E(l2_rg16plug_4_out_38), .F(l2_rg16plug_4_out_39), .G(l2_rg16plug_4_out_40),
    .H(l2_rg16plug_4_out_41), .I(l2_rg16plug_4_out_42), .J(l2_rg16plug_4_out_43), .L(l2_rg16plug_4_out_44),
    .M(l2_rg16plug_4_out_45), .N(l2_rg16plug_4_out_46), .O(l2_rg16plug_4_out_47), .P(l2_rg16plug_4_out_48),
    .Q(l2_rg16plug_4_out_49), .out_34(l2_rg16plug_5_out_34), .out_35(l2_rg16plug_5_out_35),
    .out_36(l2_rg16plug_5_out_36), .out_37(l2_rg16plug_5_out_37), .out_38(l2_rg16plug_5_out_38),
    .out_39(l2_rg16plug_5_out_39), .out_40(l2_rg16plug_5_out_40), .out_41(l2_rg16plug_5_out_41),
    .out_42(l2_rg16plug_5_out_42), .out_43(l2_rg16plug_5_out_43), .out_44(l2_rg16plug_5_out_44),
    .out_45(l2_rg16plug_5_out_45), .out_46(l2_rg16plug_5_out_46), .out_47(l2_rg16plug_5_out_47),
    .out_48(l2_rg16plug_5_out_48), .out_49(l2_rg16plug_5_out_49), .out_18(l2_rg16plug_5_out_18[0]),
    .out_19(l2_rg16plug_5_out_18[1]), .out_20(l2_rg16plug_5_out_18[2]), .out_21(l2_rg16plug_5_out_18[3]),
    .out_22(l2_rg16plug_5_out_18[4]), .out_23(l2_rg16plug_5_out_18[5]), .out_24(l2_rg16plug_5_out_18[6]),
    .out_25(l2_rg16plug_5_out_18[7]), .out_26(l2_rg16plug_5_out_18[8]), .out_27(l2_rg16plug_5_out_18[9]),
    .out_28(l2_rg16plug_5_out_18[10]), .out_29(l2_rg16plug_5_out_18[11]), .out_30(l2_rg16plug_5_out_18[12]),
    .out_31(l2_rg16plug_5_out_18[13]), .out_32(l2_rg16plug_5_out_18[14]), .out_33(l2_rg16plug_5_out_18[15]));
  L2_RG16PLUG l2_rg16plug_6 (
    .in_17(R6), .A(l2_rg16plug_5_out_34), .B(l2_rg16plug_5_out_35), .C(l2_rg16plug_5_out_36),
    .D(l2_rg16plug_5_out_37), .E(l2_rg16plug_5_out_38), .F(l2_rg16plug_5_out_39), .G(l2_rg16plug_5_out_40),
    .H(l2_rg16plug_5_out_41), .I(l2_rg16plug_5_out_42), .J(l2_rg16plug_5_out_43), .L(l2_rg16plug_5_out_44),
    .M(l2_rg16plug_5_out_45), .N(l2_rg16plug_5_out_46), .O(l2_rg16plug_5_out_47), .P(l2_rg16plug_5_out_48),
    .Q(l2_rg16plug_5_out_49), .out_34(l2_rg16plug_6_out_34), .out_35(l2_rg16plug_6_out_35),
    .out_36(l2_rg16plug_6_out_36), .out_37(l2_rg16plug_6_out_37), .out_38(l2_rg16plug_6_out_38),
    .out_39(l2_rg16plug_6_out_39), .out_40(l2_rg16plug_6_out_40), .out_41(l2_rg16plug_6_out_41),
    .out_42(l2_rg16plug_6_out_42), .out_43(l2_rg16plug_6_out_43), .out_44(l2_rg16plug_6_out_44),
    .out_45(l2_rg16plug_6_out_45), .out_46(l2_rg16plug_6_out_46), .out_47(l2_rg16plug_6_out_47),
    .out_48(l2_rg16plug_6_out_48), .out_49(l2_rg16plug_6_out_49), .out_18(l2_rg16plug_6_out_18[0]),
    .out_19(l2_rg16plug_6_out_18[1]), .out_20(l2_rg16plug_6_out_18[2]), .out_21(l2_rg16plug_6_out_18[3]),
    .out_22(l2_rg16plug_6_out_18[4]), .out_23(l2_rg16plug_6_out_18[5]), .out_24(l2_rg16plug_6_out_18[6]),
    .out_25(l2_rg16plug_6_out_18[7]), .out_26(l2_rg16plug_6_out_18[8]), .out_27(l2_rg16plug_6_out_18[9]),
    .out_28(l2_rg16plug_6_out_18[10]), .out_29(l2_rg16plug_6_out_18[11]), .out_30(l2_rg16plug_6_out_18[12]),
    .out_31(l2_rg16plug_6_out_18[13]), .out_32(l2_rg16plug_6_out_18[14]), .out_33(l2_rg16plug_6_out_18[15]));
  L2_RG16PLUG l2_rg16plug_7 (
    .in_17(R7), .A(l2_rg16plug_6_out_34), .B(l2_rg16plug_6_out_35), .C(l2_rg16plug_6_out_36),
    .D(l2_rg16plug_6_out_37), .E(l2_rg16plug_6_out_38), .F(l2_rg16plug_6_out_39), .G(l2_rg16plug_6_out_40),
    .H(l2_rg16plug_6_out_41), .I(l2_rg16plug_6_out_42), .J(l2_rg16plug_6_out_43), .L(l2_rg16plug_6_out_44),
    .M(l2_rg16plug_6_out_45), .N(l2_rg16plug_6_out_46), .O(l2_rg16plug_6_out_47), .P(l2_rg16plug_6_out_48),
    .Q(l2_rg16plug_6_out_49), .out_34(l2_rg16plug_7_out_34), .out_35(l2_rg16plug_7_out_35),
    .out_36(l2_rg16plug_7_out_36), .out_37(l2_rg16plug_7_out_37), .out_38(l2_rg16plug_7_out_38),
    .out_39(l2_rg16plug_7_out_39), .out_40(l2_rg16plug_7_out_40), .out_41(l2_rg16plug_7_out_41),
    .out_42(l2_rg16plug_7_out_42), .out_43(l2_rg16plug_7_out_43), .out_44(l2_rg16plug_7_out_44),
    .out_45(l2_rg16plug_7_out_45), .out_46(l2_rg16plug_7_out_46), .out_47(l2_rg16plug_7_out_47),
    .out_48(l2_rg16plug_7_out_48), .out_49(l2_rg16plug_7_out_49), .out_18(l2_rg16plug_7_out_18[0]),
    .out_19(l2_rg16plug_7_out_18[1]), .out_20(l2_rg16plug_7_out_18[2]), .out_21(l2_rg16plug_7_out_18[3]),
    .out_22(l2_rg16plug_7_out_18[4]), .out_23(l2_rg16plug_7_out_18[5]), .out_24(l2_rg16plug_7_out_18[6]),
    .out_25(l2_rg16plug_7_out_18[7]), .out_26(l2_rg16plug_7_out_18[8]), .out_27(l2_rg16plug_7_out_18[9]),
    .out_28(l2_rg16plug_7_out_18[10]), .out_29(l2_rg16plug_7_out_18[11]), .out_30(l2_rg16plug_7_out_18[12]),
    .out_31(l2_rg16plug_7_out_18[13]), .out_32(l2_rg16plug_7_out_18[14]), .out_33(l2_rg16plug_7_out_18[15]));
  L2_RG16PLUG l2_rg16plug_8 (
    .in_17(R8), .A(l2_rg16plug_7_out_34), .B(l2_rg16plug_7_out_35), .C(l2_rg16plug_7_out_36),
    .D(l2_rg16plug_7_out_37), .E(l2_rg16plug_7_out_38), .F(l2_rg16plug_7_out_39), .G(l2_rg16plug_7_out_40),
    .H(l2_rg16plug_7_out_41), .I(l2_rg16plug_7_out_42), .J(l2_rg16plug_7_out_43), .L(l2_rg16plug_7_out_44),
    .M(l2_rg16plug_7_out_45), .N(l2_rg16plug_7_out_46), .O(l2_rg16plug_7_out_47), .P(l2_rg16plug_7_out_48),
    .Q(l2_rg16plug_7_out_49), .out_34(l2_rg16plug_8_out_34), .out_35(l2_rg16plug_8_out_35),
    .out_36(l2_rg16plug_8_out_36), .out_37(l2_rg16plug_8_out_37), .out_38(l2_rg16plug_8_out_38),
    .out_39(l2_rg16plug_8_out_39), .out_40(l2_rg16plug_8_out_40), .out_41(l2_rg16plug_8_out_41),
    .out_42(l2_rg16plug_8_out_42), .out_43(l2_rg16plug_8_out_43), .out_44(l2_rg16plug_8_out_44),
    .out_45(l2_rg16plug_8_out_45), .out_46(l2_rg16plug_8_out_46), .out_47(l2_rg16plug_8_out_47),
    .out_48(l2_rg16plug_8_out_48), .out_49(l2_rg16plug_8_out_49), .out_18(l2_rg16plug_8_out_18[0]),
    .out_19(l2_rg16plug_8_out_18[1]), .out_20(l2_rg16plug_8_out_18[2]), .out_21(l2_rg16plug_8_out_18[3]),
    .out_22(l2_rg16plug_8_out_18[4]), .out_23(l2_rg16plug_8_out_18[5]), .out_24(l2_rg16plug_8_out_18[6]),
    .out_25(l2_rg16plug_8_out_18[7]), .out_26(l2_rg16plug_8_out_18[8]), .out_27(l2_rg16plug_8_out_18[9]),
    .out_28(l2_rg16plug_8_out_18[10]), .out_29(l2_rg16plug_8_out_18[11]), .out_30(l2_rg16plug_8_out_18[12]),
    .out_31(l2_rg16plug_8_out_18[13]), .out_32(l2_rg16plug_8_out_18[14]), .out_33(l2_rg16plug_8_out_18[15]));
  L2_RG16PLUG l2_rg16plug_9 (
    .in_17(R9), .A(l2_rg16plug_8_out_34), .B(l2_rg16plug_8_out_35), .C(l2_rg16plug_8_out_36),
    .D(l2_rg16plug_8_out_37), .E(l2_rg16plug_8_out_38), .F(l2_rg16plug_8_out_39), .G(l2_rg16plug_8_out_40),
    .H(l2_rg16plug_8_out_41), .I(l2_rg16plug_8_out_42), .J(l2_rg16plug_8_out_43), .L(l2_rg16plug_8_out_44),
    .M(l2_rg16plug_8_out_45), .N(l2_rg16plug_8_out_46), .O(l2_rg16plug_8_out_47), .P(l2_rg16plug_8_out_48),
    .Q(l2_rg16plug_8_out_49), .out_34(l2_rg16plug_9_out_34), .out_35(l2_rg16plug_9_out_35),
    .out_36(l2_rg16plug_9_out_36), .out_37(l2_rg16plug_9_out_37), .out_38(l2_rg16plug_9_out_38),
    .out_39(l2_rg16plug_9_out_39), .out_40(l2_rg16plug_9_out_40), .out_41(l2_rg16plug_9_out_41),
    .out_42(l2_rg16plug_9_out_42), .out_43(l2_rg16plug_9_out_43), .out_44(l2_rg16plug_9_out_44),
    .out_45(l2_rg16plug_9_out_45), .out_46(l2_rg16plug_9_out_46), .out_47(l2_rg16plug_9_out_47),
    .out_48(l2_rg16plug_9_out_48), .out_49(l2_rg16plug_9_out_49), .out_18(l2_rg16plug_9_out_18[0]),
    .out_19(l2_rg16plug_9_out_18[1]), .out_20(l2_rg16plug_9_out_18[2]), .out_21(l2_rg16plug_9_out_18[3]),
    .out_22(l2_rg16plug_9_out_18[4]), .out_23(l2_rg16plug_9_out_18[5]), .out_24(l2_rg16plug_9_out_18[6]),
    .out_25(l2_rg16plug_9_out_18[7]), .out_26(l2_rg16plug_9_out_18[8]), .out_27(l2_rg16plug_9_out_18[9]),
    .out_28(l2_rg16plug_9_out_18[10]), .out_29(l2_rg16plug_9_out_18[11]), .out_30(l2_rg16plug_9_out_18[12]),
    .out_31(l2_rg16plug_9_out_18[13]), .out_32(l2_rg16plug_9_out_18[14]), .out_33(l2_rg16plug_9_out_18[15]));
  L2_RG16PLUG l2_rg16plug_10 (
    .in_17(R10), .A(l2_rg16plug_9_out_34), .B(l2_rg16plug_9_out_35), .C(l2_rg16plug_9_out_36),
    .D(l2_rg16plug_9_out_37), .E(l2_rg16plug_9_out_38), .F(l2_rg16plug_9_out_39), .G(l2_rg16plug_9_out_40),
    .H(l2_rg16plug_9_out_41), .I(l2_rg16plug_9_out_42), .J(l2_rg16plug_9_out_43), .L(l2_rg16plug_9_out_44),
    .M(l2_rg16plug_9_out_45), .N(l2_rg16plug_9_out_46), .O(l2_rg16plug_9_out_47), .P(l2_rg16plug_9_out_48),
    .Q(l2_rg16plug_9_out_49), .out_34(l2_rg16plug_10_out_34), .out_35(l2_rg16plug_10_out_35),
    .out_36(l2_rg16plug_10_out_36), .out_37(l2_rg16plug_10_out_37), .out_38(l2_rg16plug_10_out_38),
    .out_39(l2_rg16plug_10_out_39), .out_40(l2_rg16plug_10_out_40), .out_41(l2_rg16plug_10_out_41),
    .out_42(l2_rg16plug_10_out_42), .out_43(l2_rg16plug_10_out_43), .out_44(l2_rg16plug_10_out_44),
    .out_45(l2_rg16plug_10_out_45), .out_46(l2_rg16plug_10_out_46), .out_47(l2_rg16plug_10_out_47),
    .out_48(l2_rg16plug_10_out_48), .out_49(l2_rg16plug_10_out_49), .out_18(l2_rg16plug_10_out_18[0]),
    .out_19(l2_rg16plug_10_out_18[1]), .out_20(l2_rg16plug_10_out_18[2]), .out_21(l2_rg16plug_10_out_18[3]),
    .out_22(l2_rg16plug_10_out_18[4]), .out_23(l2_rg16plug_10_out_18[5]), .out_24(l2_rg16plug_10_out_18[6]),
    .out_25(l2_rg16plug_10_out_18[7]), .out_26(l2_rg16plug_10_out_18[8]), .out_27(l2_rg16plug_10_out_18[9]),
    .out_28(l2_rg16plug_10_out_18[10]), .out_29(l2_rg16plug_10_out_18[11]),
    .out_30(l2_rg16plug_10_out_18[12]), .out_31(l2_rg16plug_10_out_18[13]),
    .out_32(l2_rg16plug_10_out_18[14]), .out_33(l2_rg16plug_10_out_18[15]));
  L2_RG16PLUG l2_rg16plug_11 (
    .in_17(R11), .A(l2_rg16plug_10_out_34), .B(l2_rg16plug_10_out_35), .C(l2_rg16plug_10_out_36),
    .D(l2_rg16plug_10_out_37), .E(l2_rg16plug_10_out_38), .F(l2_rg16plug_10_out_39),
    .G(l2_rg16plug_10_out_40), .H(l2_rg16plug_10_out_41), .I(l2_rg16plug_10_out_42),
    .J(l2_rg16plug_10_out_43), .L(l2_rg16plug_10_out_44), .M(l2_rg16plug_10_out_45),
    .N(l2_rg16plug_10_out_46), .O(l2_rg16plug_10_out_47), .P(l2_rg16plug_10_out_48),
    .Q(l2_rg16plug_10_out_49), .out_34(l2_rg16plug_11_out_34), .out_35(l2_rg16plug_11_out_35),
    .out_36(l2_rg16plug_11_out_36), .out_37(l2_rg16plug_11_out_37), .out_38(l2_rg16plug_11_out_38),
    .out_39(l2_rg16plug_11_out_39), .out_40(l2_rg16plug_11_out_40), .out_41(l2_rg16plug_11_out_41),
    .out_42(l2_rg16plug_11_out_42), .out_43(l2_rg16plug_11_out_43), .out_44(l2_rg16plug_11_out_44),
    .out_45(l2_rg16plug_11_out_45), .out_46(l2_rg16plug_11_out_46), .out_47(l2_rg16plug_11_out_47),
    .out_48(l2_rg16plug_11_out_48), .out_49(l2_rg16plug_11_out_49), .out_18(l2_rg16plug_11_out_18[0]),
    .out_19(l2_rg16plug_11_out_18[1]), .out_20(l2_rg16plug_11_out_18[2]), .out_21(l2_rg16plug_11_out_18[3]),
    .out_22(l2_rg16plug_11_out_18[4]), .out_23(l2_rg16plug_11_out_18[5]), .out_24(l2_rg16plug_11_out_18[6]),
    .out_25(l2_rg16plug_11_out_18[7]), .out_26(l2_rg16plug_11_out_18[8]), .out_27(l2_rg16plug_11_out_18[9]),
    .out_28(l2_rg16plug_11_out_18[10]), .out_29(l2_rg16plug_11_out_18[11]),
    .out_30(l2_rg16plug_11_out_18[12]), .out_31(l2_rg16plug_11_out_18[13]),
    .out_32(l2_rg16plug_11_out_18[14]), .out_33(l2_rg16plug_11_out_18[15]));
  L2_RG16PLUG l2_rg16plug_12 (
    .in_17(R12), .A(l2_rg16plug_11_out_34), .B(l2_rg16plug_11_out_35), .C(l2_rg16plug_11_out_36),
    .D(l2_rg16plug_11_out_37), .E(l2_rg16plug_11_out_38), .F(l2_rg16plug_11_out_39),
    .G(l2_rg16plug_11_out_40), .H(l2_rg16plug_11_out_41), .I(l2_rg16plug_11_out_42),
    .J(l2_rg16plug_11_out_43), .L(l2_rg16plug_11_out_44), .M(l2_rg16plug_11_out_45),
    .N(l2_rg16plug_11_out_46), .O(l2_rg16plug_11_out_47), .P(l2_rg16plug_11_out_48),
    .Q(l2_rg16plug_11_out_49), .out_34(l2_rg16plug_12_out_34), .out_35(l2_rg16plug_12_out_35),
    .out_36(l2_rg16plug_12_out_36), .out_37(l2_rg16plug_12_out_37), .out_38(l2_rg16plug_12_out_38),
    .out_39(l2_rg16plug_12_out_39), .out_40(l2_rg16plug_12_out_40), .out_41(l2_rg16plug_12_out_41),
    .out_42(l2_rg16plug_12_out_42), .out_43(l2_rg16plug_12_out_43), .out_44(l2_rg16plug_12_out_44),
    .out_45(l2_rg16plug_12_out_45), .out_46(l2_rg16plug_12_out_46), .out_47(l2_rg16plug_12_out_47),
    .out_48(l2_rg16plug_12_out_48), .out_49(l2_rg16plug_12_out_49), .out_18(l2_rg16plug_12_out_18[0]),
    .out_19(l2_rg16plug_12_out_18[1]), .out_20(l2_rg16plug_12_out_18[2]), .out_21(l2_rg16plug_12_out_18[3]),
    .out_22(l2_rg16plug_12_out_18[4]), .out_23(l2_rg16plug_12_out_18[5]), .out_24(l2_rg16plug_12_out_18[6]),
    .out_25(l2_rg16plug_12_out_18[7]), .out_26(l2_rg16plug_12_out_18[8]), .out_27(l2_rg16plug_12_out_18[9]),
    .out_28(l2_rg16plug_12_out_18[10]), .out_29(l2_rg16plug_12_out_18[11]),
    .out_30(l2_rg16plug_12_out_18[12]), .out_31(l2_rg16plug_12_out_18[13]),
    .out_32(l2_rg16plug_12_out_18[14]), .out_33(l2_rg16plug_12_out_18[15]));
  L2_RG16PLUG l2_rg16plug_13 (
    .in_17(R13), .A(l2_rg16plug_12_out_34), .B(l2_rg16plug_12_out_35), .C(l2_rg16plug_12_out_36),
    .D(l2_rg16plug_12_out_37), .E(l2_rg16plug_12_out_38), .F(l2_rg16plug_12_out_39),
    .G(l2_rg16plug_12_out_40), .H(l2_rg16plug_12_out_41), .I(l2_rg16plug_12_out_42),
    .J(l2_rg16plug_12_out_43), .L(l2_rg16plug_12_out_44), .M(l2_rg16plug_12_out_45),
    .N(l2_rg16plug_12_out_46), .O(l2_rg16plug_12_out_47), .P(l2_rg16plug_12_out_48),
    .Q(l2_rg16plug_12_out_49), .out_34(l2_rg16plug_13_out_34), .out_35(l2_rg16plug_13_out_35),
    .out_36(l2_rg16plug_13_out_36), .out_37(l2_rg16plug_13_out_37), .out_38(l2_rg16plug_13_out_38),
    .out_39(l2_rg16plug_13_out_39), .out_40(l2_rg16plug_13_out_40), .out_41(l2_rg16plug_13_out_41),
    .out_42(l2_rg16plug_13_out_42), .out_43(l2_rg16plug_13_out_43), .out_44(l2_rg16plug_13_out_44),
    .out_45(l2_rg16plug_13_out_45), .out_46(l2_rg16plug_13_out_46), .out_47(l2_rg16plug_13_out_47),
    .out_48(l2_rg16plug_13_out_48), .out_49(l2_rg16plug_13_out_49), .out_18(l2_rg16plug_13_out_18[0]),
    .out_19(l2_rg16plug_13_out_18[1]), .out_20(l2_rg16plug_13_out_18[2]), .out_21(l2_rg16plug_13_out_18[3]),
    .out_22(l2_rg16plug_13_out_18[4]), .out_23(l2_rg16plug_13_out_18[5]), .out_24(l2_rg16plug_13_out_18[6]),
    .out_25(l2_rg16plug_13_out_18[7]), .out_26(l2_rg16plug_13_out_18[8]), .out_27(l2_rg16plug_13_out_18[9]),
    .out_28(l2_rg16plug_13_out_18[10]), .out_29(l2_rg16plug_13_out_18[11]),
    .out_30(l2_rg16plug_13_out_18[12]), .out_31(l2_rg16plug_13_out_18[13]),
    .out_32(l2_rg16plug_13_out_18[14]), .out_33(l2_rg16plug_13_out_18[15]));
  L2_RG16PLUG l2_rg16plug_14 (
    .in_17(R14), .A(l2_rg16plug_13_out_34), .B(l2_rg16plug_13_out_35), .C(l2_rg16plug_13_out_36),
    .D(l2_rg16plug_13_out_37), .E(l2_rg16plug_13_out_38), .F(l2_rg16plug_13_out_39),
    .G(l2_rg16plug_13_out_40), .H(l2_rg16plug_13_out_41), .I(l2_rg16plug_13_out_42),
    .J(l2_rg16plug_13_out_43), .L(l2_rg16plug_13_out_44), .M(l2_rg16plug_13_out_45),
    .N(l2_rg16plug_13_out_46), .O(l2_rg16plug_13_out_47), .P(l2_rg16plug_13_out_48),
    .Q(l2_rg16plug_13_out_49), .out_34(l2_rg16plug_14_out_34), .out_35(l2_rg16plug_14_out_35),
    .out_36(l2_rg16plug_14_out_36), .out_37(l2_rg16plug_14_out_37), .out_38(l2_rg16plug_14_out_38),
    .out_39(l2_rg16plug_14_out_39), .out_40(l2_rg16plug_14_out_40), .out_41(l2_rg16plug_14_out_41),
    .out_42(l2_rg16plug_14_out_42), .out_43(l2_rg16plug_14_out_43), .out_44(l2_rg16plug_14_out_44),
    .out_45(l2_rg16plug_14_out_45), .out_46(l2_rg16plug_14_out_46), .out_47(l2_rg16plug_14_out_47),
    .out_48(l2_rg16plug_14_out_48), .out_49(l2_rg16plug_14_out_49), .out_18(l2_rg16plug_14_out_18[0]),
    .out_19(l2_rg16plug_14_out_18[1]), .out_20(l2_rg16plug_14_out_18[2]), .out_21(l2_rg16plug_14_out_18[3]),
    .out_22(l2_rg16plug_14_out_18[4]), .out_23(l2_rg16plug_14_out_18[5]), .out_24(l2_rg16plug_14_out_18[6]),
    .out_25(l2_rg16plug_14_out_18[7]), .out_26(l2_rg16plug_14_out_18[8]), .out_27(l2_rg16plug_14_out_18[9]),
    .out_28(l2_rg16plug_14_out_18[10]), .out_29(l2_rg16plug_14_out_18[11]),
    .out_30(l2_rg16plug_14_out_18[12]), .out_31(l2_rg16plug_14_out_18[13]),
    .out_32(l2_rg16plug_14_out_18[14]), .out_33(l2_rg16plug_14_out_18[15]));
  L2_RG16PLUG l2_rg16plug_15 (
    .in_17(R15), .A(l2_rg16plug_14_out_34), .B(l2_rg16plug_14_out_35), .C(l2_rg16plug_14_out_36),
    .D(l2_rg16plug_14_out_37), .E(l2_rg16plug_14_out_38), .F(l2_rg16plug_14_out_39),
    .G(l2_rg16plug_14_out_40), .H(l2_rg16plug_14_out_41), .I(l2_rg16plug_14_out_42),
    .J(l2_rg16plug_14_out_43), .L(l2_rg16plug_14_out_44), .M(l2_rg16plug_14_out_45),
    .N(l2_rg16plug_14_out_46), .O(l2_rg16plug_14_out_47), .P(l2_rg16plug_14_out_48),
    .Q(l2_rg16plug_14_out_49), .out_34(l2_rg16plug_15_out_34), .out_35(l2_rg16plug_15_out_35),
    .out_36(l2_rg16plug_15_out_36), .out_37(l2_rg16plug_15_out_37), .out_38(l2_rg16plug_15_out_38),
    .out_39(l2_rg16plug_15_out_39), .out_40(l2_rg16plug_15_out_40), .out_41(l2_rg16plug_15_out_41),
    .out_42(l2_rg16plug_15_out_42), .out_43(l2_rg16plug_15_out_43), .out_44(l2_rg16plug_15_out_44),
    .out_45(l2_rg16plug_15_out_45), .out_46(l2_rg16plug_15_out_46), .out_47(l2_rg16plug_15_out_47),
    .out_48(l2_rg16plug_15_out_48), .out_49(l2_rg16plug_15_out_49), .out_18(l2_rg16plug_15_out_18[0]),
    .out_19(l2_rg16plug_15_out_18[1]), .out_20(l2_rg16plug_15_out_18[2]), .out_21(l2_rg16plug_15_out_18[3]),
    .out_22(l2_rg16plug_15_out_18[4]), .out_23(l2_rg16plug_15_out_18[5]), .out_24(l2_rg16plug_15_out_18[6]),
    .out_25(l2_rg16plug_15_out_18[7]), .out_26(l2_rg16plug_15_out_18[8]), .out_27(l2_rg16plug_15_out_18[9]),
    .out_28(l2_rg16plug_15_out_18[10]), .out_29(l2_rg16plug_15_out_18[11]),
    .out_30(l2_rg16plug_15_out_18[12]), .out_31(l2_rg16plug_15_out_18[13]),
    .out_32(l2_rg16plug_15_out_18[14]), .out_33(l2_rg16plug_15_out_18[15]));
  L2_RG16PLUG l2_rg16plug_16 (
    .in_17(R16), .A(l2_rg16plug_15_out_34), .B(l2_rg16plug_15_out_35), .C(l2_rg16plug_15_out_36),
    .D(l2_rg16plug_15_out_37), .E(l2_rg16plug_15_out_38), .F(l2_rg16plug_15_out_39),
    .G(l2_rg16plug_15_out_40), .H(l2_rg16plug_15_out_41), .I(l2_rg16plug_15_out_42),
    .J(l2_rg16plug_15_out_43), .L(l2_rg16plug_15_out_44), .M(l2_rg16plug_15_out_45),
    .N(l2_rg16plug_15_out_46), .O(l2_rg16plug_15_out_47), .P(l2_rg16plug_15_out_48),
    .Q(l2_rg16plug_15_out_49), .out_18(l2_rg16plug_16_out_18[0]), .out_19(l2_rg16plug_16_out_18[1]),
    .out_20(l2_rg16plug_16_out_18[2]), .out_21(l2_rg16plug_16_out_18[3]), .out_22(l2_rg16plug_16_out_18[4]),
    .out_23(l2_rg16plug_16_out_18[5]), .out_24(l2_rg16plug_16_out_18[6]), .out_25(l2_rg16plug_16_out_18[7]),
    .out_26(l2_rg16plug_16_out_18[8]), .out_27(l2_rg16plug_16_out_18[9]), .out_28(l2_rg16plug_16_out_18[10]),
    .out_29(l2_rg16plug_16_out_18[11]), .out_30(l2_rg16plug_16_out_18[12]),
    .out_31(l2_rg16plug_16_out_18[13]), .out_32(l2_rg16plug_16_out_18[14]), .out_33(l2_rg16plug_16_out_18[15]));  // open: out_34, out_35, out_36, out_37, out_38, out_39, out_40, out_41, out_42, out_43, out_44, out_45, out_46, out_47, out_48, out_49
  Multiplexer #(.select(4), .width(16)) multiplexer_1 (
    .in0(l2_rg16plug_1_out_18), .in1(l2_rg16plug_2_out_18), .in2(l2_rg16plug_3_out_18),
    .in3(l2_rg16plug_4_out_18), .in4(l2_rg16plug_5_out_18), .in5(l2_rg16plug_6_out_18),
    .in6(l2_rg16plug_7_out_18), .in7(l2_rg16plug_8_out_18), .in8(l2_rg16plug_9_out_18),
    .in9(l2_rg16plug_10_out_18), .in10(l2_rg16plug_11_out_18), .in11(l2_rg16plug_12_out_18),
    .in12(l2_rg16plug_13_out_18), .in13(l2_rg16plug_14_out_18), .in14(l2_rg16plug_15_out_18),
    .in15(l2_rg16plug_16_out_18),
    .out({OUT_INPUT_4, OUT_INPUT_3, OUT_INPUT_2, OUT_INPUT, OUT_R2_3, OUT_R2_2, OUT_R2, OUT_R1_3, OUT_R1_2, OUT_R1, INS_6, INS_5, INS_4, DEST_6, DEST_5, DEST_4}),
    .sel(SELECT));  // open: en
endmodule

module L2_RG16PLUG (
  input  A,
  input  B,
  input  C,
  input  D,
  input  E,
  input  F,
  input  G,
  input  H,
  input  I,
  input  J,
  input  L,
  input  M,
  input  N,
  input  O,
  input  P,
  input  Q,
  input  in_17,
  output out_18,
  output out_19,
  output out_20,
  output out_21,
  output out_22,
  output out_23,
  output out_24,
  output out_25,
  output out_26,
  output out_27,
  output out_28,
  output out_29,
  output out_30,
  output out_31,
  output out_32,
  output out_33,
  output out_34,
  output out_35,
  output out_36,
  output out_37,
  output out_38,
  output out_39,
  output out_40,
  output out_41,
  output out_42,
  output out_43,
  output out_44,
  output out_45,
  output out_46,
  output out_47,
  output out_48,
  output out_49
);

  L2_RG16b l2_rg16b_1 (
    .in_17(in_17), .in_1(Q), .in_2(P), .in_3(O), .in_4(N), .in_5(M), .in_6(L), .in_7(J), .in_8(I), .in_9(H),
    .in_10(G), .in_11(F), .in_12(E), .in_13(D), .in_14(C), .in_15(B), .in_16(A), .out_19(out_33),
    .out_20(out_32), .out_21(out_31), .out_22(out_30), .out_23(out_29), .out_24(out_28), .out_25(out_27),
    .out_26(out_26), .out_27(out_25), .out_28(out_24), .out_29(out_23), .out_30(out_22), .out_31(out_21),
    .out_32(out_20), .out_33(out_19), .out_18(out_18));

  assign out_34 = A;
  assign out_35 = B;
  assign out_36 = C;
  assign out_37 = D;
  assign out_38 = E;
  assign out_39 = F;
  assign out_40 = G;
  assign out_41 = H;
  assign out_42 = I;
  assign out_43 = J;
  assign out_44 = L;
  assign out_45 = M;
  assign out_46 = N;
  assign out_47 = O;
  assign out_48 = P;
  assign out_49 = Q;
endmodule
