// Logisim project processor_with_ram.circ as structural Verilog: 25 circuits, main circuit main
module main (
  input  in_1,
  input  in_2,
  input  in_3,
  input  in_4
);

  wire _0_2_out, _0_3_out, _0_out, _1_2_out, _1_3_out, _1_out, _2_2_out, _2_3_out, _2_out, _3_2_out,
       _3_3_out, _3_out, _4_2_out, _4_3_out, _4_out, _5_2_out, _5_3_out, _5_out, _6_2_out, _6_3_out, _6_out,
       _7_2_out, _7_3_out, _7_out, bcd8421_1_qb, bcd8421_1_qc, bcd8421_1_qd, bcd8421_2_qb, bcd8421_2_qc,
       bcd8421_2_qd, bcd8421_3_qb, bcd8421_3_qc, bcd8421_3_qd, bcd8421_4_qb, bcd8421_4_qc, bcd8421_4_qd,
       button_1_out, button_2_out, button_3_out, button_4_out, button_5_out, button_6_out, button_7_out,
       button_8_out, CLEAR_ALL_out, CLOCK_ALL_out, demux1_16_1_out_6, demux1_16_1_out_7, demux1_16_1_out_8,
       demux1_16_1_out_9, demux1_16_1_out_10, demux1_16_1_out_11, demux1_16_1_out_12, demux1_16_1_out_13,
       demux1_16_1_out_14, demux1_16_1_out_15, demux1_16_1_out_16, demux1_16_1_out_17, demux1_16_1_out_18,
       demux1_16_1_out_19, demux1_16_1_out_20, demux1_16_1_out_21, dmux1_8_1_s0, dmux1_8_1_s1, dmux1_8_1_s2,
       dmux1_8_1_s3, dmux1_8_1_s4, dmux1_8_1_s5, dmux1_8_1_s6, dmux1_8_1_s7, l2_256b_1_dest_4,
       l2_256b_1_dest_5, l2_256b_1_dest_6, l2_256b_1_ins, l2_256b_1_ins_2, l2_256b_1_ins_3, s_out, ula_1_a,
       ula_1_b, ula_1_c, ula_1_d;
  wire [2:0] l2_256b_1_out_r1_3, l2_256b_1_out_r2_3;
  wire [3:0] bcdd8421_0_15_1_d, counter_1_q, dullentry_1_b0_2, entryslt_1_c0, l1_32b_1_d_2, l1_32b_1_d_3,
       l1_32b_1_d_4, l1_32b_1_d_5, l1_32b_1_d_6, l1_32b_1_d_7, l1_32b_1_d_8, l1_32b_1_d_9,
       l2_256b_1_out_input_4, multiplexer_1_out, multiplexer_2_out;
  wire [15:0] _0_4_out;

  Button _0 (.out(_0_out));
  Button _1 (.out(_1_out));
  BCD8421 bcd8421_1 (
    ._0(_0_out), ._1(_1_out), ._2(_2_out), ._3(_3_out), ._4(_4_out), ._5(_5_out), ._6(_6_out), ._7(_7_out),
    ._8(1'b0), ._9(1'b0), .QB(bcd8421_1_qb), .QC(bcd8421_1_qc), .QD(bcd8421_1_qd));  // open: QA
  Button button_1 (.out(button_1_out));
  DMUX1_8 dmux1_8_1 (
    .E(CLOCK_ALL_out), .in_1(l2_256b_1_dest_4), .in_2(l2_256b_1_dest_5), .in_3(l2_256b_1_dest_6),
    .S0(dmux1_8_1_s0), .S1(dmux1_8_1_s1), .S2(dmux1_8_1_s2), .S3(dmux1_8_1_s3), .S4(dmux1_8_1_s4),
    .S5(dmux1_8_1_s5), .S6(dmux1_8_1_s6), .S7(dmux1_8_1_s7));
  Button _4 (.out(_4_out));
  Button _5 (.out(_5_out));
  Button _3 (.out(_3_out));
  Button _2 (.out(_2_out));
  Demux1_16 demux1_16_1 (
    .in_5(button_1_out), .out_6(demux1_16_1_out_6), .out_7(demux1_16_1_out_7), .out_8(demux1_16_1_out_8),
    .out_9(demux1_16_1_out_9), .out_10(demux1_16_1_out_10), .out_11(demux1_16_1_out_11),
    .out_12(demux1_16_1_out_12), .out_13(demux1_16_1_out_13), .out_14(demux1_16_1_out_14),
    .out_15(demux1_16_1_out_15), .out_16(demux1_16_1_out_16), .out_17(demux1_16_1_out_17),
    .out_18(demux1_16_1_out_18), .out_19(demux1_16_1_out_19), .out_20(demux1_16_1_out_20),
    .out_21(demux1_16_1_out_21), .in_1(in_1), .in_2(in_2), .in_3(in_3), .in_4(in_4));
  Button _7 (.out(_7_out));
  Button _6 (.out(_6_out));
  L1_32b l1_32b_1 (
    .R0(dmux1_8_1_s0), .R1(dmux1_8_1_s1), .R2(dmux1_8_1_s2), .R3(dmux1_8_1_s3), .R4(dmux1_8_1_s4),
    .R5(dmux1_8_1_s5), .R6(dmux1_8_1_s6), .R7(dmux1_8_1_s7), .A(ula_1_a), .B(ula_1_b), .C(ula_1_c),
    .D(ula_1_d), .CLEAR(CLEAR_ALL_out), .D_2(l1_32b_1_d_2[0]), .C_2(l1_32b_1_d_2[1]), .B_2(l1_32b_1_d_2[2]),
    .A_2(l1_32b_1_d_2[3]), .D_3(l1_32b_1_d_3[0]), .C_3(l1_32b_1_d_3[1]), .B_3(l1_32b_1_d_3[2]),
    .A_3(l1_32b_1_d_3[3]), .D_4(l1_32b_1_d_4[0]), .C_4(l1_32b_1_d_4[1]), .B_4(l1_32b_1_d_4[2]),
    .A_4(l1_32b_1_d_4[3]), .D_5(l1_32b_1_d_5[0]), .C_5(l1_32b_1_d_5[1]), .B_5(l1_32b_1_d_5[2]),
    .A_5(l1_32b_1_d_5[3]), .D_6(l1_32b_1_d_6[0]), .C_6(l1_32b_1_d_6[1]), .B_6(l1_32b_1_d_6[2]),
    .A_6(l1_32b_1_d_6[3]), .D_7(l1_32b_1_d_7[0]), .C_7(l1_32b_1_d_7[1]), .B_7(l1_32b_1_d_7[2]),
    .A_7(l1_32b_1_d_7[3]), .D_8(l1_32b_1_d_8[0]), .C_8(l1_32b_1_d_8[1]), .B_8(l1_32b_1_d_8[2]),
    .A_8(l1_32b_1_d_8[3]), .D_9(l1_32b_1_d_9[0]), .C_9(l1_32b_1_d_9[1]), .B_9(l1_32b_1_d_9[2]),
    .A_9(l1_32b_1_d_9[3]));
  Hex_Digit_Display hex_digit_display_1 (.value(l1_32b_1_d_2));  // open: dp
  Hex_Digit_Display hex_digit_display_2 (.value(l1_32b_1_d_3));  // open: dp
  Hex_Digit_Display hex_digit_display_3 (.value(l1_32b_1_d_4));  // open: dp
  Hex_Digit_Display hex_digit_display_4 (.value(l1_32b_1_d_5));  // open: dp
  Hex_Digit_Display hex_digit_display_5 (.value(l1_32b_1_d_6));  // open: dp
  Hex_Digit_Display hex_digit_display_6 (.value(l1_32b_1_d_7));  // open: dp
  Hex_Digit_Display hex_digit_display_7 (.value(l1_32b_1_d_8));  // open: dp
  Hex_Digit_Display hex_digit_display_8 (.value(l1_32b_1_d_9));  // open: dp
  Button button_2 (.out(button_2_out));
  Button button_3 (.out(button_3_out));
  Button button_4 (.out(button_4_out));
  Button button_5 (.out(button_5_out));
  BCD8421 bcd8421_2 (
    ._0(button_3_out), ._1(button_2_out), ._2(button_7_out), ._3(button_6_out), ._4(button_4_out),
    ._5(button_5_out), ._6(button_8_out), ._7(s_out), ._8(1'b0), ._9(1'b0), .QB(bcd8421_2_qb),
    .QC(bcd8421_2_qc), .QD(bcd8421_2_qd));  // open: QA
  Button button_6 (.out(button_6_out));
  Button button_7 (.out(button_7_out));
  Button s (.out(s_out));
  Button button_8 (.out(button_8_out));
  Button _3_2 (.out(_3_2_out));
  Button _0_2 (.out(_0_2_out));
  Button _2_2 (.out(_2_2_out));
  Button _1_2 (.out(_1_2_out));
  BCD8421 bcd8421_3 (
    ._0(_0_2_out), ._1(_1_2_out), ._2(_2_2_out), ._3(_3_2_out), ._4(_4_2_out), ._5(_5_2_out), ._6(_6_2_out),
    ._7(_7_2_out), ._8(1'b0), ._9(1'b0), .QB(bcd8421_3_qb), .QC(bcd8421_3_qc), .QD(bcd8421_3_qd));  // open: QA
  Button _5_2 (.out(_5_2_out));
  Button _7_2 (.out(_7_2_out));
  Button _4_2 (.out(_4_2_out));
  Button _6_2 (.out(_6_2_out));
  Multiplexer #(.select(3), .width(4)) multiplexer_1 (
    .in0(l1_32b_1_d_2), .in1(l1_32b_1_d_3), .in2(l1_32b_1_d_4), .in3(l1_32b_1_d_5), .in4(l1_32b_1_d_6),
    .in5(l1_32b_1_d_7), .in6(l1_32b_1_d_8), .in7(l1_32b_1_d_9), .out(multiplexer_1_out),
    .sel(l2_256b_1_out_r1_3));  // open: en
  Multiplexer #(.select(3), .width(4)) multiplexer_2 (
    .in0(l1_32b_1_d_2), .in1(l1_32b_1_d_3), .in2(l1_32b_1_d_4), .in3(l1_32b_1_d_5), .in4(l1_32b_1_d_6),
    .in5(l1_32b_1_d_7), .in6(l1_32b_1_d_8), .in7(l1_32b_1_d_9), .out(multiplexer_2_out),
    .sel(l2_256b_1_out_r2_3));  // open: en
  Button _1_3 (.out(_1_3_out));
  Button _2_3 (.out(_2_3_out));
  Button _0_3 (.out(_0_3_out));
  BCD8421 bcd8421_4 (
    ._0(_0_3_out), ._1(_1_3_out), ._2(_2_3_out), ._3(_3_3_out), ._4(_4_3_out), ._5(_5_3_out), ._6(_6_3_out),
    ._7(_7_3_out), ._8(1'b0), ._9(1'b0), .QB(bcd8421_4_qb), .QC(bcd8421_4_qc), .QD(bcd8421_4_qd));  // open: QA
  L2_256b l2_256b_1 (
    .R1_5(demux1_16_1_out_6), .R2_4(demux1_16_1_out_7), .R3(demux1_16_1_out_8), .R4(demux1_16_1_out_9),
    .R5(demux1_16_1_out_10), .R6(demux1_16_1_out_11), .R7(demux1_16_1_out_12), .R8(demux1_16_1_out_13),
    .R9(demux1_16_1_out_14), .R10(demux1_16_1_out_15), .R11(demux1_16_1_out_16), .R12(demux1_16_1_out_17),
    .R13(demux1_16_1_out_18), .R14(demux1_16_1_out_19), .R15(demux1_16_1_out_20), .R16(demux1_16_1_out_21),
    .DEST(bcd8421_1_qb), .DEST_2(bcd8421_1_qc), .DEST_3(bcd8421_1_qd), .OP(bcd8421_2_qb),
    .OP_2(bcd8421_2_qc), .OP_3(bcd8421_2_qd), .R1(bcd8421_3_qb), .R1_2(bcd8421_3_qc), .R1_3(bcd8421_3_qd),
    .R2(bcd8421_4_qb), .R2_2(bcd8421_4_qc), .R2_3(bcd8421_4_qd), .R1_4(bcdd8421_0_15_1_d[3]),
    .INPUT(bcdd8421_0_15_1_d[2]), .INPUT_2(bcdd8421_0_15_1_d[1]), .INPUT_3(bcdd8421_0_15_1_d[0]),
    .DEST_4(l2_256b_1_dest_4), .DEST_5(l2_256b_1_dest_5), .DEST_6(l2_256b_1_dest_6), .INS(l2_256b_1_ins),
    .INS_2(l2_256b_1_ins_2), .INS_3(l2_256b_1_ins_3), .OUT_R1(l2_256b_1_out_r1_3[2]),
    .OUT_R1_2(l2_256b_1_out_r1_3[1]), .OUT_R1_3(l2_256b_1_out_r1_3[0]), .OUT_R2(l2_256b_1_out_r2_3[2]),
    .OUT_R2_2(l2_256b_1_out_r2_3[1]), .OUT_R2_3(l2_256b_1_out_r2_3[0]), .OUT_INPUT(l2_256b_1_out_input_4[3]),
    .OUT_INPUT_2(l2_256b_1_out_input_4[2]), .OUT_INPUT_3(l2_256b_1_out_input_4[1]),
    .OUT_INPUT_4(l2_256b_1_out_input_4[0]), .SELECT(counter_1_q), .CLEAR(CLEAR_ALL_out));
  Button _4_3 (.out(_4_3_out));
  Button _3_3 (.out(_3_3_out));
  Button _5_3 (.out(_5_3_out));
  Button _6_3 (.out(_6_3_out));
  Counter #(.width(4), .max('hf)) counter_1 (.Q(counter_1_q), .clk(CLOCK_ALL_out));  // open: load, D, count, carry, clr
  Hex_Digit_Display hex_digit_display_9 (.value(multiplexer_1_out));  // open: dp
  Hex_Digit_Display hex_digit_display_10 (.value(multiplexer_2_out));  // open: dp
  Button _7_3 (.out(_7_3_out));
  Button _0_4 (.out(_0_4_out[0]));
  Button _1_4 (.out(_0_4_out[1]));
  Button _5_4 (.out(_0_4_out[5]));
  Button _4_4 (.out(_0_4_out[4]));
  Button _9 (.out(_0_4_out[9]));
  Button _8 (.out(_0_4_out[8]));
  Button _12 (.out(_0_4_out[12]));
  Button _13 (.out(_0_4_out[13]));
  ENTRYSLT entryslt_1 (
    .A0(multiplexer_1_out[0]), .A1(multiplexer_1_out[1]), .A2(multiplexer_1_out[2]),
    .A3(multiplexer_1_out[3]), .B0(l2_256b_1_out_input_4[0]), .B1(l2_256b_1_out_input_4[1]),
    .B2(l2_256b_1_out_input_4[2]), .B3(l2_256b_1_out_input_4[3]), .in_1(l2_256b_1_ins),
    .in_2(l2_256b_1_ins_2), .in_3(l2_256b_1_ins_3), .C0(entryslt_1_c0[0]), .C1(entryslt_1_c0[1]),
    .C2(entryslt_1_c0[2]), .C3(entryslt_1_c0[3]));
  DULLENTRY dullentry_1 (
    .B0(multiplexer_2_out[0]), .B1(multiplexer_2_out[1]), .B2(multiplexer_2_out[2]),
    .B3(multiplexer_2_out[3]), .in_1(l2_256b_1_ins), .in_2(l2_256b_1_ins_2), .in_3(l2_256b_1_ins_3),
    .B0_2(dullentry_1_b0_2[0]), .B1_2(dullentry_1_b0_2[1]), .B2_2(dullentry_1_b0_2[2]),
    .B3_2(dullentry_1_b0_2[3]));
  BCDD8421_0_15 bcdd8421_0_15_1 (
    ._0(_0_4_out[0]), ._1(_0_4_out[1]), ._2(_0_4_out[2]), ._3(_0_4_out[3]), ._4(_0_4_out[4]),
    ._5(_0_4_out[5]), ._6(_0_4_out[6]), ._7(_0_4_out[7]), ._8(_0_4_out[8]), ._9(_0_4_out[9]),
    ._10(_0_4_out[10]), ._11(_0_4_out[11]), ._12(_0_4_out[12]), ._13(_0_4_out[13]), ._14(_0_4_out[14]),
    ._15(_0_4_out[15]), .A(bcdd8421_0_15_1_d[3]), .B(bcdd8421_0_15_1_d[2]), .C(bcdd8421_0_15_1_d[1]),
    .D(bcdd8421_0_15_1_d[0]));
  Button _2_4 (.out(_0_4_out[2]));
  Button _3_4 (.out(_0_4_out[3]));
  Button _7_4 (.out(_0_4_out[7]));
  Button _6_4 (.out(_0_4_out[6]));
  Button _10 (.out(_0_4_out[10]));
  Button _11 (.out(_0_4_out[11]));
  Button _15 (.out(_0_4_out[15]));
  Button _14 (.out(_0_4_out[14]));
  Hex_Digit_Display hex_digit_display_11 (.value(bcdd8421_0_15_1_d));  // open: dp
  ULA ula_1 (
    .D0(entryslt_1_c0[0]), .C0(entryslt_1_c0[1]), .B0(entryslt_1_c0[2]), .A0(entryslt_1_c0[3]),
    .D1(dullentry_1_b0_2[0]), .C1(dullentry_1_b0_2[1]), .B1(dullentry_1_b0_2[2]), .A1(dullentry_1_b0_2[3]),
    .in_1(l2_256b_1_ins), .in_2(l2_256b_1_ins_2), .in_3(l2_256b_1_ins_3), .D(ula_1_d), .C(ula_1_c),
    .B(ula_1_b), .A(ula_1_a));
  Button CLEAR_ALL (.out(CLEAR_ALL_out));
  Clock CLOCK_ALL (.out(CLOCK_ALL_out));

  // Notes on the sheet:
  //   Instruction:
  //   16bits
  //   Example:
  //   DEST+OP+R1+R2+INPUT
  //   (3B)+(3B)+(3B)+(3B)+(4B)
  //   000 110 000 000 0101
  //   001 110 000 000 0011
  //   010 100 000 001 0000 
  //   DEST (L1)
  //   OPERATION
  //   R1(L1)
  //   R2(L1)
  //   INPUT
  //   INPUT
endmodule

// +
module ADDER1B (
  input  Te,
  input  A,
  input  B,
  output S,
  output Ts
);

  wire and_1_out, and_2_out, and_3_out, xor_1_out;

  xor xor_1 (xor_1_out, A, B);
  and and_1 (and_1_out, B, A);
  and and_2 (and_2_out, Te, B);
  and and_3 (and_3_out, A, Te);
  xor xor_2 (S, xor_1_out, Te);
  or or_1 (Ts, and_1_out, and_2_out, and_3_out);
endmodule

module ADDER4B (
  input  D0,
  input  D1,
  input  C0,
  input  C1,
  input  B0,
  input  B1,
  input  A0,
  input  A1,
  output D,
  output C,
  output B,
  output A,
  output Ovf
);

  wire adder1b_1_ts, adder1b_2_ts, adder1b_3_ts;

  ADDER1B adder1b_1 (.Te(1'b0), .A(D0), .B(D1), .S(D), .Ts(adder1b_1_ts));
  ADDER1B adder1b_2 (.Te(adder1b_1_ts), .A(C0), .B(C1), .S(C), .Ts(adder1b_2_ts));
  ADDER1B adder1b_3 (.Te(adder1b_2_ts), .A(B0), .B(B1), .S(B), .Ts(adder1b_3_ts));
  ADDER1B adder1b_4 (.Te(adder1b_3_ts), .A(A0), .B(A1), .S(A), .Ts(Ovf));
endmodule

module AND4b (
  input  D0,
  input  D1,
  input  C0,
  input  C1,
  input  B0,
  input  B1,
  input  A0,
  input  A1,
  output D,
  output C,
  output B,
  output A
);

  and and_1 (D, D0, D1);
  and and_2 (C, C0, C1);
  and and_3 (B, B0, B1);
  and and_4 (A, A0, A1);
endmodule

// MUX 32:4
module MUX32_4 (
  input  in_1,
  input  in_2,
  input  in_3,
  input  D,
  input  C,
  input  B,
  input  A,
  input  D_2,
  input  C_2,
  input  B_2,
  input  A_2,
  input  D_3,
  input  C_3,
  input  B_3,
  input  A_3,
  input  D_4,
  input  C_4,
  input  B_4,
  input  A_4,
  input  D_5,
  input  C_5,
  input  B_5,
  input  A_5,
  input  D_6,
  input  C_6,
  input  B_6,
  input  A_6,
  input  D_7,
  input  C_7,
  input  B_7,
  input  A_7,
  input  D_8,
  input  C_8,
  input  B_8,
  input  A_8,
  output D_9,
  output C_9,
  output B_9,
  output A_9
);

  wire _0_out, _1_out, _2_out, _3_out, _4_out, _5_out, _6_out, _7_out, _8_out, _9_out, _10_out, _11_out,
       _12_out, _13_out, _14_out, _15_out, _16_out, _17_out, _18_out, _19_out, _20_out, _21_out, _22_out,
       _23_out, _24_out, _25_out, _26_out, _27_out, _28_out, _29_out, _30_out, _31_out, and_1_out, and_2_out,
       and_3_out, and_4_out, and_5_out, and_6_out, and_7_out, and_8_out, not_1_out, not_2_out, not_3_out,
       or_1_out, or_2_out, or_3_out, or_4_out, or_5_out, or_6_out, or_7_out, or_8_out;

  not not_1 (not_1_out, in_2);
  not not_2 (not_2_out, in_3);
  and _0 (_0_out, D, not_1_out, not_2_out);
  and _1 (_1_out, D_2, not_1_out, in_3);
  and _2 (_2_out, D_3, in_2, not_2_out);
  and _3 (_3_out, D_4, in_2, in_3);
  and _4 (_4_out, D_5, not_1_out, not_2_out);
  and _5 (_5_out, D_6, not_1_out, in_3);
  and _6 (_6_out, D_7, in_2, not_2_out);
  and _7 (_7_out, D_8, in_2, in_3);
  and _8 (_8_out, C, not_1_out, not_2_out);
  and _9 (_9_out, C_2, not_1_out, in_3);
  and _10 (_10_out, C_3, in_2, not_2_out);
  and _11 (_11_out, C_4, in_2, in_3);
  and _12 (_12_out, C_5, not_1_out, not_2_out);
  and _13 (_13_out, C_6, not_1_out, in_3);
  and _14 (_14_out, C_7, in_2, not_2_out);
  and _15 (_15_out, C_8, C_8, in_2, in_3);
  and _16 (_16_out, B, not_1_out, not_2_out);
  and _17 (_17_out, B_2, not_1_out, in_3);
  and _18 (_18_out, B_3, in_2, not_2_out);
  and _19 (_19_out, B_4, in_2, in_3);
  and _20 (_20_out, B_5, not_1_out, not_2_out);
  and _21 (_21_out, B_6, not_1_out, in_3);
  and _22 (_22_out, B_7, in_2, not_2_out);
  and _23 (_23_out, B_8, in_2, in_3);
  and _24 (_24_out, A, not_1_out, not_2_out);
  and _25 (_25_out, A_2, not_1_out, in_3);
  and _26 (_26_out, A_3, in_2, not_2_out);
  and _27 (_27_out, A_4, in_2, in_3);
  and _28 (_28_out, A_5, not_1_out, not_2_out);
  and _29 (_29_out, A_6, not_1_out, in_3);
  and _30 (_30_out, A_7, in_2, not_2_out);
  and _31 (_31_out, A_8, in_2, in_3);
  or or_1 (or_1_out, _0_out, _1_out, _2_out, _3_out);
  or or_2 (or_2_out, _4_out, _5_out, _6_out, _7_out);
  or or_3 (or_3_out, _8_out, _9_out, _10_out, _11_out);
  or or_4 (or_4_out, _12_out, _13_out, _14_out, _15_out);
  or or_5 (or_5_out, _16_out, _17_out, _18_out, _19_out);
  or or_6 (or_6_out, _20_out, _21_out, _22_out, _23_out);
  or or_7 (or_7_out, _24_out, _25_out, _26_out, _27_out);
  or or_8 (or_8_out, _28_out, _29_out, _30_out, _31_out);
  not not_3 (not_3_out, in_1);
  and and_1 (and_1_out, or_1_out, not_3_out);
  and and_2 (and_2_out, or_2_out, in_1);
  and and_3 (and_3_out, or_3_out, not_3_out);
  and and_4 (and_4_out, or_4_out, in_1);
  and and_5 (and_5_out, or_5_out, not_3_out);
  and and_6 (and_6_out, or_6_out, in_1);
  and and_7 (and_7_out, or_7_out, not_3_out);
  and and_8 (and_8_out, or_8_out, in_1);
  or or_9 (D_9, and_1_out, and_2_out);
  or or_10 (C_9, and_3_out, and_4_out);
  or or_11 (B_9, and_5_out, and_6_out);
  or or_12 (A_9, and_7_out, and_8_out);
endmodule

// OR 4b
module OR4b (
  input  D0,
  input  D1,
  input  C0,
  input  C1,
  input  B0,
  input  B1,
  input  A0,
  input  A1,
  output D,
  output C,
  output B,
  output A
);

  or or_1 (D, D0, D1);
  or or_2 (C, C0, C1);
  or or_3 (B, B0, B1);
  or or_4 (A, A0, A1);
endmodule

// NAND 4B
module NAND4b (
  input  D0,
  input  D1,
  input  C0,
  input  C1,
  input  B0,
  input  B1,
  input  A0,
  input  A1,
  output out_9,
  output out_10,
  output out_11,
  output out_12
);

  nand nand_1 (out_9, D0, D1);
  nand nand_2 (out_10, C0, C1);
  nand nand_3 (out_11, B0, B1);
  nand nand_4 (out_12, A0, A1);
endmodule

// XOR 4B
module XOR4b (
  input  D0,
  input  D1,
  input  C0,
  input  C1,
  input  B0,
  input  B1,
  input  A0,
  input  A1,
  output D,
  output C,
  output B,
  output A
);

  xor xor_1 (D, D0, D1);
  xor xor_2 (C, C0, C1);
  xor xor_3 (B, B0, B1);
  xor xor_4 (A, A0, A1);
endmodule

// SLT 4B
module SLT4b (
  input  D0,
  input  D1,
  input  C0,
  input  C1,
  input  B0,
  input  B1,
  input  A0,
  input  A1,
  output out_9,
  output out_10,
  output out_11,
  output out_12
);

  SUBTRACTOR4B subtractor4b_1 (
    .D0(D0), .D1(D1), .C0(C0), .C1(C1), .B0(B0), .B1(B1), .A0(A0), .A1(A1), .Overflow(out_9));  // open: out_9, out_10, out_11, out_12

  assign out_10 = 1'b0;
  assign out_11 = 1'b0;
  assign out_12 = 1'b0;
endmodule

// -
module SUBTRACTOR1B (
  input  in_1,
  input  in_2,
  input  in_3,
  output out_4,
  output out_5
);

  wire and_1_out, and_2_out, and_3_out, not_1_out, xor_1_out;

  not not_1 (not_1_out, in_2);
  xor xor_1 (xor_1_out, in_2, in_3);
  and and_1 (and_1_out, not_1_out, in_3);
  and and_2 (and_2_out, not_1_out, in_1);
  and and_3 (and_3_out, in_3, in_1);
  xor xor_2 (out_4, xor_1_out, in_1);
  or or_1 (out_5, and_1_out, and_2_out, and_3_out);
endmodule

// subtrador 4B
module SUBTRACTOR4B (
  input  D0,
  input  D1,
  input  C0,
  input  C1,
  input  B0,
  input  B1,
  input  A0,
  input  A1,
  output out_9,
  output out_10,
  output out_11,
  output out_12,
  output Overflow
);

  wire subtractor1b_1_out_5, subtractor1b_2_out_5, subtractor1b_3_out_5;

  SUBTRACTOR1B subtractor1b_1 (.in_1(1'b0), .in_2(D0), .in_3(D1), .out_4(out_9), .out_5(subtractor1b_1_out_5));
  SUBTRACTOR1B subtractor1b_2 (
    .in_1(subtractor1b_1_out_5), .in_2(C0), .in_3(C1), .out_4(out_10), .out_5(subtractor1b_2_out_5));
  SUBTRACTOR1B subtractor1b_3 (
    .in_1(subtractor1b_2_out_5), .in_2(B0), .in_3(B1), .out_4(out_11), .out_5(subtractor1b_3_out_5));
  SUBTRACTOR1B subtractor1b_4 (.in_1(subtractor1b_3_out_5), .in_2(A0), .in_3(A1), .out_4(out_12), .out_5(Overflow));
endmodule

// FFD
module Flip_Flop_D (
  input  D,
  input  CLK,
  input  CLEAR,
  output Q,
  output Q_prime
);

  D_Flip_Flop d_ff_1 (.clk(CLK), .D(D), .Q(Q_prime), .Qn(Q), .reset(CLEAR));  // open: preset, en
endmodule

module L1_RG4B (
  input  DA,
  input  DB,
  input  DC,
  input  DD,
  input  CLOCK,
  input  CLEAR,
  output QA,
  output QB,
  output QC,
  output QD
);

  D_Flip_Flop #(.trigger("high")) d_ff_1 (.clk(CLOCK), .D(DA), .Q(QA), .reset(CLEAR));  // open: Qn, preset, en
  D_Flip_Flop #(.trigger("high")) d_ff_2 (.clk(CLOCK), .D(DB), .Q(QB), .reset(CLEAR));  // open: Qn, preset, en
  D_Flip_Flop #(.trigger("high")) d_ff_3 (.clk(CLOCK), .D(DC), .Q(QC), .reset(CLEAR));  // open: Qn, preset, en
  D_Flip_Flop #(.trigger("high")) d_ff_4 (.clk(CLOCK), .D(DD), .Q(QD), .reset(CLEAR));  // open: Qn, preset, en
endmodule

// ULA 4B
module ULA (
  input  in_1,
  input  in_2,
  input  in_3,
  input  D0,
  input  C0,
  input  B0,
  input  A0,
  input  D1,
  input  C1,
  input  B1,
  input  A1,
  output D,
  output C,
  output B,
  output A
);

  wire adder4b_1_a, adder4b_1_b, adder4b_1_c, adder4b_1_d, adder4b_2_a, adder4b_2_b, adder4b_2_c,
       adder4b_2_d, and4b_1_a, and4b_1_b, and4b_1_c, and4b_1_d, nand4b_1_out_9, nand4b_1_out_10,
       nand4b_1_out_11, nand4b_1_out_12, or4b_1_a, or4b_1_b, or4b_1_c, or4b_1_d, slt4b_1_out_9,
       slt4b_1_out_10, slt4b_1_out_11, slt4b_1_out_12, subtractor4b_1_out_9, subtractor4b_1_out_10,
       subtractor4b_1_out_11, subtractor4b_1_out_12, xor4b_1_a, xor4b_1_b, xor4b_1_c, xor4b_1_d;

  AND4b and4b_1 (
    .D0(D0), .D1(D1), .C0(C0), .C1(C1), .B0(B0), .B1(B1), .A0(A0), .A1(A1), .D(and4b_1_d), .C(and4b_1_c),
    .B(and4b_1_b), .A(and4b_1_a));
  OR4b or4b_1 (
    .D0(D0), .D1(D1), .C0(C0), .C1(C1), .B0(B0), .B1(B1), .A0(A0), .A1(A1), .D(or4b_1_d), .C(or4b_1_c),
    .B(or4b_1_b), .A(or4b_1_a));
  NAND4b nand4b_1 (
    .D0(D0), .D1(D1), .C0(C0), .C1(C1), .B0(B0), .B1(B1), .A0(A0), .A1(A1), .out_9(nand4b_1_out_9),
    .out_10(nand4b_1_out_10), .out_11(nand4b_1_out_11), .out_12(nand4b_1_out_12));
  XOR4b xor4b_1 (
    .D0(D0), .D1(D1), .C0(C0), .C1(C1), .B0(B0), .B1(B1), .A0(A0), .A1(A1), .D(xor4b_1_d), .C(xor4b_1_c),
    .B(xor4b_1_b), .A(xor4b_1_a));
  ADDER4B adder4b_1 (
    .D0(D0), .D1(D1), .C0(C0), .C1(C1), .B0(B0), .B1(B1), .A0(A0), .A1(A1), .D(adder4b_1_d), .C(adder4b_1_c),
    .B(adder4b_1_b), .A(adder4b_1_a));  // open: Ovf
  SUBTRACTOR4B subtractor4b_1 (
    .D0(D0), .D1(D1), .C0(C0), .C1(C1), .B0(B0), .B1(B1), .A0(A0), .A1(A1), .out_9(subtractor4b_1_out_9),
    .out_10(subtractor4b_1_out_10), .out_11(subtractor4b_1_out_11), .out_12(subtractor4b_1_out_12));  // open: Overflow
  ADDER4B adder4b_2 (
    .D0(D0), .D1(D1), .C0(C0), .C1(C1), .B0(B0), .B1(B1), .A0(A0), .A1(A1), .D(adder4b_2_d), .C(adder4b_2_c),
    .B(adder4b_2_b), .A(adder4b_2_a));  // open: Ovf
  SLT4b slt4b_1 (
    .D0(D0), .D1(D1), .C0(C0), .C1(C1), .B0(B0), .B1(B1), .A0(A0), .A1(A1), .out_9(slt4b_1_out_9),
    .out_10(slt4b_1_out_10), .out_11(slt4b_1_out_11), .out_12(slt4b_1_out_12));
  MUX32_4 mux32_4_1 (
    .D(and4b_1_d), .C(and4b_1_c), .B(and4b_1_b), .A(and4b_1_a), .D_2(or4b_1_d), .C_2(or4b_1_c),
    .B_2(or4b_1_b), .A_2(or4b_1_a), .D_3(nand4b_1_out_9), .C_3(nand4b_1_out_10), .B_3(nand4b_1_out_11),
    .A_3(nand4b_1_out_12), .D_4(xor4b_1_d), .C_4(xor4b_1_c), .B_4(xor4b_1_b), .A_4(xor4b_1_a),
    .D_5(adder4b_1_d), .C_5(adder4b_1_c), .B_5(adder4b_1_b), .A_5(adder4b_1_a), .D_6(subtractor4b_1_out_9),
    .C_6(subtractor4b_1_out_10), .B_6(subtractor4b_1_out_11), .A_6(subtractor4b_1_out_12), .D_7(adder4b_2_d),
    .C_7(adder4b_2_c), .B_7(adder4b_2_b), .A_7(adder4b_2_a), .D_8(slt4b_1_out_9), .C_8(slt4b_1_out_10),
    .B_8(slt4b_1_out_11), .A_8(slt4b_1_out_12), .in_1(in_1), .in_2(in_2), .in_3(in_3), .D_9(D), .C_9(C),
    .B_9(B), .A_9(A));
endmodule

// L1 32 BITS
module L1_32b (
  input  A,
  input  B,
  input  C,
  input  D,
  input  R0,
  input  R1,
  input  R2,
  input  R3,
  input  R4,
  input  R5,
  input  R6,
  input  R7,
  input  CLEAR,
  output D_2,
  output C_2,
  output B_2,
  output A_2,
  output D_3,
  output C_3,
  output B_3,
  output A_3,
  output D_4,
  output C_4,
  output B_4,
  output A_4,
  output D_5,
  output C_5,
  output B_5,
  output A_5,
  output D_6,
  output C_6,
  output B_6,
  output A_6,
  output D_7,
  output C_7,
  output B_7,
  output A_7,
  output D_8,
  output C_8,
  output B_8,
  output A_8,
  output D_9,
  output C_9,
  output B_9,
  output A_9
);

  L1_RG4B l1_rg4b_1 (.CLOCK(R0), .DA(A), .DB(B), .DC(C), .DD(D), .QA(A_2), .QB(B_2), .QC(C_2), .QD(D_2), .CLEAR(CLEAR));
  L1_RG4B l1_rg4b_2 (.CLOCK(R1), .DA(A), .DB(B), .DC(C), .DD(D), .QA(A_3), .QB(B_3), .QC(C_3), .QD(D_3), .CLEAR(CLEAR));
  L1_RG4B l1_rg4b_3 (.CLOCK(R2), .DA(A), .DB(B), .DC(C), .DD(D), .QA(A_4), .QB(B_4), .QC(C_4), .QD(D_4), .CLEAR(CLEAR));
  L1_RG4B l1_rg4b_4 (.CLOCK(R3), .DA(A), .DB(B), .DC(C), .DD(D), .QA(A_5), .QB(B_5), .QC(C_5), .QD(D_5), .CLEAR(CLEAR));
  L1_RG4B l1_rg4b_5 (.CLOCK(R4), .DA(A), .DB(B), .DC(C), .DD(D), .QA(A_6), .QB(B_6), .QC(C_6), .QD(D_6), .CLEAR(CLEAR));
  L1_RG4B l1_rg4b_6 (.CLOCK(R5), .DA(A), .DB(B), .DC(C), .DD(D), .QA(A_7), .QB(B_7), .QC(C_7), .QD(D_7), .CLEAR(CLEAR));
  L1_RG4B l1_rg4b_7 (.CLOCK(R6), .DA(A), .DB(B), .DC(C), .DD(D), .QA(A_8), .QB(B_8), .QC(C_8), .QD(D_8), .CLEAR(CLEAR));
  L1_RG4B l1_rg4b_8 (.CLOCK(R7), .DA(A), .DB(B), .DC(C), .DD(D), .QA(A_9), .QB(B_9), .QC(C_9), .QD(D_9), .CLEAR(CLEAR));
endmodule

module DMUX1_8 (
  input  in_1,
  input  in_2,
  input  in_3,
  input  E,
  output S0,
  output S1,
  output S2,
  output S3,
  output S4,
  output S5,
  output S6,
  output S7
);

  wire not_1_out, not_2_out, not_3_out, not_4_out, not_5_out, not_6_out, not_7_out, not_8_out, not_9_out,
       not_10_out, not_11_out, not_12_out;

  not not_1 (not_1_out, in_1);
  not not_2 (not_2_out, in_2);
  not not_3 (not_3_out, in_3);
  not not_4 (not_4_out, in_1);
  not not_5 (not_5_out, in_2);
  not not_6 (not_6_out, in_1);
  not not_7 (not_7_out, in_3);
  not not_8 (not_8_out, in_1);
  not not_9 (not_9_out, in_2);
  not not_10 (not_10_out, in_3);
  not not_11 (not_11_out, in_2);
  not not_12 (not_12_out, in_3);
  and and_1 (S0, not_1_out, not_2_out, not_3_out, E);
  and and_2 (S1, not_4_out, not_5_out, in_3, E);
  and and_3 (S2, not_6_out, in_2, not_7_out, E);
  and and_4 (S3, not_8_out, in_2, in_3, E);
  and and_5 (S4, in_1, not_9_out, not_10_out, E);
  and and_6 (S5, in_1, not_11_out, in_3, E);
  and and_7 (S6, in_1, in_2, not_12_out, E);
  and and_8 (S7, in_1, in_2, in_3, E);
endmodule

module BCD8421 (
  input  _0,
  input  _1,
  input  _2,
  input  _3,
  input  _4,
  input  _5,
  input  _6,
  input  _7,
  input  _8,
  input  _9,
  output QA,
  output QB,
  output QC,
  output QD
);

  wire nand_1_out, nand_2_out, nand_3_out, nand_4_out, not_1_out, not_2_out, not_3_out, not_4_out, not_5_out,
       not_6_out, not_7_out, not_8_out, not_9_out, or_1_out;

  or or_1 (or_1_out, _9, _8, _7, _6, _5, _4, _3, _2, _1, _0);
  not not_1 (not_1_out, _2);
  not not_2 (not_2_out, _1);
  not not_3 (not_3_out, _3);
  not not_4 (not_4_out, _4);
  L1_RG4B l1_rg4b_1 (
    .CLOCK(or_1_out), .DA(nand_4_out), .DB(nand_3_out), .DC(nand_2_out), .DD(nand_1_out), .QA(QA), .QB(QB),
    .QC(QC), .QD(QD));  // open: CLEAR
  not not_5 (not_5_out, _5);
  not not_6 (not_6_out, _6);
  not not_7 (not_7_out, _8);
  not not_8 (not_8_out, _7);
  not not_9 (not_9_out, _9);
  nand nand_1 (nand_1_out, not_2_out, not_3_out, not_5_out, not_8_out, not_9_out);
  nand nand_2 (nand_2_out, not_1_out, not_3_out, not_6_out, not_8_out);
  nand nand_3 (nand_3_out, not_4_out, not_5_out, not_6_out, not_8_out);
  nand nand_4 (nand_4_out, not_7_out, not_9_out);
endmodule

module Keyboards (
);

  wire _0_2_out, _1_2_out, _2_2_out, _3_2_out, _4_2_out, _5_2_out, _6_2_out, _7_2_out, bcd8421_1_qb,
       bcd8421_1_qc, bcd8421_1_qd, bcd8421_2_qa, bcd8421_2_qb, bcd8421_2_qc, bcd8421_2_qd, bcdd8421_0_15_1_a,
       bcdd8421_0_15_1_b, bcdd8421_0_15_1_c, bcdd8421_0_15_1_d, button_2_out, button_3_out, button_4_out,
       button_5_out, button_6_out, button_7_out, button_out, s_out;
  wire [3:0] bcdd8421_0_15_2_d;
  wire [15:0] _0_3_out, _0_out;

  Button _1 (.out(_0_out[1]));
  Button _0 (.out(_0_out[0]));
  Button _4 (.out(_0_out[4]));
  Button _5 (.out(_0_out[5]));
  Button _8 (.out(_0_out[8]));
  Button _9 (.out(_0_out[9]));
  Button _12 (.out(_0_out[12]));
  Button _13 (.out(_0_out[13]));
  BCDD8421_0_15 bcdd8421_0_15_1 (
    ._0(_0_out[0]), ._1(_0_out[1]), ._2(_0_out[2]), ._3(_0_out[3]), ._4(_0_out[4]), ._5(_0_out[5]),
    ._6(_0_out[6]), ._7(_0_out[7]), ._8(_0_out[8]), ._9(_0_out[9]), ._10(_0_out[10]), ._11(_0_out[11]),
    ._12(_0_out[12]), ._13(_0_out[13]), ._14(_0_out[14]), ._15(_0_out[15]), .A(bcdd8421_0_15_1_a),
    .B(bcdd8421_0_15_1_b), .C(bcdd8421_0_15_1_c), .D(bcdd8421_0_15_1_d));
  Button _2 (.out(_0_out[2]));
  Button _3 (.out(_0_out[3]));
  Button _7 (.out(_0_out[7]));
  Button _6 (.out(_0_out[6]));
  Button _10 (.out(_0_out[10]));
  Button _11 (.out(_0_out[11]));
  Button _15 (.out(_0_out[15]));
  Button _14 (.out(_0_out[14]));
  Button _1_2 (.out(_1_2_out));
  Button _0_2 (.out(_0_2_out));
  BCD8421 bcd8421_1 (
    ._0(_0_2_out), ._1(_1_2_out), ._2(_2_2_out), ._3(_3_2_out), ._4(_4_2_out), ._5(_5_2_out), ._6(_6_2_out),
    ._7(_7_2_out), ._8(1'b0), ._9(1'b0), .QB(bcd8421_1_qb), .QC(bcd8421_1_qc), .QD(bcd8421_1_qd));  // open: QA
  Button _2_2 (.out(_2_2_out));
  Button _4_2 (.out(_4_2_out));
  Button _5_2 (.out(_5_2_out));
  Button _3_2 (.out(_3_2_out));
  Button _0_3 (.out(_0_3_out[0]));
  Button _4_3 (.out(_0_3_out[4]));
  Button _8_2 (.out(_0_3_out[8]));
  Button _12_2 (.out(_0_3_out[12]));
  Button _6_2 (.out(_6_2_out));
  Button _7_2 (.out(_7_2_out));
  BCDD8421_0_15 bcdd8421_0_15_2 (
    ._0(_0_3_out[0]), ._1(_0_3_out[1]), ._2(_0_3_out[2]), ._3(_0_3_out[3]), ._4(_0_3_out[4]),
    ._5(_0_3_out[5]), ._6(_0_3_out[6]), ._7(_0_3_out[7]), ._8(_0_3_out[8]), ._9(_0_3_out[9]),
    ._10(_0_3_out[10]), ._11(_0_3_out[11]), ._12(_0_3_out[12]), ._13(_0_3_out[13]), ._14(_0_3_out[14]),
    ._15(_0_3_out[15]), .A(bcdd8421_0_15_2_d[3]), .B(bcdd8421_0_15_2_d[2]), .C(bcdd8421_0_15_2_d[1]),
    .D(bcdd8421_0_15_2_d[0]));
  Button _2_3 (.out(_0_3_out[2]));
  Button _3_3 (.out(_0_3_out[3]));
  Button _1_3 (.out(_0_3_out[1]));
  Button _6_3 (.out(_0_3_out[6]));
  Button _7_3 (.out(_0_3_out[7]));
  Button _5_3 (.out(_0_3_out[5]));
  Button _10_2 (.out(_0_3_out[10]));
  Button _11_2 (.out(_0_3_out[11]));
  Button _9_2 (.out(_0_3_out[9]));
  Button _13_2 (.out(_0_3_out[13]));
  Button _15_2 (.out(_0_3_out[15]));
  Button _14_2 (.out(_0_3_out[14]));
  Button button (.out(button_out));
  Button button_2 (.out(button_2_out));
  BCD8421 bcd8421_2 (
    ._0(button_out), ._1(button_3_out), ._2(button_4_out), ._3(button_5_out), ._4(button_2_out),
    ._5(button_7_out), ._6(button_6_out), ._7(s_out), ._8(1'b0), ._9(1'b0), .QA(bcd8421_2_qa),
    .QB(bcd8421_2_qb), .QC(bcd8421_2_qc), .QD(bcd8421_2_qd));
  Hex_Digit_Display hex_digit_display_1 (.value(bcdd8421_0_15_2_d));  // open: dp
  Button button_3 (.out(button_3_out));
  Button button_4 (.out(button_4_out));
  Button button_5 (.out(button_5_out));
  Button button_6 (.out(button_6_out));
  Button button_7 (.out(button_7_out));
  Button s (.out(s_out));

  // Notes on the sheet:
  //   INPUT
  //   INPUT
endmodule

module Demux1_16 (
  input  in_1,
  input  in_2,
  input  in_3,
  input  in_4,
  input  in_5,
  output out_6,
  output out_7,
  output out_8,
  output out_9,
  output out_10,
  output out_11,
  output out_12,
  output out_13,
  output out_14,
  output out_15,
  output out_16,
  output out_17,
  output out_18,
  output out_19,
  output out_20,
  output out_21
);

  and and_1 (out_6, ~in_1, ~in_2, ~in_3, ~in_4, in_5);  // AND_Gate
  and and_2 (out_7, ~in_1, ~in_2, ~in_3, in_4, in_5);  // AND_Gate
  and and_3 (out_8, ~in_1, ~in_2, in_3, ~in_4, in_5);  // AND_Gate
  and and_4 (out_9, ~in_1, ~in_2, in_3, in_4, in_5);  // AND_Gate
  and and_5 (out_10, ~in_1, in_2, ~in_3, ~in_4, in_5);  // AND_Gate
  and and_6 (out_11, ~in_1, in_2, ~in_3, in_4, in_5);  // AND_Gate
  and and_7 (out_12, ~in_1, in_2, in_3, ~in_4, in_5);  // AND_Gate
  and and_8 (out_13, ~in_1, in_2, in_3, in_4, in_5);  // AND_Gate
  and and_9 (out_14, in_1, ~in_2, ~in_3, ~in_4, in_5);  // AND_Gate
  and and_10 (out_15, in_1, ~in_2, ~in_3, in_4, in_5);  // AND_Gate
  and and_11 (out_16, in_1, ~in_2, in_3, ~in_4, in_5);  // AND_Gate
  and and_12 (out_17, in_1, ~in_2, in_3, in_4, in_5);  // AND_Gate
  and and_13 (out_18, in_1, in_2, ~in_3, ~in_4, in_5);  // AND_Gate
  and and_14 (out_19, in_1, in_2, ~in_3, in_4, in_5);  // AND_Gate
  and and_15 (out_20, in_1, in_2, in_3, ~in_4, in_5);  // AND_Gate
  and and_16 (out_21, in_1, in_2, in_3, in_4, in_5);
endmodule

module BCDD8421_0_15 (
  input  _0,
  input  _1,
  input  _2,
  input  _3,
  input  _4,
  input  _5,
  input  _6,
  input  _7,
  input  _8,
  input  _9,
  input  _10,
  input  _11,
  input  _12,
  input  _13,
  input  _14,
  input  _15,
  output A,
  output B,
  output C,
  output D
);

  wire nand_1_out, nand_2_out, nand_3_out, nand_4_out, not_1_out, not_2_out, not_3_out, not_4_out, not_5_out,
       not_6_out, not_7_out, not_8_out, not_9_out, not_10_out, not_11_out, not_12_out, not_13_out,
       not_14_out, not_15_out, or_1_out;

  or or_1 (or_1_out, _15, _14, _13, _12, _11, _10, _9, _8, _7, _6, _5, _4, _3, _2, _1, _0);
  not not_1 (not_1_out, _2);
  not not_2 (not_2_out, _1);
  L1_RG4B l1_rg4b_1 (
    .CLOCK(or_1_out), .DA(nand_4_out), .DB(nand_3_out), .DC(nand_2_out), .DD(nand_1_out), .QA(A), .QB(B),
    .QC(C), .QD(D));  // open: CLEAR
  not not_3 (not_3_out, _4);
  not not_4 (not_4_out, _3);
  not not_5 (not_5_out, _6);
  not not_6 (not_6_out, _5);
  not not_7 (not_7_out, _7);
  not not_8 (not_8_out, _8);
  not not_9 (not_9_out, _9);
  not not_10 (not_10_out, _10);
  not not_11 (not_11_out, _11);
  not not_12 (not_12_out, _12);
  not not_13 (not_13_out, _14);
  not not_14 (not_14_out, _13);
  not not_15 (not_15_out, _15);
  nand nand_1 (nand_1_out, not_15_out, not_14_out, not_11_out, not_9_out, not_7_out, not_6_out, not_4_out, not_2_out);
  nand nand_2 (nand_2_out, not_15_out, not_13_out, not_11_out, not_10_out, not_7_out, not_5_out, not_4_out, not_1_out);
  nand nand_3 (nand_3_out, not_15_out, not_13_out, not_14_out, not_12_out, not_7_out, not_5_out, not_6_out, not_3_out);
  nand nand_4 (nand_4_out, not_15_out, not_13_out, not_14_out, not_12_out, not_11_out, not_10_out, not_9_out, not_8_out);
endmodule

module DULLENTRY (
  input  in_1,
  input  in_2,
  input  in_3,
  input  B0,
  input  B1,
  input  B2,
  input  B3,
  output B0_2,
  output B1_2,
  output B2_2,
  output B3_2
);

  wire and_1_out, not_1_out;

  not not_1 (not_1_out, in_3);
  Multiplexer #(.width(4)) multiplexer_1 (
    .in0({B3, B2, B1, B0}), .in1(4'b0000), .out({B3_2, B2_2, B1_2, B0_2}), .sel(and_1_out));  // open: en
  and and_1 (and_1_out, not_1_out, in_2, in_1);
endmodule

module ENTRYSLT (
  input  in_1,
  input  in_2,
  input  in_3,
  input  A0,
  input  A1,
  input  A2,
  input  A3,
  input  B0,
  input  B1,
  input  B2,
  input  B3,
  output C0,
  output C1,
  output C2,
  output C3
);

  wire and_1_out, not_1_out;

  not not_1 (not_1_out, in_3);
  Multiplexer #(.width(4)) multiplexer_1 (
    .in0({A3, A2, A1, A0}), .in1({B3, B2, B1, B0}), .out({C3, C2, C1, C0}), .sel(and_1_out));  // open: en
  and and_1 (and_1_out, not_1_out, in_2, in_1);
endmodule

module L2_RG16b (
  input  in_1,
  input  in_2,
  input  in_3,
  input  in_4,
  input  in_5,
  input  in_6,
  input  in_7,
  input  in_8,
  input  in_9,
  input  in_10,
  input  in_11,
  input  in_12,
  input  in_13,
  input  in_14,
  input  in_15,
  input  in_16,
  input  CLOCK,
  input  CLEAR,
  output out_19,
  output out_20,
  output out_21,
  output out_22,
  output out_23,
  output out_24,
  output out_25,
  output out_26,
  output out_27,
  output out_28,
  output out_29,
  output out_30,
  output out_31,
  output out_32,
  output out_33,
  output out_34
);

  Flip_Flop_D flip_flop_d_1 (.D(in_1), .CLK(CLOCK), .CLEAR(CLEAR), .Q_prime(out_20));  // open: Q
  Flip_Flop_D flip_flop_d_2 (.D(in_3), .CLK(CLOCK), .CLEAR(CLEAR), .Q_prime(out_22));  // open: Q
  Flip_Flop_D flip_flop_d_3 (.D(in_2), .CLK(CLOCK), .CLEAR(CLEAR), .Q_prime(out_21));  // open: Q
  Flip_Flop_D flip_flop_d_4 (.D(in_4), .CLK(CLOCK), .CLEAR(CLEAR), .Q_prime(out_23));  // open: Q
  Flip_Flop_D flip_flop_d_5 (.D(in_5), .CLK(CLOCK), .CLEAR(CLEAR), .Q_prime(out_24));  // open: Q
  Flip_Flop_D flip_flop_d_6 (.D(in_6), .CLK(CLOCK), .CLEAR(CLEAR), .Q_prime(out_25));  // open: Q
  Flip_Flop_D flip_flop_d_7 (.D(in_7), .CLK(CLOCK), .CLEAR(CLEAR), .Q_prime(out_26));  // open: Q
  Flip_Flop_D flip_flop_d_8 (.D(in_8), .CLK(CLOCK), .CLEAR(CLEAR), .Q_prime(out_27));  // open: Q
  Flip_Flop_D flip_flop_d_9 (.D(in_9), .CLK(CLOCK), .CLEAR(CLEAR), .Q_prime(out_28));  // open: Q
  Flip_Flop_D flip_flop_d_10 (.D(in_10), .CLK(CLOCK), .CLEAR(CLEAR), .Q_prime(out_29));  // open: Q
  Flip_Flop_D flip_flop_d_11 (.D(in_11), .CLK(CLOCK), .CLEAR(CLEAR), .Q_prime(out_30));  // open: Q
  Flip_Flop_D flip_flop_d_12 (.D(in_12), .CLK(CLOCK), .CLEAR(CLEAR), .Q_prime(out_31));  // open: Q
  Flip_Flop_D flip_flop_d_13 (.D(in_13), .CLK(CLOCK), .CLEAR(CLEAR), .Q_prime(out_32));  // open: Q
  Flip_Flop_D flip_flop_d_14 (.D(in_14), .CLK(CLOCK), .CLEAR(CLEAR), .Q_prime(out_33));  // open: Q
  Flip_Flop_D flip_flop_d_15 (.D(in_15), .CLK(CLOCK), .CLEAR(CLEAR), .Q_prime(out_34));  // open: Q
  Flip_Flop_D flip_flop_d_16 (.D(in_16), .CLK(CLOCK), .CLEAR(CLEAR), .Q_prime(out_19));  // open: Q
endmodule

// L2 256 BITS
module L2_256b (
  input  DEST,
  input  DEST_2,
  input  DEST_3,
  input  OP,
  input  OP_2,
  input  OP_3,
  input  R1,
  input  R1_2,
  input  R1_3,
  input  R2,
  input  R2_2,
  input  R2_3,
  input  R1_4,
  input  INPUT,
  input  INPUT_2,
  input  INPUT_3,
  input  R1_5,
  input  R2_4,
  input  R3,
  input  R4,
  input  R5,
  input  R6,
  input  R7,
  input  R8,
  input  [3:0] SELECT,
  input  R9,
  input  R10,
  input  R11,
  input  R12,
  input  R13,
  input  R14,
  input  R15,
  input  R16,
  input  CLEAR,
  output DEST_4,
  output DEST_5,
  output DEST_6,
  output INS,
  output INS_2,
  output INS_3,
  output OUT_INPUT,
  output OUT_INPUT_2,
  output OUT_INPUT_3,
  output OUT_INPUT_4,
  output OUT_R1,
  output OUT_R1_2,
  output OUT_R1_3,
  output OUT_R2,
  output OUT_R2_2,
  output OUT_R2_3
);

  wire l2_rg16plug_1_out_35, l2_rg16plug_1_out_36, l2_rg16plug_1_out_37, l2_rg16plug_1_out_38,
       l2_rg16plug_1_out_39, l2_rg16plug_1_out_40, l2_rg16plug_1_out_41, l2_rg16plug_1_out_42,
       l2_rg16plug_1_out_43, l2_rg16plug_1_out_44, l2_rg16plug_1_out_45, l2_rg16plug_1_out_46,
       l2_rg16plug_1_out_47, l2_rg16plug_1_out_48, l2_rg16plug_1_out_49, l2_rg16plug_1_out_50,
       l2_rg16plug_2_out_35, l2_rg16plug_2_out_36, l2_rg16plug_2_out_37, l2_rg16plug_2_out_38,
       l2_rg16plug_2_out_39, l2_rg16plug_2_out_40, l2_rg16plug_2_out_41, l2_rg16plug_2_out_42,
       l2_rg16plug_2_out_43, l2_rg16plug_2_out_44, l2_rg16plug_2_out_45, l2_rg16plug_2_out_46,
       l2_rg16plug_2_out_47, l2_rg16plug_2_out_48, l2_rg16plug_2_out_49, l2_rg16plug_2_out_50,
       l2_rg16plug_3_out_35, l2_rg16plug_3_out_36, l2_rg16plug_3_out_37, l2_rg16plug_3_out_38,
       l2_rg16plug_3_out_39, l2_rg16plug_3_out_40, l2_rg16plug_3_out_41, l2_rg16plug_3_out_42,
       l2_rg16plug_3_out_43, l2_rg16plug_3_out_44, l2_rg16plug_3_out_45, l2_rg16plug_3_out_46,
       l2_rg16plug_3_out_47, l2_rg16plug_3_out_48, l2_rg16plug_3_out_49, l2_rg16plug_3_out_50,
       l2_rg16plug_4_out_35, l2_rg16plug_4_out_36, l2_rg16plug_4_out_37, l2_rg16plug_4_out_38,
       l2_rg16plug_4_out_39, l2_rg16plug_4_out_40, l2_rg16plug_4_out_41, l2_rg16plug_4_out_42,
       l2_rg16plug_4_out_43, l2_rg16plug_4_out_44, l2_rg16plug_4_out_45, l2_rg16plug_4_out_46,
       l2_rg16plug_4_out_47, l2_rg16plug_4_out_48, l2_rg16plug_4_out_49, l2_rg16plug_4_out_50,
       l2_rg16plug_5_out_35, l2_rg16plug_5_out_36, l2_rg16plug_5_out_37, l2_rg16plug_5_out_38,
       l2_rg16plug_5_out_39, l2_rg16plug_5_out_40, l2_rg16plug_5_out_41, l2_rg16plug_5_out_42,
       l2_rg16plug_5_out_43, l2_rg16plug_5_out_44, l2_rg16plug_5_out_45, l2_rg16plug_5_out_46,
       l2_rg16plug_5_out_47, l2_rg16plug_5_out_48, l2_rg16plug_5_out_49, l2_rg16plug_5_out_50,
       l2_rg16plug_6_out_35, l2_rg16plug_6_out_36, l2_rg16plug_6_out_37, l2_rg16plug_6_out_38,
       l2_rg16plug_6_out_39, l2_rg16plug_6_out_40, l2_rg16plug_6_out_41, l2_rg16plug_6_out_42,
       l2_rg16plug_6_out_43, l2_rg16plug_6_out_44, l2_rg16plug_6_out_45, l2_rg16plug_6_out_46,
       l2_rg16plug_6_out_47, l2_rg16plug_6_out_48, l2_rg16plug_6_out_49, l2_rg16plug_6_out_50,
       l2_rg16plug_7_out_35, l2_rg16plug_7_out_36, l2_rg16plug_7_out_37, l2_rg16plug_7_out_38,
       l2_rg16plug_7_out_39, l2_rg16plug_7_out_40, l2_rg16plug_7_out_41, l2_rg16plug_7_out_42,
       l2_rg16plug_7_out_43, l2_rg16plug_7_out_44, l2_rg16plug_7_out_45, l2_rg16plug_7_out_46,
       l2_rg16plug_7_out_47, l2_rg16plug_7_out_48, l2_rg16plug_7_out_49, l2_rg16plug_7_out_50,
       l2_rg16plug_8_out_35, l2_rg16plug_8_out_36, l2_rg16plug_8_out_37, l2_rg16plug_8_out_38,
       l2_rg16plug_8_out_39, l2_rg16plug_8_out_40, l2_rg16plug_8_out_41, l2_rg16plug_8_out_42,
       l2_rg16plug_8_out_43, l2_rg16plug_8_out_44, l2_rg16plug_8_out_45, l2_rg16plug_8_out_46,
       l2_rg16plug_8_out_47, l2_rg16plug_8_out_48, l2_rg16plug_8_out_49, l2_rg16plug_8_out_50,
       l2_rg16plug_9_out_35, l2_rg16plug_9_out_36, l2_rg16plug_9_out_37, l2_rg16plug_9_out_38,
       l2_rg16plug_9_out_39, l2_rg16plug_9_out_40, l2_rg16plug_9_out_41, l2_rg16plug_9_out_42,
       l2_rg16plug_9_out_43, l2_rg16plug_9_out_44, l2_rg16plug_9_out_45, l2_rg16plug_9_out_46,
       l2_rg16plug_9_out_47, l2_rg16plug_9_out_48, l2_rg16plug_9_out_49, l2_rg16plug_9_out_50,
       l2_rg16plug_10_out_35, l2_rg16plug_10_out_36, l2_rg16plug_10_out_37, l2_rg16plug_10_out_38,
       l2_rg16plug_10_out_39, l2_rg16plug_10_out_40, l2_rg16plug_10_out_41, l2_rg16plug_10_out_42,
       l2_rg16plug_10_out_43, l2_rg16plug_10_out_44, l2_rg16plug_10_out_45, l2_rg16plug_10_out_46,
       l2_rg16plug_10_out_47, l2_rg16plug_10_out_48, l2_rg16plug_10_out_49, l2_rg16plug_10_out_50,
       l2_rg16plug_11_out_35, l2_rg16plug_11_out_36, l2_rg16plug_11_out_37, l2_rg16plug_11_out_38,
       l2_rg16plug_11_out_39, l2_rg16plug_11_out_40, l2_rg16plug_11_out_41, l2_rg16plug_11_out_42,
       l2_rg16plug_11_out_43, l2_rg16plug_11_out_44, l2_rg16plug_11_out_45, l2_rg16plug_11_out_46,
       l2_rg16plug_11_out_47, l2_rg16plug_11_out_48, l2_rg16plug_11_out_49, l2_rg16plug_11_out_50,
       l2_rg16plug_12_out_35, l2_rg16plug_12_out_36, l2_rg16plug_12_out_37, l2_rg16plug_12_out_38,
       l2_rg16plug_12_out_39, l2_rg16plug_12_out_40, l2_rg16plug_12_out_41, l2_rg16plug_12_out_42,
       l2_rg16plug_12_out_43, l2_rg16plug_12_out_44, l2_rg16plug_12_out_45, l2_rg16plug_12_out_46,
       l2_rg16plug_12_out_47, l2_rg16plug_12_out_48, l2_rg16plug_12_out_49, l2_rg16plug_12_out_50,
       l2_rg16plug_13_out_35, l2_rg16plug_13_out_36, l2_rg16plug_13_out_37, l2_rg16plug_13_out_38,
       l2_rg16plug_13_out_39, l2_rg16plug_13_out_40, l2_rg16plug_13_out_41, l2_rg16plug_13_out_42,
       l2_rg16plug_13_out_43, l2_rg16plug_13_out_44, l2_rg16plug_13_out_45, l2_rg16plug_13_out_46,
       l2_rg16plug_13_out_47, l2_rg16plug_13_out_48, l2_rg16plug_13_out_49, l2_rg16plug_13_out_50,
       l2_rg16plug_14_out_35, l2_rg16plug_14_out_36, l2_rg16plug_14_out_37, l2_rg16plug_14_out_38,
       l2_rg16plug_14_out_39, l2_rg16plug_14_out_40, l2_rg16plug_14_out_41, l2_rg16plug_14_out_42,
       l2_rg16plug_14_out_43, l2_rg16plug_14_out_44, l2_rg16plug_14_out_45, l2_rg16plug_14_out_46,
       l2_rg16plug_14_out_47, l2_rg16plug_14_out_48, l2_rg16plug_14_out_49, l2_rg16plug_14_out_50,
       l2_rg16plug_15_out_35, l2_rg16plug_15_out_36, l2_rg16plug_15_out_37, l2_rg16plug_15_out_38,
       l2_rg16plug_15_out_39, l2_rg16plug_15_out_40, l2_rg16plug_15_out_41, l2_rg16plug_15_out_42,
       l2_rg16plug_15_out_43, l2_rg16plug_15_out_44, l2_rg16plug_15_out_45, l2_rg16plug_15_out_46,
       l2_rg16plug_15_out_47, l2_rg16plug_15_out_48, l2_rg16plug_15_out_49, l2_rg16plug_15_out_50;
  wire [15:0] l2_rg16plug_1_out_19, l2_rg16plug_2_out_19, l2_rg16plug_3_out_19, l2_rg16plug_4_out_19,
       l2_rg16plug_5_out_19, l2_rg16plug_6_out_19, l2_rg16plug_7_out_19, l2_rg16plug_8_out_19,
       l2_rg16plug_9_out_19, l2_rg16plug_10_out_19, l2_rg16plug_11_out_19, l2_rg16plug_12_out_19,
       l2_rg16plug_13_out_19, l2_rg16plug_14_out_19, l2_rg16plug_15_out_19, l2_rg16plug_16_out_19;

  L2_RG16PLUG l2_rg16plug_1 (
    .CLOCK(R1_5), .CLEAR(CLEAR), .A(DEST), .B(DEST_2), .C(DEST_3), .D(OP), .E(OP_2), .F(OP_3), .G(R1),
    .H(R1_2), .I(R1_3), .J(R2), .L(R2_2), .M(R2_3), .N(R1_4), .O(INPUT), .P(INPUT_2), .Q(INPUT_3),
    .out_35(l2_rg16plug_1_out_35), .out_36(l2_rg16plug_1_out_36), .out_37(l2_rg16plug_1_out_37),
    .out_38(l2_rg16plug_1_out_38), .out_39(l2_rg16plug_1_out_39), .out_40(l2_rg16plug_1_out_40),
    .out_41(l2_rg16plug_1_out_41), .out_42(l2_rg16plug_1_out_42), .out_43(l2_rg16plug_1_out_43),
    .out_44(l2_rg16plug_1_out_44), .out_45(l2_rg16plug_1_out_45), .out_46(l2_rg16plug_1_out_46),
    .out_47(l2_rg16plug_1_out_47), .out_48(l2_rg16plug_1_out_48), .out_49(l2_rg16plug_1_out_49),
    .out_50(l2_rg16plug_1_out_50), .out_19(l2_rg16plug_1_out_19[0]), .out_20(l2_rg16plug_1_out_19[1]),
    .out_21(l2_rg16plug_1_out_19[2]), .out_22(l2_rg16plug_1_out_19[3]), .out_23(l2_rg16plug_1_out_19[4]),
    .out_24(l2_rg16plug_1_out_19[5]), .out_25(l2_rg16plug_1_out_19[6]), .out_26(l2_rg16plug_1_out_19[7]),
    .out_27(l2_rg16plug_1_out_19[8]), .out_28(l2_rg16plug_1_out_19[9]), .out_29(l2_rg16plug_1_out_19[10]),
    .out_30(l2_rg16plug_1_out_19[11]), .out_31(l2_rg16plug_1_out_19[12]), .out_32(l2_rg16plug_1_out_19[13]),
    .out_33(l2_rg16plug_1_out_19[14]), .out_34(l2_rg16plug_1_out_19[15]));
  L2_RG16PLUG l2_rg16plug_2 (
    .CLOCK(R2_4), .CLEAR(CLEAR), .A(l2_rg16plug_1_out_35), .B(l2_rg16plug_1_out_36),
    .C(l2_rg16plug_1_out_37), .D(l2_rg16plug_1_out_38), .E(l2_rg16plug_1_out_39), .F(l2_rg16plug_1_out_40),
    .G(l2_rg16plug_1_out_41), .H(l2_rg16plug_1_out_42), .I(l2_rg16plug_1_out_43), .J(l2_rg16plug_1_out_44),
    .L(l2_rg16plug_1_out_45), .M(l2_rg16plug_1_out_46), .N(l2_rg16plug_1_out_47), .O(l2_rg16plug_1_out_48),
    .P(l2_rg16plug_1_out_49), .Q(l2_rg16plug_1_out_50), .out_35(l2_rg16plug_2_out_35),
    .out_36(l2_rg16plug_2_out_36), .out_37(l2_rg16plug_2_out_37), .out_38(l2_rg16plug_2_out_38),
    .out_39(l2_rg16plug_2_out_39), .out_40(l2_rg16plug_2_out_40), .out_41(l2_rg16plug_2_out_41),
    .out_42(l2_rg16plug_2_out_42), .out_43(l2_rg16plug_2_out_43), .out_44(l2_rg16plug_2_out_44),
    .out_45(l2_rg16plug_2_out_45), .out_46(l2_rg16plug_2_out_46), .out_47(l2_rg16plug_2_out_47),
    .out_48(l2_rg16plug_2_out_48), .out_49(l2_rg16plug_2_out_49), .out_50(l2_rg16plug_2_out_50),
    .out_19(l2_rg16plug_2_out_19[0]), .out_20(l2_rg16plug_2_out_19[1]), .out_21(l2_rg16plug_2_out_19[2]),
    .out_22(l2_rg16plug_2_out_19[3]), .out_23(l2_rg16plug_2_out_19[4]), .out_24(l2_rg16plug_2_out_19[5]),
    .out_25(l2_rg16plug_2_out_19[6]), .out_26(l2_rg16plug_2_out_19[7]), .out_27(l2_rg16plug_2_out_19[8]),
    .out_28(l2_rg16plug_2_out_19[9]), .out_29(l2_rg16plug_2_out_19[10]), .out_30(l2_rg16plug_2_out_19[11]),
    .out_31(l2_rg16plug_2_out_19[12]), .out_32(l2_rg16plug_2_out_19[13]), .out_33(l2_rg16plug_2_out_19[14]),
    .out_34(l2_rg16plug_2_out_19[15]));
  L2_RG16PLUG l2_rg16plug_3 (
    .CLOCK(R3), .CLEAR(CLEAR), .A(l2_rg16plug_2_out_35), .B(l2_rg16plug_2_out_36), .C(l2_rg16plug_2_out_37),
    .D(l2_rg16plug_2_out_38), .E(l2_rg16plug_2_out_39), .F(l2_rg16plug_2_out_40), .G(l2_rg16plug_2_out_41),
    .H(l2_rg16plug_2_out_42), .I(l2_rg16plug_2_out_43), .J(l2_rg16plug_2_out_44), .L(l2_rg16plug_2_out_45),
    .M(l2_rg16plug_2_out_46), .N(l2_rg16plug_2_out_47), .O(l2_rg16plug_2_out_48), .P(l2_rg16plug_2_out_49),
    .Q(l2_rg16plug_2_out_50), .out_35(l2_rg16plug_3_out_35), .out_36(l2_rg16plug_3_out_36),
    .out_37(l2_rg16plug_3_out_37), .out_38(l2_rg16plug_3_out_38), .out_39(l2_rg16plug_3_out_39),
    .out_40(l2_rg16plug_3_out_40), .out_41(l2_rg16plug_3_out_41), .out_42(l2_rg16plug_3_out_42),
    .out_43(l2_rg16plug_3_out_43), .out_44(l2_rg16plug_3_out_44), .out_45(l2_rg16plug_3_out_45),
    .out_46(l2_rg16plug_3_out_46), .out_47(l2_rg16plug_3_out_47), .out_48(l2_rg16plug_3_out_48),
    .out_49(l2_rg16plug_3_out_49), .out_50(l2_rg16plug_3_out_50), .out_19(l2_rg16plug_3_out_19[0]),
    .out_20(l2_rg16plug_3_out_19[1]), .out_21(l2_rg16plug_3_out_19[2]), .out_22(l2_rg16plug_3_out_19[3]),
    .out_23(l2_rg16plug_3_out_19[4]), .out_24(l2_rg16plug_3_out_19[5]), .out_25(l2_rg16plug_3_out_19[6]),
    .out_26(l2_rg16plug_3_out_19[7]), .out_27(l2_rg16plug_3_out_19[8]), .out_28(l2_rg16plug_3_out_19[9]),
    .out_29(l2_rg16plug_3_out_19[10]), .out_30(l2_rg16plug_3_out_19[11]), .out_31(l2_rg16plug_3_out_19[12]),
    .out_32(l2_rg16plug_3_out_19[13]), .out_33(l2_rg16plug_3_out_19[14]), .out_34(l2_rg16plug_3_out_19[15]));
  L2_RG16PLUG l2_rg16plug_4 (
    .CLOCK(R4), .CLEAR(CLEAR), .A(l2_rg16plug_3_out_35), .B(l2_rg16plug_3_out_36), .C(l2_rg16plug_3_out_37),
    .D(l2_rg16plug_3_out_38), .E(l2_rg16plug_3_out_39), .F(l2_rg16plug_3_out_40), .G(l2_rg16plug_3_out_41),
    .H(l2_rg16plug_3_out_42), .I(l2_rg16plug_3_out_43), .J(l2_rg16plug_3_out_44), .L(l2_rg16plug_3_out_45),
    .M(l2_rg16plug_3_out_46), .N(l2_rg16plug_3_out_47), .O(l2_rg16plug_3_out_48), .P(l2_rg16plug_3_out_49),
    .Q(l2_rg16plug_3_out_50), .out_35(l2_rg16plug_4_out_35), .out_36(l2_rg16plug_4_out_36),
    .out_37(l2_rg16plug_4_out_37), .out_38(l2_rg16plug_4_out_38), .out_39(l2_rg16plug_4_out_39),
    .out_40(l2_rg16plug_4_out_40), .out_41(l2_rg16plug_4_out_41), .out_42(l2_rg16plug_4_out_42),
    .out_43(l2_rg16plug_4_out_43), .out_44(l2_rg16plug_4_out_44), .out_45(l2_rg16plug_4_out_45),
    .out_46(l2_rg16plug_4_out_46), .out_47(l2_rg16plug_4_out_47), .out_48(l2_rg16plug_4_out_48),
    .out_49(l2_rg16plug_4_out_49), .out_50(l2_rg16plug_4_out_50), .out_19(l2_rg16plug_4_out_19[0]),
    .out_20(l2_rg16plug_4_out_19[1]), .out_21(l2_rg16plug_4_out_19[2]), .out_22(l2_rg16plug_4_out_19[3]),
    .out_23(l2_rg16plug_4_out_19[4]), .out_24(l2_rg16plug_4_out_19[5]), .out_25(l2_rg16plug_4_out_19[6]),
    .out_26(l2_rg16plug_4_out_19[7]), .out_27(l2_rg16plug_4_out_19[8]), .out_28(l2_rg16plug_4_out_19[9]),
    .out_29(l2_rg16plug_4_out_19[10]), .out_30(l2_rg16plug_4_out_19[11]), .out_31(l2_rg16plug_4_out_19[12]),
    .out_32(l2_rg16plug_4_out_19[13]), .out_33(l2_rg16plug_4_out_19[14]), .out_34(l2_rg16plug_4_out_19[15]));
  L2_RG16PLUG l2_rg16plug_5 (
    .CLOCK(R5), .CLEAR(CLEAR), .A(l2_rg16plug_4_out_35), .B(l2_rg16plug_4_out_36), .C(l2_rg16plug_4_out_37),
    .D(l2_rg16plug_4_out_38), .E(l2_rg16plug_4_out_39), .F(l2_rg16plug_4_out_40), .G(l2_rg16plug_4_out_41),
    .H(l2_rg16plug_4_out_42), .I(l2_rg16plug_4_out_43), .J(l2_rg16plug_4_out_44), .L(l2_rg16plug_4_out_45),
    .M(l2_rg16plug_4_out_46), .N(l2_rg16plug_4_out_47), .O(l2_rg16plug_4_out_48), .P(l2_rg16plug_4_out_49),
    .Q(l2_rg16plug_4_out_50), .out_35(l2_rg16plug_5_out_35), .out_36(l2_rg16plug_5_out_36),
    .out_37(l2_rg16plug_5_out_37), .out_38(l2_rg16plug_5_out_38), .out_39(l2_rg16plug_5_out_39),
    .out_40(l2_rg16plug_5_out_40), .out_41(l2_rg16plug_5_out_41), .out_42(l2_rg16plug_5_out_42),
    .out_43(l2_rg16plug_5_out_43), .out_44(l2_rg16plug_5_out_44), .out_45(l2_rg16plug_5_out_45),
    .out_46(l2_rg16plug_5_out_46), .out_47(l2_rg16plug_5_out_47), .out_48(l2_rg16plug_5_out_48),
    .out_49(l2_rg16plug_5_out_49), .out_50(l2_rg16plug_5_out_50), .out_19(l2_rg16plug_5_out_19[0]),
    .out_20(l2_rg16plug_5_out_19[1]), .out_21(l2_rg16plug_5_out_19[2]), .out_22(l2_rg16plug_5_out_19[3]),
    .out_23(l2_rg16plug_5_out_19[4]), .out_24(l2_rg16plug_5_out_19[5]), .out_25(l2_rg16plug_5_out_19[6]),
    .out_26(l2_rg16plug_5_out_19[7]), .out_27(l2_rg16plug_5_out_19[8]), .out_28(l2_rg16plug_5_out_19[9]),
    .out_29(l2_rg16plug_5_out_19[10]), .out_30(l2_rg16plug_5_out_19[11]), .out_31(l2_rg16plug_5_out_19[12]),
    .out_32(l2_rg16plug_5_out_19[13]), .out_33(l2_rg16plug_5_out_19[14]), .out_34(l2_rg16plug_5_out_19[15]));
  L2_RG16PLUG l2_rg16plug_6 (
    .CLOCK(R6), .CLEAR(CLEAR), .A(l2_rg16plug_5_out_35), .B(l2_rg16plug_5_out_36), .C(l2_rg16plug_5_out_37),
    .D(l2_rg16plug_5_out_38), .E(l2_rg16plug_5_out_39), .F(l2_rg16plug_5_out_40), .G(l2_rg16plug_5_out_41),
    .H(l2_rg16plug_5_out_42), .I(l2_rg16plug_5_out_43), .J(l2_rg16plug_5_out_44), .L(l2_rg16plug_5_out_45),
    .M(l2_rg16plug_5_out_46), .N(l2_rg16plug_5_out_47), .O(l2_rg16plug_5_out_48), .P(l2_rg16plug_5_out_49),
    .Q(l2_rg16plug_5_out_50), .out_35(l2_rg16plug_6_out_35), .out_36(l2_rg16plug_6_out_36),
    .out_37(l2_rg16plug_6_out_37), .out_38(l2_rg16plug_6_out_38), .out_39(l2_rg16plug_6_out_39),
    .out_40(l2_rg16plug_6_out_40), .out_41(l2_rg16plug_6_out_41), .out_42(l2_rg16plug_6_out_42),
    .out_43(l2_rg16plug_6_out_43), .out_44(l2_rg16plug_6_out_44), .out_45(l2_rg16plug_6_out_45),
    .out_46(l2_rg16plug_6_out_46), .out_47(l2_rg16plug_6_out_47), .out_48(l2_rg16plug_6_out_48),
    .out_49(l2_rg16plug_6_out_49), .out_50(l2_rg16plug_6_out_50), .out_19(l2_rg16plug_6_out_19[0]),
    .out_20(l2_rg16plug_6_out_19[1]), .out_21(l2_rg16plug_6_out_19[2]), .out_22(l2_rg16plug_6_out_19[3]),
    .out_23(l2_rg16plug_6_out_19[4]), .out_24(l2_rg16plug_6_out_19[5]), .out_25(l2_rg16plug_6_out_19[6]),
    .out_26(l2_rg16plug_6_out_19[7]), .out_27(l2_rg16plug_6_out_19[8]), .out_28(l2_rg16plug_6_out_19[9]),
    .out_29(l2_rg16plug_6_out_19[10]), .out_30(l2_rg16plug_6_out_19[11]), .out_31(l2_rg16plug_6_out_19[12]),
    .out_32(l2_rg16plug_6_out_19[13]), .out_33(l2_rg16plug_6_out_19[14]), .out_34(l2_rg16plug_6_out_19[15]));
  L2_RG16PLUG l2_rg16plug_7 (
    .CLOCK(R7), .CLEAR(CLEAR), .A(l2_rg16plug_6_out_35), .B(l2_rg16plug_6_out_36), .C(l2_rg16plug_6_out_37),
    .D(l2_rg16plug_6_out_38), .E(l2_rg16plug_6_out_39), .F(l2_rg16plug_6_out_40), .G(l2_rg16plug_6_out_41),
    .H(l2_rg16plug_6_out_42), .I(l2_rg16plug_6_out_43), .J(l2_rg16plug_6_out_44), .L(l2_rg16plug_6_out_45),
    .M(l2_rg16plug_6_out_46), .N(l2_rg16plug_6_out_47), .O(l2_rg16plug_6_out_48), .P(l2_rg16plug_6_out_49),
    .Q(l2_rg16plug_6_out_50), .out_35(l2_rg16plug_7_out_35), .out_36(l2_rg16plug_7_out_36),
    .out_37(l2_rg16plug_7_out_37), .out_38(l2_rg16plug_7_out_38), .out_39(l2_rg16plug_7_out_39),
    .out_40(l2_rg16plug_7_out_40), .out_41(l2_rg16plug_7_out_41), .out_42(l2_rg16plug_7_out_42),
    .out_43(l2_rg16plug_7_out_43), .out_44(l2_rg16plug_7_out_44), .out_45(l2_rg16plug_7_out_45),
    .out_46(l2_rg16plug_7_out_46), .out_47(l2_rg16plug_7_out_47), .out_48(l2_rg16plug_7_out_48),
    .out_49(l2_rg16plug_7_out_49), .out_50(l2_rg16plug_7_out_50), .out_19(l2_rg16plug_7_out_19[0]),
    .out_20(l2_rg16plug_7_out_19[1]), .out_21(l2_rg16plug_7_out_19[2]), .out_22(l2_rg16plug_7_out_19[3]),
    .out_23(l2_rg16plug_7_out_19[4]), .out_24(l2_rg16plug_7_out_19[5]), .out_25(l2_rg16plug_7_out_19[6]),
    .out_26(l2_rg16plug_7_out_19[7]), .out_27(l2_rg16plug_7_out_19[8]), .out_28(l2_rg16plug_7_out_19[9]),
    .out_29(l2_rg16plug_7_out_19[10]), .out_30(l2_rg16plug_7_out_19[11]), .out_31(l2_rg16plug_7_out_19[12]),
    .out_32(l2_rg16plug_7_out_19[13]), .out_33(l2_rg16plug_7_out_19[14]), .out_34(l2_rg16plug_7_out_19[15]));
  L2_RG16PLUG l2_rg16plug_8 (
    .CLOCK(R8), .CLEAR(CLEAR), .A(l2_rg16plug_7_out_35), .B(l2_rg16plug_7_out_36), .C(l2_rg16plug_7_out_37),
    .D(l2_rg16plug_7_out_38), .E(l2_rg16plug_7_out_39), .F(l2_rg16plug_7_out_40), .G(l2_rg16plug_7_out_41),
    .H(l2_rg16plug_7_out_42), .I(l2_rg16plug_7_out_43), .J(l2_rg16plug_7_out_44), .L(l2_rg16plug_7_out_45),
    .M(l2_rg16plug_7_out_46), .N(l2_rg16plug_7_out_47), .O(l2_rg16plug_7_out_48), .P(l2_rg16plug_7_out_49),
    .Q(l2_rg16plug_7_out_50), .out_35(l2_rg16plug_8_out_35), .out_36(l2_rg16plug_8_out_36),
    .out_37(l2_rg16plug_8_out_37), .out_38(l2_rg16plug_8_out_38), .out_39(l2_rg16plug_8_out_39),
    .out_40(l2_rg16plug_8_out_40), .out_41(l2_rg16plug_8_out_41), .out_42(l2_rg16plug_8_out_42),
    .out_43(l2_rg16plug_8_out_43), .out_44(l2_rg16plug_8_out_44), .out_45(l2_rg16plug_8_out_45),
    .out_46(l2_rg16plug_8_out_46), .out_47(l2_rg16plug_8_out_47), .out_48(l2_rg16plug_8_out_48),
    .out_49(l2_rg16plug_8_out_49), .out_50(l2_rg16plug_8_out_50), .out_19(l2_rg16plug_8_out_19[0]),
    .out_20(l2_rg16plug_8_out_19[1]), .out_21(l2_rg16plug_8_out_19[2]), .out_22(l2_rg16plug_8_out_19[3]),
    .out_23(l2_rg16plug_8_out_19[4]), .out_24(l2_rg16plug_8_out_19[5]), .out_25(l2_rg16plug_8_out_19[6]),
    .out_26(l2_rg16plug_8_out_19[7]), .out_27(l2_rg16plug_8_out_19[8]), .out_28(l2_rg16plug_8_out_19[9]),
    .out_29(l2_rg16plug_8_out_19[10]), .out_30(l2_rg16plug_8_out_19[11]), .out_31(l2_rg16plug_8_out_19[12]),
    .out_32(l2_rg16plug_8_out_19[13]), .out_33(l2_rg16plug_8_out_19[14]), .out_34(l2_rg16plug_8_out_19[15]));
  L2_RG16PLUG l2_rg16plug_9 (
    .CLOCK(R9), .CLEAR(CLEAR), .A(l2_rg16plug_8_out_35), .B(l2_rg16plug_8_out_36), .C(l2_rg16plug_8_out_37),
    .D(l2_rg16plug_8_out_38), .E(l2_rg16plug_8_out_39), .F(l2_rg16plug_8_out_40), .G(l2_rg16plug_8_out_41),
    .H(l2_rg16plug_8_out_42), .I(l2_rg16plug_8_out_43), .J(l2_rg16plug_8_out_44), .L(l2_rg16plug_8_out_45),
    .M(l2_rg16plug_8_out_46), .N(l2_rg16plug_8_out_47), .O(l2_rg16plug_8_out_48), .P(l2_rg16plug_8_out_49),
    .Q(l2_rg16plug_8_out_50), .out_35(l2_rg16plug_9_out_35), .out_36(l2_rg16plug_9_out_36),
    .out_37(l2_rg16plug_9_out_37), .out_38(l2_rg16plug_9_out_38), .out_39(l2_rg16plug_9_out_39),
    .out_40(l2_rg16plug_9_out_40), .out_41(l2_rg16plug_9_out_41), .out_42(l2_rg16plug_9_out_42),
    .out_43(l2_rg16plug_9_out_43), .out_44(l2_rg16plug_9_out_44), .out_45(l2_rg16plug_9_out_45),
    .out_46(l2_rg16plug_9_out_46), .out_47(l2_rg16plug_9_out_47), .out_48(l2_rg16plug_9_out_48),
    .out_49(l2_rg16plug_9_out_49), .out_50(l2_rg16plug_9_out_50), .out_19(l2_rg16plug_9_out_19[0]),
    .out_20(l2_rg16plug_9_out_19[1]), .out_21(l2_rg16plug_9_out_19[2]), .out_22(l2_rg16plug_9_out_19[3]),
    .out_23(l2_rg16plug_9_out_19[4]), .out_24(l2_rg16plug_9_out_19[5]), .out_25(l2_rg16plug_9_out_19[6]),
    .out_26(l2_rg16plug_9_out_19[7]), .out_27(l2_rg16plug_9_out_19[8]), .out_28(l2_rg16plug_9_out_19[9]),
    .out_29(l2_rg16plug_9_out_19[10]), .out_30(l2_rg16plug_9_out_19[11]), .out_31(l2_rg16plug_9_out_19[12]),
    .out_32(l2_rg16plug_9_out_19[13]), .out_33(l2_rg16plug_9_out_19[14]), .out_34(l2_rg16plug_9_out_19[15]));
  L2_RG16PLUG l2_rg16plug_10 (
    .CLOCK(R10), .CLEAR(CLEAR), .A(l2_rg16plug_9_out_35), .B(l2_rg16plug_9_out_36), .C(l2_rg16plug_9_out_37),
    .D(l2_rg16plug_9_out_38), .E(l2_rg16plug_9_out_39), .F(l2_rg16plug_9_out_40), .G(l2_rg16plug_9_out_41),
    .H(l2_rg16plug_9_out_42), .I(l2_rg16plug_9_out_43), .J(l2_rg16plug_9_out_44), .L(l2_rg16plug_9_out_45),
    .M(l2_rg16plug_9_out_46), .N(l2_rg16plug_9_out_47), .O(l2_rg16plug_9_out_48), .P(l2_rg16plug_9_out_49),
    .Q(l2_rg16plug_9_out_50), .out_35(l2_rg16plug_10_out_35), .out_36(l2_rg16plug_10_out_36),
    .out_37(l2_rg16plug_10_out_37), .out_38(l2_rg16plug_10_out_38), .out_39(l2_rg16plug_10_out_39),
    .out_40(l2_rg16plug_10_out_40), .out_41(l2_rg16plug_10_out_41), .out_42(l2_rg16plug_10_out_42),
    .out_43(l2_rg16plug_10_out_43), .out_44(l2_rg16plug_10_out_44), .out_45(l2_rg16plug_10_out_45),
    .out_46(l2_rg16plug_10_out_46), .out_47(l2_rg16plug_10_out_47), .out_48(l2_rg16plug_10_out_48),
    .out_49(l2_rg16plug_10_out_49), .out_50(l2_rg16plug_10_out_50), .out_19(l2_rg16plug_10_out_19[0]),
    .out_20(l2_rg16plug_10_out_19[1]), .out_21(l2_rg16plug_10_out_19[2]), .out_22(l2_rg16plug_10_out_19[3]),
    .out_23(l2_rg16plug_10_out_19[4]), .out_24(l2_rg16plug_10_out_19[5]), .out_25(l2_rg16plug_10_out_19[6]),
    .out_26(l2_rg16plug_10_out_19[7]), .out_27(l2_rg16plug_10_out_19[8]), .out_28(l2_rg16plug_10_out_19[9]),
    .out_29(l2_rg16plug_10_out_19[10]), .out_30(l2_rg16plug_10_out_19[11]),
    .out_31(l2_rg16plug_10_out_19[12]), .out_32(l2_rg16plug_10_out_19[13]),
    .out_33(l2_rg16plug_10_out_19[14]), .out_34(l2_rg16plug_10_out_19[15]));
  L2_RG16PLUG l2_rg16plug_11 (
    .CLOCK(R11), .CLEAR(CLEAR), .A(l2_rg16plug_10_out_35), .B(l2_rg16plug_10_out_36),
    .C(l2_rg16plug_10_out_37), .D(l2_rg16plug_10_out_38), .E(l2_rg16plug_10_out_39),
    .F(l2_rg16plug_10_out_40), .G(l2_rg16plug_10_out_41), .H(l2_rg16plug_10_out_42),
    .I(l2_rg16plug_10_out_43), .J(l2_rg16plug_10_out_44), .L(l2_rg16plug_10_out_45),
    .M(l2_rg16plug_10_out_46), .N(l2_rg16plug_10_out_47), .O(l2_rg16plug_10_out_48),
    .P(l2_rg16plug_10_out_49), .Q(l2_rg16plug_10_out_50), .out_35(l2_rg16plug_11_out_35),
    .out_36(l2_rg16plug_11_out_36), .out_37(l2_rg16plug_11_out_37), .out_38(l2_rg16plug_11_out_38),
    .out_39(l2_rg16plug_11_out_39), .out_40(l2_rg16plug_11_out_40), .out_41(l2_rg16plug_11_out_41),
    .out_42(l2_rg16plug_11_out_42), .out_43(l2_rg16plug_11_out_43), .out_44(l2_rg16plug_11_out_44),
    .out_45(l2_rg16plug_11_out_45), .out_46(l2_rg16plug_11_out_46), .out_47(l2_rg16plug_11_out_47),
    .out_48(l2_rg16plug_11_out_48), .out_49(l2_rg16plug_11_out_49), .out_50(l2_rg16plug_11_out_50),
    .out_19(l2_rg16plug_11_out_19[0]), .out_20(l2_rg16plug_11_out_19[1]), .out_21(l2_rg16plug_11_out_19[2]),
    .out_22(l2_rg16plug_11_out_19[3]), .out_23(l2_rg16plug_11_out_19[4]), .out_24(l2_rg16plug_11_out_19[5]),
    .out_25(l2_rg16plug_11_out_19[6]), .out_26(l2_rg16plug_11_out_19[7]), .out_27(l2_rg16plug_11_out_19[8]),
    .out_28(l2_rg16plug_11_out_19[9]), .out_29(l2_rg16plug_11_out_19[10]),
    .out_30(l2_rg16plug_11_out_19[11]), .out_31(l2_rg16plug_11_out_19[12]),
    .out_32(l2_rg16plug_11_out_19[13]), .out_33(l2_rg16plug_11_out_19[14]), .out_34(l2_rg16plug_11_out_19[15]));
  L2_RG16PLUG l2_rg16plug_12 (
    .CLOCK(R12), .CLEAR(CLEAR), .A(l2_rg16plug_11_out_35), .B(l2_rg16plug_11_out_36),
    .C(l2_rg16plug_11_out_37), .D(l2_rg16plug_11_out_38), .E(l2_rg16plug_11_out_39),
    .F(l2_rg16plug_11_out_40), .G(l2_rg16plug_11_out_41), .H(l2_rg16plug_11_out_42),
    .I(l2_rg16plug_11_out_43), .J(l2_rg16plug_11_out_44), .L(l2_rg16plug_11_out_45),
    .M(l2_rg16plug_11_out_46), .N(l2_rg16plug_11_out_47), .O(l2_rg16plug_11_out_48),
    .P(l2_rg16plug_11_out_49), .Q(l2_rg16plug_11_out_50), .out_35(l2_rg16plug_12_out_35),
    .out_36(l2_rg16plug_12_out_36), .out_37(l2_rg16plug_12_out_37), .out_38(l2_rg16plug_12_out_38),
    .out_39(l2_rg16plug_12_out_39), .out_40(l2_rg16plug_12_out_40), .out_41(l2_rg16plug_12_out_41),
    .out_42(l2_rg16plug_12_out_42), .out_43(l2_rg16plug_12_out_43), .out_44(l2_rg16plug_12_out_44),
    .out_45(l2_rg16plug_12_out_45), .out_46(l2_rg16plug_12_out_46), .out_47(l2_rg16plug_12_out_47),
    .out_48(l2_rg16plug_12_out_48), .out_49(l2_rg16plug_12_out_49), .out_50(l2_rg16plug_12_out_50),
    .out_19(l2_rg16plug_12_out_19[0]), .out_20(l2_rg16plug_12_out_19[1]), .out_21(l2_rg16plug_12_out_19[2]),
    .out_22(l2_rg16plug_12_out_19[3]), .out_23(l2_rg16plug_12_out_19[4]), .out_24(l2_rg16plug_12_out_19[5]),
    .out_25(l2_rg16plug_12_out_19[6]), .out_26(l2_rg16plug_12_out_19[7]), .out_27(l2_rg16plug_12_out_19[8]),
    .out_28(l2_rg16plug_12_out_19[9]), .out_29(l2_rg16plug_12_out_19[10]),
    .out_30(l2_rg16plug_12_out_19[11]), .out_31(l2_rg16plug_12_out_19[12]),
    .out_32(l2_rg16plug_12_out_19[13]), .out_33(l2_rg16plug_12_out_19[14]), .out_34(l2_rg16plug_12_out_19[15]));
  L2_RG16PLUG l2_rg16plug_13 (
    .CLOCK(R13), .CLEAR(CLEAR), .A(l2_rg16plug_12_out_35), .B(l2_rg16plug_12_out_36),
    .C(l2_rg16plug_12_out_37), .D(l2_rg16plug_12_out_38), .E(l2_rg16plug_12_out_39),
    .F(l2_rg16plug_12_out_40), .G(l2_rg16plug_12_out_41), .H(l2_rg16plug_12_out_42),
    .I(l2_rg16plug_12_out_43), .J(l2_rg16plug_12_out_44), .L(l2_rg16plug_12_out_45),
    .M(l2_rg16plug_12_out_46), .N(l2_rg16plug_12_out_47), .O(l2_rg16plug_12_out_48),
    .P(l2_rg16plug_12_out_49), .Q(l2_rg16plug_12_out_50), .out_35(l2_rg16plug_13_out_35),
    .out_36(l2_rg16plug_13_out_36), .out_37(l2_rg16plug_13_out_37), .out_38(l2_rg16plug_13_out_38),
    .out_39(l2_rg16plug_13_out_39), .out_40(l2_rg16plug_13_out_40), .out_41(l2_rg16plug_13_out_41),
    .out_42(l2_rg16plug_13_out_42), .out_43(l2_rg16plug_13_out_43), .out_44(l2_rg16plug_13_out_44),
    .out_45(l2_rg16plug_13_out_45), .out_46(l2_rg16plug_13_out_46), .out_47(l2_rg16plug_13_out_47),
    .out_48(l2_rg16plug_13_out_48), .out_49(l2_rg16plug_13_out_49), .out_50(l2_rg16plug_13_out_50),
    .out_19(l2_rg16plug_13_out_19[0]), .out_20(l2_rg16plug_13_out_19[1]), .out_21(l2_rg16plug_13_out_19[2]),
    .out_22(l2_rg16plug_13_out_19[3]), .out_23(l2_rg16plug_13_out_19[4]), .out_24(l2_rg16plug_13_out_19[5]),
    .out_25(l2_rg16plug_13_out_19[6]), .out_26(l2_rg16plug_13_out_19[7]), .out_27(l2_rg16plug_13_out_19[8]),
    .out_28(l2_rg16plug_13_out_19[9]), .out_29(l2_rg16plug_13_out_19[10]),
    .out_30(l2_rg16plug_13_out_19[11]), .out_31(l2_rg16plug_13_out_19[12]),
    .out_32(l2_rg16plug_13_out_19[13]), .out_33(l2_rg16plug_13_out_19[14]), .out_34(l2_rg16plug_13_out_19[15]));
  L2_RG16PLUG l2_rg16plug_14 (
    .CLOCK(R14), .CLEAR(CLEAR), .A(l2_rg16plug_13_out_35), .B(l2_rg16plug_13_out_36),
    .C(l2_rg16plug_13_out_37), .D(l2_rg16plug_13_out_38), .E(l2_rg16plug_13_out_39),
    .F(l2_rg16plug_13_out_40), .G(l2_rg16plug_13_out_41), .H(l2_rg16plug_13_out_42),
    .I(l2_rg16plug_13_out_43), .J(l2_rg16plug_13_out_44), .L(l2_rg16plug_13_out_45),
    .M(l2_rg16plug_13_out_46), .N(l2_rg16plug_13_out_47), .O(l2_rg16plug_13_out_48),
    .P(l2_rg16plug_13_out_49), .Q(l2_rg16plug_13_out_50), .out_35(l2_rg16plug_14_out_35),
    .out_36(l2_rg16plug_14_out_36), .out_37(l2_rg16plug_14_out_37), .out_38(l2_rg16plug_14_out_38),
    .out_39(l2_rg16plug_14_out_39), .out_40(l2_rg16plug_14_out_40), .out_41(l2_rg16plug_14_out_41),
    .out_42(l2_rg16plug_14_out_42), .out_43(l2_rg16plug_14_out_43), .out_44(l2_rg16plug_14_out_44),
    .out_45(l2_rg16plug_14_out_45), .out_46(l2_rg16plug_14_out_46), .out_47(l2_rg16plug_14_out_47),
    .out_48(l2_rg16plug_14_out_48), .out_49(l2_rg16plug_14_out_49), .out_50(l2_rg16plug_14_out_50),
    .out_19(l2_rg16plug_14_out_19[0]), .out_20(l2_rg16plug_14_out_19[1]), .out_21(l2_rg16plug_14_out_19[2]),
    .out_22(l2_rg16plug_14_out_19[3]), .out_23(l2_rg16plug_14_out_19[4]), .out_24(l2_rg16plug_14_out_19[5]),
    .out_25(l2_rg16plug_14_out_19[6]), .out_26(l2_rg16plug_14_out_19[7]), .out_27(l2_rg16plug_14_out_19[8]),
    .out_28(l2_rg16plug_14_out_19[9]), .out_29(l2_rg16plug_14_out_19[10]),
    .out_30(l2_rg16plug_14_out_19[11]), .out_31(l2_rg16plug_14_out_19[12]),
    .out_32(l2_rg16plug_14_out_19[13]), .out_33(l2_rg16plug_14_out_19[14]), .out_34(l2_rg16plug_14_out_19[15]));
  L2_RG16PLUG l2_rg16plug_15 (
    .CLOCK(R15), .CLEAR(CLEAR), .A(l2_rg16plug_14_out_35), .B(l2_rg16plug_14_out_36),
    .C(l2_rg16plug_14_out_37), .D(l2_rg16plug_14_out_38), .E(l2_rg16plug_14_out_39),
    .F(l2_rg16plug_14_out_40), .G(l2_rg16plug_14_out_41), .H(l2_rg16plug_14_out_42),
    .I(l2_rg16plug_14_out_43), .J(l2_rg16plug_14_out_44), .L(l2_rg16plug_14_out_45),
    .M(l2_rg16plug_14_out_46), .N(l2_rg16plug_14_out_47), .O(l2_rg16plug_14_out_48),
    .P(l2_rg16plug_14_out_49), .Q(l2_rg16plug_14_out_50), .out_35(l2_rg16plug_15_out_35),
    .out_36(l2_rg16plug_15_out_36), .out_37(l2_rg16plug_15_out_37), .out_38(l2_rg16plug_15_out_38),
    .out_39(l2_rg16plug_15_out_39), .out_40(l2_rg16plug_15_out_40), .out_41(l2_rg16plug_15_out_41),
    .out_42(l2_rg16plug_15_out_42), .out_43(l2_rg16plug_15_out_43), .out_44(l2_rg16plug_15_out_44),
    .out_45(l2_rg16plug_15_out_45), .out_46(l2_rg16plug_15_out_46), .out_47(l2_rg16plug_15_out_47),
    .out_48(l2_rg16plug_15_out_48), .out_49(l2_rg16plug_15_out_49), .out_50(l2_rg16plug_15_out_50),
    .out_19(l2_rg16plug_15_out_19[0]), .out_20(l2_rg16plug_15_out_19[1]), .out_21(l2_rg16plug_15_out_19[2]),
    .out_22(l2_rg16plug_15_out_19[3]), .out_23(l2_rg16plug_15_out_19[4]), .out_24(l2_rg16plug_15_out_19[5]),
    .out_25(l2_rg16plug_15_out_19[6]), .out_26(l2_rg16plug_15_out_19[7]), .out_27(l2_rg16plug_15_out_19[8]),
    .out_28(l2_rg16plug_15_out_19[9]), .out_29(l2_rg16plug_15_out_19[10]),
    .out_30(l2_rg16plug_15_out_19[11]), .out_31(l2_rg16plug_15_out_19[12]),
    .out_32(l2_rg16plug_15_out_19[13]), .out_33(l2_rg16plug_15_out_19[14]), .out_34(l2_rg16plug_15_out_19[15]));
  L2_RG16PLUG l2_rg16plug_16 (
    .CLOCK(R16), .CLEAR(CLEAR), .A(l2_rg16plug_15_out_35), .B(l2_rg16plug_15_out_36),
    .C(l2_rg16plug_15_out_37), .D(l2_rg16plug_15_out_38), .E(l2_rg16plug_15_out_39),
    .F(l2_rg16plug_15_out_40), .G(l2_rg16plug_15_out_41), .H(l2_rg16plug_15_out_42),
    .I(l2_rg16plug_15_out_43), .J(l2_rg16plug_15_out_44), .L(l2_rg16plug_15_out_45),
    .M(l2_rg16plug_15_out_46), .N(l2_rg16plug_15_out_47), .O(l2_rg16plug_15_out_48),
    .P(l2_rg16plug_15_out_49), .Q(l2_rg16plug_15_out_50), .out_19(l2_rg16plug_16_out_19[0]),
    .out_20(l2_rg16plug_16_out_19[1]), .out_21(l2_rg16plug_16_out_19[2]), .out_22(l2_rg16plug_16_out_19[3]),
    .out_23(l2_rg16plug_16_out_19[4]), .out_24(l2_rg16plug_16_out_19[5]), .out_25(l2_rg16plug_16_out_19[6]),
    .out_26(l2_rg16plug_16_out_19[7]), .out_27(l2_rg16plug_16_out_19[8]), .out_28(l2_rg16plug_16_out_19[9]),
    .out_29(l2_rg16plug_16_out_19[10]), .out_30(l2_rg16plug_16_out_19[11]),
    .out_31(l2_rg16plug_16_out_19[12]), .out_32(l2_rg16plug_16_out_19[13]),
    .out_33(l2_rg16plug_16_out_19[14]), .out_34(l2_rg16plug_16_out_19[15]));  // open: out_35, out_36, out_37, out_38, out_39, out_40, out_41, out_42, out_43, out_44, out_45, out_46, out_47, out_48, out_49, out_50
  Multiplexer #(.select(4), .width(16)) multiplexer_1 (
    .in0(l2_rg16plug_1_out_19), .in1(l2_rg16plug_2_out_19), .in2(l2_rg16plug_3_out_19),
    .in3(l2_rg16plug_4_out_19), .in4(l2_rg16plug_5_out_19), .in5(l2_rg16plug_6_out_19),
    .in6(l2_rg16plug_7_out_19), .in7(l2_rg16plug_8_out_19), .in8(l2_rg16plug_9_out_19),
    .in9(l2_rg16plug_10_out_19), .in10(l2_rg16plug_11_out_19), .in11(l2_rg16plug_12_out_19),
    .in12(l2_rg16plug_13_out_19), .in13(l2_rg16plug_14_out_19), .in14(l2_rg16plug_15_out_19),
    .in15(l2_rg16plug_16_out_19),
    .out({OUT_INPUT_4, OUT_INPUT_3, OUT_INPUT_2, OUT_INPUT, OUT_R2_3, OUT_R2_2, OUT_R2, OUT_R1_3, OUT_R1_2, OUT_R1, INS_3, INS_2, INS, DEST_6, DEST_5, DEST_4}),
    .sel(SELECT));  // open: en
endmodule

module L2_RG16PLUG (
  input  A,
  input  B,
  input  C,
  input  D,
  input  E,
  input  F,
  input  G,
  input  H,
  input  I,
  input  J,
  input  L,
  input  M,
  input  N,
  input  O,
  input  P,
  input  Q,
  input  CLOCK,
  input  CLEAR,
  output out_19,
  output out_20,
  output out_21,
  output out_22,
  output out_23,
  output out_24,
  output out_25,
  output out_26,
  output out_27,
  output out_28,
  output out_29,
  output out_30,
  output out_31,
  output out_32,
  output out_33,
  output out_34,
  output out_35,
  output out_36,
  output out_37,
  output out_38,
  output out_39,
  output out_40,
  output out_41,
  output out_42,
  output out_43,
  output out_44,
  output out_45,
  output out_46,
  output out_47,
  output out_48,
  output out_49,
  output out_50
);

  L2_RG16b l2_rg16b_1 (
    .CLOCK(CLOCK), .CLEAR(CLEAR), .in_1(Q), .in_2(P), .in_3(O), .in_4(N), .in_5(M), .in_6(L), .in_7(J),
    .in_8(I), .in_9(H), .in_10(G), .in_11(F), .in_12(E), .in_13(D), .in_14(C), .in_15(B), .in_16(A),
    .out_20(out_34), .out_21(out_33), .out_22(out_32), .out_23(out_31), .out_24(out_30), .out_25(out_29),
    .out_26(out_28), .out_27(out_27), .out_28(out_26), .out_29(out_25), .out_30(out_24), .out_31(out_23),
    .out_32(out_22), .out_33(out_21), .out_34(out_20), .out_19(out_19));

  assign out_35 = A;
  assign out_36 = B;
  assign out_37 = C;
  assign out_38 = D;
  assign out_39 = E;
  assign out_40 = F;
  assign out_41 = G;
  assign out_42 = H;
  assign out_43 = I;
  assign out_44 = J;
  assign out_45 = L;
  assign out_46 = M;
  assign out_47 = N;
  assign out_48 = O;
  assign out_49 = P;
  assign out_50 = Q;
endmodule
